// Logisim project MIbz_TOY8_BYTE.circ as structural Verilog
module TOY_Bit (
  input  [3:0] in_1,
  input  [7:0] in_2,
  output [7:0] out_3,
  output [7:0] out_4,
  output [7:0] out_5,
  output [7:0] out_6,
  output [7:0] out_7,
  output [7:0] out_8,
  output [7:0] out_9,
  output [7:0] out_10,
  output [7:0] out_11,
  output [7:0] out_12,
  output [7:0] out_13,
  output [7:0] out_14,
  output [7:0] out_15,
  output [7:0] out_16,
  output [7:0] out_17,
  output [7:0] out_18,
  output [7:0] out_19
);

  wire button_1_out, button_2_out, clock_1_out, interface_cpu_1_halt, interface_cpu_1_running, RUN_out;
  wire [3:0] interface_cpu_1_pc;

  Hex_Digit_Display hex_digit_display_1 (.value(in_1));  // open: dp
  Hex_Digit_Display hex_digit_display_2 (.value(in_2[7:4]));  // open: dp
  Hex_Digit_Display hex_digit_display_3 (.value(in_2[3:0]));  // open: dp
  Interface_CPU interface_cpu_1 (
    .Look_2(out_3), .RUN(RUN_out), .Load(button_1_out), .Look(button_2_out), .PC(interface_cpu_1_pc),
    .x0(out_4), .x1(out_5), .x2(out_6), .x3(out_7), .x4(out_8), .x5(out_9), .x6(out_10), .x7(out_11),
    .x8(out_12), .x9(out_13), .xA(out_14), .xB(out_15), .xC(out_16), .xD(out_17), .xE(out_18), .xF(out_19),
    .RUNNING(interface_cpu_1_running), .DATA_IN(in_2), .Clock(clock_1_out), .ADDR(in_1),
    .Halt(interface_cpu_1_halt));
  Button RUN (.out(RUN_out));
  Clock clock_1 (.out(clock_1_out));
  Button button_1 (.out(button_1_out));
  Button button_2 (.out(button_2_out));
  LED led_1 (.in(interface_cpu_1_running));
  LED led_2 (.in(interface_cpu_1_halt));
  Hex_Digit_Display hex_digit_display_4 (.value(interface_cpu_1_pc));  // open: dp
endmodule

module Interface_CPU (
  input  [7:0] DATA_IN,
  input  RUN,
  input  Load,
  input  Clock,
  input  [3:0] ADDR,
  input  Look,
  output RUNNING,
  output [7:0] x0,
  output [7:0] x1,
  output [7:0] x2,
  output [7:0] x3,
  output [7:0] x4,
  output Halt,
  output [7:0] x5,
  output [7:0] x6,
  output [7:0] x7,
  output [7:0] x8,
  output [7:0] x9,
  output [7:0] xA,
  output [7:0] xB,
  output [7:0] xC,
  output [7:0] xD,
  output [7:0] xE,
  output [7:0] xF,
  output [3:0] PC,
  output [7:0] Look_2
);

  wire clock_v2_1_exec_write, clock_v2_1_execute, clock_v2_1_fetch, clock_v2_1_write,
       control_unit_1_adder_mux_ir, control_unit_1_adder_mux_pc, control_unit_1_alu_add,
       control_unit_1_alu_and, control_unit_1_alu_xor, control_unit_1_ir_write, control_unit_1_memory_write,
       control_unit_1_pc_increment, control_unit_1_pc_load, control_unit_1_pc_write,
       control_unit_1_r_mux_alu, control_unit_1_r_mux_ir, control_unit_1_r_mux_mem, control_unit_1_r_write,
       n3_way_r_mux_1_out_24, n3_way_r_mux_1_out_25, n3_way_r_mux_1_out_26, n3_way_r_mux_1_out_27,
       n3_way_r_mux_1_out_28, n3_way_r_mux_1_out_29, n3_way_r_mux_1_out_30, n3_way_r_mux_1_out_31, or_2_out_3;
  wire [2:0] ir_1_out_10;
  wire [3:0] addr_mux_2_way_1_out_14, ir_1_out_17, or_1_out;
  wire [7:0] memory_bank_again_1_out, n8_bit_alu_1_out, n8_bitwise_or_1_o, n8r_1_out_10;

  IR ir_1 (
    .in_1(memory_bank_again_1_out[0]), .in_2(memory_bank_again_1_out[1]), .in_3(memory_bank_again_1_out[2]),
    .in_4(memory_bank_again_1_out[3]), .in_5(memory_bank_again_1_out[4]), .in_6(memory_bank_again_1_out[5]),
    .in_7(memory_bank_again_1_out[6]), .in_8(memory_bank_again_1_out[7]), .IR_WRITE(control_unit_1_ir_write),
    .out_10(ir_1_out_10[0]), .out_11(ir_1_out_10[1]), .out_12(ir_1_out_10[2]), .out_14(ir_1_out_17[3]),
    .out_15(ir_1_out_17[2]), .out_16(ir_1_out_17[1]), .out_17(ir_1_out_17[0]));  // open: out_13
  _3_way_r_mux u_3_way_r_mux_1 (
    .in_1(n8_bit_alu_1_out[0]), .in_2(n8_bit_alu_1_out[1]), .in_3(n8_bit_alu_1_out[2]),
    .in_4(n8_bit_alu_1_out[3]), .in_5(n8_bit_alu_1_out[4]), .in_6(n8_bit_alu_1_out[5]),
    .in_7(n8_bit_alu_1_out[6]), .in_8(n8_bit_alu_1_out[7]), .in_9(memory_bank_again_1_out[0]),
    .in_10(memory_bank_again_1_out[1]), .in_11(memory_bank_again_1_out[2]),
    .in_12(memory_bank_again_1_out[3]), .in_13(memory_bank_again_1_out[4]),
    .in_14(memory_bank_again_1_out[5]), .in_15(memory_bank_again_1_out[6]),
    .in_16(memory_bank_again_1_out[7]), .R_MUX_ALU(control_unit_1_r_mux_alu),
    .R_MUX_MEM(control_unit_1_r_mux_mem), .R_MUX_IR(control_unit_1_r_mux_ir), .out_24(n3_way_r_mux_1_out_24),
    .out_25(n3_way_r_mux_1_out_25), .out_26(n3_way_r_mux_1_out_26), .out_27(n3_way_r_mux_1_out_27),
    .out_28(n3_way_r_mux_1_out_28), .out_29(n3_way_r_mux_1_out_29), .out_30(n3_way_r_mux_1_out_30),
    .out_31(n3_way_r_mux_1_out_31), .in_17(ir_1_out_17[3]), .in_18(ir_1_out_17[2]), .in_19(ir_1_out_17[1]),
    .in_20(ir_1_out_17[0]));
  _8R u_8r_1 (
    .in_1(n3_way_r_mux_1_out_24), .in_2(n3_way_r_mux_1_out_25), .in_3(n3_way_r_mux_1_out_26),
    .in_4(n3_way_r_mux_1_out_27), .in_5(n3_way_r_mux_1_out_28), .in_6(n3_way_r_mux_1_out_29),
    .in_7(n3_way_r_mux_1_out_30), .in_8(n3_way_r_mux_1_out_31), .R_WRITE(control_unit_1_r_write),
    .out_10(n8r_1_out_10));
  _8_bit_ALU u_8_bit_alu_1 (
    .A(n8r_1_out_10), .B(memory_bank_again_1_out), .OUT(n8_bit_alu_1_out), .Cin(1'b0),
    .Adder(control_unit_1_alu_add), .AND(control_unit_1_alu_and), .XOR(control_unit_1_alu_xor));  // open: Cout
  Control_Unit control_unit_1 (
    .OP(ir_1_out_10), .ALU_ADD(control_unit_1_alu_add), .ALU_XOR(control_unit_1_alu_xor),
    .ALU_AND(control_unit_1_alu_and), .R_MUX_ALU(control_unit_1_r_mux_alu),
    .R_MUX_MEM(control_unit_1_r_mux_mem), .R_MUX_IR(control_unit_1_r_mux_ir),
    .R_WRITE(control_unit_1_r_write), .HALT(Halt), .MEMORY_WRITE(control_unit_1_memory_write),
    .PC_LOAD(control_unit_1_pc_load), .PC_INCREMENT(control_unit_1_pc_increment),
    .PC_WRITE(control_unit_1_pc_write), .ADDER_MUX_PC(control_unit_1_adder_mux_pc),
    .ADDER_MUX_IR(control_unit_1_adder_mux_ir), .FETCH(clock_v2_1_fetch), .FETCH_WRITE(clock_v2_1_write),
    .EXECUTE_WRITE(clock_v2_1_exec_write), .EXECUTE(clock_v2_1_execute), .IR_WRITE(control_unit_1_ir_write),
    .R(n8r_1_out_10));
  Clock_V2 clock_v2_1 (
    .Exec_Write(clock_v2_1_exec_write), .halt(Halt), .run(RUN), .fetch(clock_v2_1_fetch),
    .write(clock_v2_1_write), .Execute(clock_v2_1_execute), .Clock(Clock), .Running(RUNNING));
  PC2 pc2_1 (
    .in_1(ir_1_out_17[0]), .in_2(ir_1_out_17[1]), .in_3(ir_1_out_17[2]), .in_4(ir_1_out_17[3]),
    .INCREMENT(control_unit_1_pc_increment), .LOAD(control_unit_1_pc_load), .WRITE(control_unit_1_pc_write),
    .out_8(PC[0]), .out_9(PC[1]), .out_10(PC[2]), .out_11(PC[3]));
  addr_MUX_2_way addr_mux_2_way_1 (
    .in_1(PC[0]), .in_2(ir_1_out_17[0]), .in_3(PC[1]), .in_4(ir_1_out_17[1]), .in_5(PC[2]),
    .in_6(ir_1_out_17[2]), .in_7(PC[3]), .in_8(ir_1_out_17[3]), .ADDR_MUX_PC(control_unit_1_adder_mux_pc),
    .ADDR_MUX_IR(control_unit_1_adder_mux_ir), .out_11(addr_mux_2_way_1_out_14[3]),
    .out_12(addr_mux_2_way_1_out_14[2]), .out_13(addr_mux_2_way_1_out_14[1]),
    .out_14(addr_mux_2_way_1_out_14[0]));
  assign or_1_out = ADDR | addr_mux_2_way_1_out_14;  // OR_Gate or_1, 4 bits wide
  _8_bitwise_OR u_8_bitwise_or_1 (.A(DATA_IN), .B(n8r_1_out_10), .O(n8_bitwise_or_1_o));
  OR or_2 (.in_1(Load), .in_2(control_unit_1_memory_write), .out_3(or_2_out_3));
  Memory_Bank__again memory_bank_again_1 (
    .In(n8_bitwise_or_1_o), .Addr(or_1_out), .WE(or_2_out_3), .OUT(memory_bank_again_1_out), .x0(x0),
    .x1(x1), .x2(x2), .x3(x3), .x4(x4), .x5(x5), .x6(x6), .x7(x7), .x8(x8), .x9(x9), .xA(xA), .xB(xB),
    .xC(xC), .xD(xD), .xE(xE), .xF(xF));
  _9_bit_AND u_9_bit_and_1 (.O(memory_bank_again_1_out), .in_2(Look), .out_3(Look_2));

  // Notes on the sheet:
  //   Inputs for data values:
endmodule

module CPU_8_bit (
  input  in_1,
  input  in_2,
  input  in_3,
  input  in_4,
  input  in_5,
  input  in_6,
  input  in_7,
  input  in_8,
  input  in_9,
  input  in_10,
  input  Load,
  input  in_12,
  input  [2:0] in_13,
  input  in_14,
  input  in_15,
  input  in_16,
  input  in_17,
  input  Look,
  output [7:0] Look_2
);

  wire clock_1_out, control_unit_1_p4, control_unit_1_p5, control_unit_1_p6, control_unit_1_p11,
       control_unit_1_p12, control_unit_1_p13, control_unit_1_p14, control_unit_1_p15, control_unit_1_p16,
       control_unit_1_p17, control_unit_1_p18, control_unit_1_p19, control_unit_1_p20, control_unit_1_p21,
       control_unit_1_p22, n3_way_r_mux_1_p21, n3_way_r_mux_1_p22, n3_way_r_mux_1_p23, n3_way_r_mux_1_p24,
       n3_way_r_mux_1_p25, n3_way_r_mux_1_p26, n3_way_r_mux_1_p27, n3_way_r_mux_1_p28, n3_way_r_mux_1_p29,
       n3_way_r_mux_1_p30, n3_way_r_mux_1_p31, or_1_out_3, pc2_1_out_8, pc2_1_out_9, pc2_1_out_10,
       pc2_1_out_11;
  wire [3:0] addr_mux_2_way_1_out_11, ir_1_out_17, n4b_decider_1_out_4, n4b_decider_2_out_4;
  wire [7:0] decider_1_out_4, n3_way_r_mux_1_p1, n3_way_r_mux_1_p9, n8r_1_out_10;

  IR ir_1 (
    .in_1(n3_way_r_mux_1_p9[0]), .in_2(n3_way_r_mux_1_p9[1]), .in_3(n3_way_r_mux_1_p9[2]),
    .in_4(n3_way_r_mux_1_p9[3]), .in_5(n3_way_r_mux_1_p9[4]), .in_6(n3_way_r_mux_1_p9[5]),
    .in_7(n3_way_r_mux_1_p9[6]), .in_8(n3_way_r_mux_1_p9[7]), .IR_WRITE(control_unit_1_p13),
    .out_10(in_13[0]), .out_11(in_13[1]), .out_12(in_13[2]), .out_14(ir_1_out_17[3]),
    .out_15(ir_1_out_17[2]), .out_16(ir_1_out_17[1]), .out_17(ir_1_out_17[0]));  // open: out_13
  // _3_way_r_mux 3_way_r_mux_1: pin names not known; wires that end beside it: n3_way_r_mux_1_p1[0], n3_way_r_mux_1_p1[1], n3_way_r_mux_1_p1[2], n3_way_r_mux_1_p1[3], n3_way_r_mux_1_p1[4], n3_way_r_mux_1_p1[5], n3_way_r_mux_1_p1[6], n3_way_r_mux_1_p1[7], n3_way_r_mux_1_p9[0], n3_way_r_mux_1_p9[1], n3_way_r_mux_1_p9[2], n3_way_r_mux_1_p9[3], n3_way_r_mux_1_p9[4], n3_way_r_mux_1_p9[5], n3_way_r_mux_1_p9[6], n3_way_r_mux_1_p9[7], ir_1_out_17[3], ir_1_out_17[2], ir_1_out_17[1], ir_1_out_17[0], n3_way_r_mux_1_p21, n3_way_r_mux_1_p22, n3_way_r_mux_1_p23, n3_way_r_mux_1_p24, n3_way_r_mux_1_p25, n3_way_r_mux_1_p26, n3_way_r_mux_1_p27, n3_way_r_mux_1_p28, n3_way_r_mux_1_p29, n3_way_r_mux_1_p30, n3_way_r_mux_1_p31
  _8R u_8r_1 (
    .in_1(n3_way_r_mux_1_p24), .in_2(n3_way_r_mux_1_p25), .in_3(n3_way_r_mux_1_p26),
    .in_4(n3_way_r_mux_1_p27), .in_5(n3_way_r_mux_1_p28), .in_6(n3_way_r_mux_1_p29),
    .in_7(n3_way_r_mux_1_p30), .in_8(n3_way_r_mux_1_p31), .R_WRITE(control_unit_1_p11), .out_10(n8r_1_out_10));
  _8_bit_ALU u_8_bit_alu_1 (
    .A(decider_1_out_4), .B(n3_way_r_mux_1_p9), .OUT(n3_way_r_mux_1_p1), .Cin(in_9),
    .Adder(control_unit_1_p4), .AND(control_unit_1_p6), .XOR(control_unit_1_p5));  // open: Cout
  decider decider_1 (
    .in_1(Load), .in_2({in_1, in_2, in_3, in_4, in_5, in_6, in_7, in_8}), .in_3(n8r_1_out_10),
    .out_4(decider_1_out_4));
  Clock clock_1 (.out(clock_1_out));
  // Control_Unit control_unit_1: pin names not known; wires that end beside it: in_13[0], in_13[1], in_13[2], control_unit_1_p4, control_unit_1_p5, control_unit_1_p6, n8r_1_out_10, n3_way_r_mux_1_p21, n3_way_r_mux_1_p22, n3_way_r_mux_1_p23, control_unit_1_p11, control_unit_1_p12, control_unit_1_p13, control_unit_1_p14, control_unit_1_p15, control_unit_1_p16, control_unit_1_p17, control_unit_1_p18, control_unit_1_p19, control_unit_1_p20, control_unit_1_p21, control_unit_1_p22
  Clock_V2 clock_v2_1 (
    .Exec_Write(control_unit_1_p16), .halt(in_12), .run(in_10), .fetch(control_unit_1_p12),
    .write(control_unit_1_p14), .Execute(control_unit_1_p15), .Clock(clock_1_out));  // open: Running
  _4b_decider u_4b_decider_1 (
    .Selection(in_10), .A({in_14, in_15, in_16, in_17}), .B(ir_1_out_17), .out_4(n4b_decider_1_out_4));
  PC2 pc2_1 (
    .in_1(n4b_decider_1_out_4[0]), .in_2(n4b_decider_1_out_4[1]), .in_3(n4b_decider_1_out_4[2]),
    .in_4(n4b_decider_1_out_4[3]), .INCREMENT(control_unit_1_p19), .LOAD(control_unit_1_p18),
    .WRITE(control_unit_1_p20), .out_8(pc2_1_out_8), .out_9(pc2_1_out_9), .out_10(pc2_1_out_10),
    .out_11(pc2_1_out_11));
  addr_MUX_2_way addr_mux_2_way_1 (
    .in_1(pc2_1_out_8), .in_2(pc2_1_out_9), .in_3(pc2_1_out_10), .in_4(pc2_1_out_11), .in_5(ir_1_out_17[0]),
    .in_6(ir_1_out_17[1]), .in_7(ir_1_out_17[2]), .in_8(ir_1_out_17[3]), .ADDR_MUX_PC(control_unit_1_p21),
    .ADDR_MUX_IR(control_unit_1_p22), .out_11(addr_mux_2_way_1_out_11[0]),
    .out_12(addr_mux_2_way_1_out_11[1]), .out_13(addr_mux_2_way_1_out_11[2]),
    .out_14(addr_mux_2_way_1_out_11[3]));
  _4b_decider u_4b_decider_2 (
    .Selection(1'b1), .A({in_14, in_15, in_16, in_17}), .B(addr_mux_2_way_1_out_11),
    .out_4(n4b_decider_2_out_4));
  OR or_1 (.in_1(Load), .in_2(control_unit_1_p17), .out_3(or_1_out_3));
  Mem_Bank mem_bank_1 (
    .Memory_Write(or_1_out_3), .in_3(n4b_decider_2_out_4[0]), .in_4(n4b_decider_2_out_4[1]),
    .in_5(n4b_decider_2_out_4[2]), .in_6(n4b_decider_2_out_4[3]), .in_1(decider_1_out_4),
    .out_8(n3_way_r_mux_1_p9), .in_7(clock_1_out));
  _9_bit_AND u_9_bit_and_1 (.O(n3_way_r_mux_1_p9), .in_2(Look), .out_3(Look_2));

  // Notes on the sheet:
  //   Inputs for data values:
endmodule

module NOT (
  input  X,
  output Q
);

  Pull_Resistor pull_resistor_1 (.node(Q));
  Transistor transistor_1 (.in(1'b1), .out(Q), .gate(X));
endmodule

module AND (
  input  in_1,
  input  in_2,
  output out_3
);

  wire transistor_1_out;

  Pull_Resistor pull_resistor_1 (.node(in_1));
  Pull_Resistor pull_resistor_2 (.node(in_2));
  Transistor #(.\type ("n")) transistor_1 (.in(1'b1), .out(transistor_1_out), .gate(in_1));
  Pull_Resistor pull_resistor_3 (.node(out_3));
  Transistor #(.\type ("n")) transistor_2 (.in(transistor_1_out), .out(out_3), .gate(in_2));
endmodule

module OR (
  input  in_1,
  input  in_2,
  output out_3
);

  Transistor #(.\type ("n")) transistor_1 (.in(1'b1), .out(out_3), .gate(in_1));
  Transistor #(.\type ("n")) transistor_2 (.in(1'b1), .out(out_3), .gate(in_2));
  Pull_Resistor pull_resistor_1 (.node(out_3));
endmodule

module XOR (
  input  INPUT_1,
  input  INPUT_2,
  output OUT
);

  wire and_1_out_3, and_2_out_3, not_1_q, not_2_q;

  NOT not_1 (.Q(not_1_q));  // open: X
  NOT not_2 (.Q(not_2_q));  // open: X
  AND and_1 (.in_1(not_1_q), .out_3(and_1_out_3), .in_2(INPUT_2));
  AND and_2 (.in_1(INPUT_1), .out_3(and_2_out_3), .in_2(not_2_q));
  OR or_1 (.in_1(and_1_out_3), .in_2(and_2_out_3), .out_3(OUT));

  // Notes on the sheet:
  //   NOT
  //   NOT
endmodule

module NAND (
  input  AND,
  input  in_2,
  output out_3
);

  wire and_1_out_3;

  AND and_1 (.in_1(AND), .out_3(and_1_out_3), .in_2(in_2));
  NOT NOT (.Q(out_3));  // open: X
endmodule

module NOR (
  input  in_1,
  input  in_2,
  output out_3
);

  wire nand_1_out_3, nand_2_out_3, nand_3_out_3;

  NAND nand_1 (.AND(in_1), .in_2(in_1), .out_3(nand_1_out_3));
  NAND nand_2 (.AND(in_2), .in_2(in_2), .out_3(nand_2_out_3));
  NAND nand_3 (.AND(nand_1_out_3), .in_2(nand_2_out_3), .out_3(nand_3_out_3));
  NAND nand_4 (.AND(nand_3_out_3), .in_2(nand_3_out_3), .out_3(out_3));

  // Notes on the sheet:
  //   NAND
  //   NAND
  //   NAND
  //   NAND
endmodule

module XNOR (
  input  in_1,
  input  in_2,
  output out_3
);

  wire and_1_out_3, nor_1_out_3;

  AND and_1 (.in_1(in_2), .out_3(and_1_out_3), .in_2(in_1));
  NOR nor_1 (.in_1(in_1), .in_2(in_2), .out_3(nor_1_out_3));
  OR or_1 (.in_1(nor_1_out_3), .in_2(and_1_out_3), .out_3(out_3));

  // Notes on the sheet:
  //   NOR
  //   AND
  //   OR
endmodule

// FA
module Full_Adder (
  input  A,
  input  B,
  input  CIN,
  output SUM,
  output COUT
);

  wire and_1_out_3, and_2_out_3, XOR_out;

  XOR XOR (.INPUT_1(A), .INPUT_2(B), .OUT(XOR_out));
  AND and_1 (.in_1(A), .out_3(and_1_out_3), .in_2(B));
  XOR XOR_2 (.INPUT_1(XOR_out), .INPUT_2(CIN), .OUT(SUM));
  AND and_2 (.in_1(XOR_out), .out_3(and_2_out_3), .in_2(CIN));
  OR OR (.in_1(and_1_out_3), .in_2(and_2_out_3), .out_3(COUT));

  // Notes on the sheet:
  //   Sum
  //   Carry Out (A+B)
endmodule

module Adder4bit (
  input  A3,
  input  A2,
  input  A1,
  input  A0,
  input  B3,
  input  B2,
  input  B1,
  input  B0,
  input  CIN,
  output COUT,
  output S3,
  output S2,
  output S1,
  output S0
);

  wire FA_2_p2, FA_3_p2, FA_p2;

  // Full_Adder FA: pin names not known; wires that end beside it: S3, FA_p2, FA_p2
  // Full_Adder FA_2: pin names not known; wires that end beside it: S2, FA_2_p2, FA_2_p2
  // Full_Adder FA_3: pin names not known; wires that end beside it: S1, FA_3_p2, FA_3_p2
  // Full_Adder FA_4: pin names not known; wires that end beside it: S0, CIN
endmodule

// 8-Bit ALU
module _8_bit_ALU (
  input  Adder,
  input  AND,
  input  XOR,
  input  Cin,
  input  [7:0] A,
  input  [7:0] B,
  output Cout,
  output [7:0] OUT
);

  wire n3_8_decoder_1_out_7, n3_8_decoder_1_out_9, n3_8_decoder_1_out_10;
  wire [7:0] adder_1_sum, n8_bit_and_1_o, n8_bit_xor_1_o, n9_bit_and_1_out_3, n9_bit_and_2_out_3,
       n9_bit_and_3_out_3;

  Adder adder_1 (.A(A), .in_2(Cin), .B(B), .in_4(Cin), .Sum(adder_1_sum), .Cout(Cout));
  _8_bit_AND u_8_bit_and_1 (.A(A), .B(B), .O(n8_bit_and_1_o));
  _8_bit_XOR u_8_bit_xor_1 (.A(A), .B(B), .O(n8_bit_xor_1_o));
  _3_8_decoder u_3_8_decoder_1 (
    .A(XOR), .B(AND), .C(Adder), .out_7(n3_8_decoder_1_out_7), .out_9(n3_8_decoder_1_out_9),
    .out_10(n3_8_decoder_1_out_10));  // open: out_4, out_5, out_6, out_8, out_11
  _9_bit_AND u_9_bit_and_1 (.O(adder_1_sum), .in_2(n3_8_decoder_1_out_10), .out_3(n9_bit_and_1_out_3));
  _9_bit_AND u_9_bit_and_2 (.O(n8_bit_and_1_o), .in_2(n3_8_decoder_1_out_9), .out_3(n9_bit_and_2_out_3));
  _9_bit_AND u_9_bit_and_3 (.O(n8_bit_xor_1_o), .in_2(n3_8_decoder_1_out_7), .out_3(n9_bit_and_3_out_3));
  _8_bitx3_OR u_8_bitx3_or_1 (
    .ADDER(n9_bit_and_1_out_3), .AND(n9_bit_and_2_out_3), .XOR(n9_bit_and_3_out_3), .out_4(OUT));

  // Notes on the sheet:
  //   Decoder
  //   AND
  //   AND
  //   AND
  //   DECODER
  //   OR
  //   OR
endmodule

module Full_Adder_v2 (
  input  A,
  input  B,
  input  CIN,
  output Sum,
  output COUT
);

  wire and_1_out_3, and_2_out_3, xor_1_out;

  AND and_1 (.in_1(A), .out_3(and_1_out_3), .in_2(B));
  XOR xor_1 (.INPUT_1(A), .INPUT_2(B), .OUT(xor_1_out));
  AND and_2 (.in_1(xor_1_out), .out_3(and_2_out_3), .in_2(CIN));
  XOR xor_2 (.INPUT_1(xor_1_out), .INPUT_2(CIN), .OUT(Sum));
  OR or_1 (.in_1(and_1_out_3), .in_2(and_2_out_3), .out_3(COUT));
endmodule

module _4_bit_Add_Sub (
  input  Cin,
  input  A0,
  input  A1,
  input  A2,
  input  A3,
  input  B0,
  input  B1,
  input  B2,
  input  B3,
  output S0,
  output S1,
  output S2,
  output S3,
  output Cout
);

  wire full_adder_v2_1_cout, full_adder_v2_2_cout, full_adder_v2_3_cout, xor_1_out, xor_2_out, xor_3_out,
       xor_4_out;

  XOR xor_1 (.INPUT_1(Cin), .INPUT_2(B0), .OUT(xor_1_out));
  XOR xor_2 (.INPUT_1(Cin), .INPUT_2(B1), .OUT(xor_2_out));
  XOR xor_3 (.INPUT_1(Cin), .INPUT_2(B2), .OUT(xor_3_out));
  XOR xor_4 (.INPUT_1(Cin), .INPUT_2(B3), .OUT(xor_4_out));
  Full_Adder_v2 full_adder_v2_1 (.A(A0), .B(xor_1_out), .CIN(Cin), .Sum(S0), .COUT(full_adder_v2_1_cout));
  Full_Adder_v2 full_adder_v2_2 (
    .A(A1), .B(xor_2_out), .CIN(full_adder_v2_1_cout), .Sum(S1), .COUT(full_adder_v2_2_cout));
  Full_Adder_v2 full_adder_v2_3 (
    .A(A2), .B(xor_3_out), .CIN(full_adder_v2_2_cout), .Sum(S2), .COUT(full_adder_v2_3_cout));
  Full_Adder_v2 full_adder_v2_4 (.A(A3), .B(xor_4_out), .CIN(full_adder_v2_3_cout), .Sum(S3), .COUT(Cout));
endmodule

module _8_bit_add_sub (
  input  A7,
  input  A6,
  input  A5,
  input  A4,
  input  A3,
  input  A2,
  input  A1,
  input  A0,
  input  CIN_Mode,
  input  B7,
  input  B6,
  input  B5,
  input  B4,
  input  B3,
  input  B2,
  input  B1,
  input  B0,
  output Cout,
  output S7,
  output S6,
  output S5,
  output S4,
  output S3,
  output S2,
  output S1,
  output S0
);

  wire full_adder_2_cout, full_adder_3_cout, full_adder_4_cout, full_adder_5_cout, full_adder_6_cout,
       full_adder_7_cout, full_adder_8_cout, xor_1_out, xor_2_out, xor_3_out, xor_4_out, xor_5_out,
       xor_6_out, xor_7_out, xor_8_out;

  XOR xor_1 (.INPUT_1(B7), .INPUT_2(CIN_Mode), .OUT(xor_1_out));
  Full_Adder full_adder_1 (.A(A7), .B(xor_1_out), .CIN(full_adder_2_cout), .SUM(S7), .COUT(Cout));
  XOR xor_2 (.INPUT_1(B6), .INPUT_2(CIN_Mode), .OUT(xor_2_out));
  Full_Adder full_adder_2 (.A(A6), .B(xor_2_out), .CIN(full_adder_3_cout), .SUM(S6), .COUT(full_adder_2_cout));
  Full_Adder full_adder_3 (.A(A5), .B(xor_3_out), .CIN(full_adder_4_cout), .SUM(S5), .COUT(full_adder_3_cout));
  XOR xor_3 (.INPUT_1(B5), .INPUT_2(CIN_Mode), .OUT(xor_3_out));
  XOR xor_4 (.INPUT_1(CIN_Mode), .INPUT_2(B4), .OUT(xor_4_out));
  Full_Adder full_adder_4 (.A(A4), .B(xor_4_out), .CIN(full_adder_5_cout), .SUM(S4), .COUT(full_adder_4_cout));
  Full_Adder full_adder_5 (.A(A3), .B(xor_5_out), .CIN(full_adder_6_cout), .SUM(S3), .COUT(full_adder_5_cout));
  XOR xor_5 (.INPUT_1(B3), .INPUT_2(CIN_Mode), .OUT(xor_5_out));
  XOR xor_6 (.INPUT_1(B2), .INPUT_2(CIN_Mode), .OUT(xor_6_out));
  Full_Adder full_adder_6 (.A(A2), .B(xor_6_out), .CIN(full_adder_7_cout), .SUM(S2), .COUT(full_adder_6_cout));
  Full_Adder full_adder_7 (.A(A1), .B(xor_7_out), .CIN(full_adder_8_cout), .SUM(S1), .COUT(full_adder_7_cout));
  XOR xor_7 (.INPUT_1(B1), .INPUT_2(CIN_Mode), .OUT(xor_7_out));
  XOR xor_8 (.INPUT_1(CIN_Mode), .INPUT_2(B0), .OUT(xor_8_out));
  Full_Adder full_adder_8 (.A(A0), .B(xor_8_out), .CIN(CIN_Mode), .SUM(S0), .COUT(full_adder_8_cout));
endmodule

module _8_bit_AND (
  input  [7:0] A,
  input  [7:0] B,
  output [7:0] O
);

  AND and_1 (.in_1(B[7]), .out_3(O[7]), .in_2(A[7]));
  AND and_2 (.in_1(B[5]), .out_3(O[5]), .in_2(A[5]));
  AND and_3 (.in_1(B[6]), .out_3(O[6]), .in_2(A[6]));
  AND and_4 (.in_1(B[4]), .out_3(O[4]), .in_2(A[4]));
  AND and_5 (.in_1(B[3]), .out_3(O[3]), .in_2(A[3]));
  AND and_6 (.in_1(B[1]), .out_3(O[1]), .in_2(A[1]));
  AND and_7 (.in_1(B[2]), .out_3(O[2]), .in_2(A[2]));
  AND and_8 (.in_1(B[0]), .out_3(O[0]), .in_2(A[0]));
endmodule

module _8_bit_XOR (
  input  [7:0] A,
  input  [7:0] B,
  output [7:0] O
);

  XOR xor_1 (.INPUT_1(B[7]), .INPUT_2(A[7]), .OUT(O[7]));
  XOR xor_2 (.INPUT_1(B[6]), .INPUT_2(A[6]), .OUT(O[6]));
  XOR xor_3 (.INPUT_1(B[5]), .INPUT_2(A[5]), .OUT(O[5]));
  XOR xor_4 (.INPUT_1(B[4]), .INPUT_2(A[4]), .OUT(O[4]));
  XOR xor_5 (.INPUT_1(B[3]), .INPUT_2(A[3]), .OUT(O[3]));
  XOR xor_6 (.INPUT_1(B[2]), .INPUT_2(A[2]), .OUT(O[2]));
  XOR xor_7 (.INPUT_1(B[1]), .INPUT_2(A[1]), .OUT(O[1]));
  XOR xor_8 (.INPUT_1(B[0]), .INPUT_2(A[0]), .OUT(O[0]));
endmodule

module _8_bit_OR (
  input  B5,
  input  A4,
  input  A0,
  input  B7,
  input  A7,
  input  B6,
  input  A6,
  input  A5,
  input  B4,
  input  B3,
  input  A3,
  input  B2,
  input  A2,
  input  B1,
  input  A1,
  input  B0,
  output O7,
  output O6,
  output O5,
  output O4,
  output O3,
  output O2,
  output O1,
  output O0
);

  OR or_1 (.in_1(A7), .in_2(B7), .out_3(O7));
  OR or_2 (.in_1(A6), .in_2(B6), .out_3(O6));
  OR or_3 (.in_1(A5), .in_2(B5), .out_3(O5));
  OR or_4 (.in_1(A4), .in_2(B4), .out_3(O4));
  OR or_5 (.in_1(A3), .in_2(B3), .out_3(O3));
  OR or_6 (.in_1(A2), .in_2(B2), .out_3(O2));
  OR or_7 (.in_1(A1), .in_2(B1), .out_3(O1));
  OR or_8 (.in_1(A0), .in_2(B0), .out_3(O0));
endmodule

module Adder_8_bit (
  input  [7:0] B,
  input  [7:0] A,
  input  Cin,
  output [7:0] O,
  output Cout
);

  wire full_adder_2_cout, full_adder_3_cout, full_adder_4_cout, full_adder_5_cout, full_adder_6_cout,
       full_adder_7_cout, full_adder_8_cout;

  Full_Adder full_adder_1 (.A(A[7]), .B(B[7]), .CIN(full_adder_2_cout), .SUM(O[7]), .COUT(Cout));
  Full_Adder full_adder_2 (.A(A[6]), .B(B[6]), .CIN(full_adder_3_cout), .SUM(O[6]), .COUT(full_adder_2_cout));
  Full_Adder full_adder_3 (.A(A[5]), .B(B[5]), .CIN(full_adder_4_cout), .SUM(O[5]), .COUT(full_adder_3_cout));
  Full_Adder full_adder_4 (.A(A[4]), .B(B[4]), .CIN(full_adder_5_cout), .SUM(O[4]), .COUT(full_adder_4_cout));
  Full_Adder full_adder_5 (.A(A[3]), .B(B[3]), .CIN(full_adder_6_cout), .SUM(O[3]), .COUT(full_adder_5_cout));
  Full_Adder full_adder_6 (.A(A[2]), .B(B[2]), .CIN(full_adder_7_cout), .SUM(O[2]), .COUT(full_adder_6_cout));
  Full_Adder full_adder_7 (.A(A[1]), .B(B[1]), .CIN(full_adder_8_cout), .SUM(O[1]), .COUT(full_adder_7_cout));
  Full_Adder full_adder_8 (.A(A[0]), .B(B[0]), .CIN(Cin), .SUM(O[0]), .COUT(full_adder_8_cout));
endmodule

module _3_8_decoder (
  input  A,
  input  B,
  input  C,
  output out_4,
  output out_5,
  output out_6,
  output out_7,
  output out_8,
  output out_9,
  output out_10,
  output out_11
);

  wire not_1_q, not_2_q, not_3_q;

  NOT not_1 (.Q(not_1_q));  // open: X
  NOT not_2 (.Q(not_2_q));  // open: X
  NOT not_3 (.Q(not_3_q));  // open: X
  _3_input_AND u_3_input_and_1 (.in_1(A), .in_2(B), .in_3(C), .out_4(out_4));
  _3_input_AND u_3_input_and_2 (.in_1(A), .in_2(B), .in_3(not_1_q), .out_4(out_5));
  _3_input_AND u_3_input_and_3 (.in_1(A), .in_2(not_2_q), .in_3(C), .out_4(out_6));
  _3_input_AND u_3_input_and_4 (.in_1(A), .in_2(not_2_q), .in_3(not_1_q), .out_4(out_7));
  _3_input_AND u_3_input_and_5 (.in_1(not_3_q), .in_2(B), .in_3(C), .out_4(out_8));
  _3_input_AND u_3_input_and_6 (.in_1(not_3_q), .in_2(B), .in_3(not_1_q), .out_4(out_9));
  _3_input_AND u_3_input_and_7 (.in_1(not_3_q), .in_2(not_2_q), .in_3(C), .out_4(out_10));
  _3_input_AND u_3_input_and_8 (.in_1(not_3_q), .in_2(not_2_q), .in_3(not_1_q), .out_4(out_11));
endmodule

module _3x8_MUX (
  input  X,
  input  A,
  input  B,
  input  C,
  output [7:0] Out
);

  wire not_1_q, not_2_q, not_3_q;

  NOT not_1 (.Q(not_1_q), .X(A));
  NOT not_2 (.Q(not_2_q), .X(B));
  NOT not_3 (.Q(not_3_q), .X(C));
  _4_bit_AND u_4_bit_and_1 (.in_1(X), .in_2(not_1_q), .in_3(not_2_q), .in_4(not_3_q), .out_5(Out[0]));
  _4_bit_AND u_4_bit_and_2 (.in_1(X), .in_2(not_1_q), .in_3(not_2_q), .in_4(C), .out_5(Out[1]));
  _4_bit_AND u_4_bit_and_3 (.in_1(X), .in_2(not_1_q), .in_3(B), .in_4(not_3_q), .out_5(Out[2]));
  _4_bit_AND u_4_bit_and_4 (.in_1(X), .in_2(not_1_q), .in_3(B), .in_4(C), .out_5(Out[3]));
  _4_bit_AND u_4_bit_and_5 (.in_1(X), .in_2(A), .in_3(not_2_q), .in_4(not_3_q), .out_5(Out[4]));
  _4_bit_AND u_4_bit_and_6 (.in_1(X), .in_2(A), .in_3(not_2_q), .in_4(C), .out_5(Out[5]));
  _4_bit_AND u_4_bit_and_7 (.in_1(X), .in_2(A), .in_3(B), .in_4(not_3_q), .out_5(Out[6]));
  _4_bit_AND u_4_bit_and_8 (.in_1(X), .in_2(A), .in_3(B), .in_4(C), .out_5(Out[7]));

  // Notes on the sheet:
  //   NOT
  //   NOT
  //   NOT
  //   4B AND
  //   4B AND
  //   4B AND
  //   4B AND
  //   4B AND
  //   4B AND
  //   4B AND
  //   4B AND
endmodule

module MAJ (
  input  A,
  input  B,
  input  x,
  output Out
);

  wire and_1_out_3, and_2_out_3, and_3_out_3, or_1_out_3;

  AND and_1 (.in_1(A), .out_3(and_1_out_3), .in_2(B));
  AND and_2 (.in_1(A), .out_3(and_2_out_3), .in_2(x));
  AND and_3 (.in_1(B), .out_3(and_3_out_3), .in_2(x));
  OR or_1 (.in_1(and_1_out_3), .in_2(and_2_out_3), .out_3(or_1_out_3));
  OR or_2 (.in_1(or_1_out_3), .in_2(and_3_out_3), .out_3(Out));
endmodule

module ODD (
  input  A,
  input  B,
  input  x,
  output Out
);

  wire xor_1_out;

  XOR xor_1 (.INPUT_1(A), .INPUT_2(B), .OUT(xor_1_out));
  XOR xor_2 (.INPUT_1(xor_1_out), .INPUT_2(x), .OUT(Out));
endmodule

module Adder (
  input  [7:0] A,
  input  in_2,
  input  [7:0] B,
  input  in_4,
  output [7:0] Sum,
  output Cout
);

  wire maj_1_out, maj_2_out, maj_3_out, maj_4_out, maj_5_out, maj_6_out, maj_7_out;

  MAJ maj_1 (.A(A[0]), .B(B[0]), .x(in_2), .Out(maj_1_out));
  ODD odd_1 (.A(A[0]), .B(B[0]), .x(in_4), .Out(Sum[0]));
  MAJ maj_2 (.A(A[1]), .B(B[1]), .x(maj_1_out), .Out(maj_2_out));
  ODD odd_2 (.A(A[1]), .B(B[1]), .x(maj_1_out), .Out(Sum[1]));
  MAJ maj_3 (.A(A[2]), .B(B[2]), .x(maj_2_out), .Out(maj_3_out));
  ODD odd_3 (.A(A[2]), .B(B[2]), .x(maj_2_out), .Out(Sum[2]));
  MAJ maj_4 (.A(A[3]), .B(B[3]), .x(maj_3_out), .Out(maj_4_out));
  ODD odd_4 (.A(A[3]), .B(B[3]), .x(maj_3_out), .Out(Sum[3]));
  MAJ maj_5 (.A(A[4]), .B(B[4]), .x(maj_4_out), .Out(maj_5_out));
  ODD odd_5 (.A(A[4]), .B(B[4]), .x(maj_4_out), .Out(Sum[4]));
  MAJ maj_6 (.A(A[5]), .B(B[5]), .x(maj_5_out), .Out(maj_6_out));
  ODD odd_6 (.A(A[5]), .B(B[5]), .x(maj_5_out), .Out(Sum[5]));
  MAJ maj_7 (.A(A[6]), .B(B[6]), .x(maj_6_out), .Out(maj_7_out));
  ODD odd_7 (.A(A[6]), .B(B[6]), .x(maj_6_out), .Out(Sum[6]));
  MAJ maj_8 (.A(A[7]), .B(B[7]), .x(maj_7_out), .Out(Cout));
  ODD odd_8 (.A(A[7]), .B(B[7]), .x(maj_7_out), .Out(Sum[7]));
endmodule

module _3_input_AND (
  input  in_1,
  input  in_2,
  input  in_3,
  output out_4
);

  wire and_1_out_3;

  AND and_1 (.in_1(in_1), .out_3(and_1_out_3), .in_2(in_2));
  AND and_2 (.in_1(and_1_out_3), .out_3(out_4), .in_2(in_3));
endmodule

module _9_bit_AND (
  input  [7:0] O,
  input  in_2,
  output [7:0] out_3
);

  AND and_1 (.in_1(in_2), .out_3(out_3[7]), .in_2(O[7]));
  AND and_2 (.in_1(in_2), .out_3(out_3[6]), .in_2(O[6]));
  AND and_3 (.in_1(in_2), .out_3(out_3[5]), .in_2(O[5]));
  AND and_4 (.in_1(in_2), .out_3(out_3[4]), .in_2(O[4]));
  AND and_5 (.in_1(in_2), .out_3(out_3[3]), .in_2(O[3]));
  AND and_6 (.in_1(in_2), .out_3(out_3[2]), .in_2(O[2]));
  AND and_7 (.in_1(in_2), .out_3(out_3[1]), .in_2(O[1]));
  AND and_8 (.in_1(in_2), .out_3(out_3[0]), .in_2(O[0]));
endmodule

module _8_bitx3_OR (
  input  [7:0] ADDER,
  input  [7:0] AND,
  input  [7:0] XOR,
  output [7:0] out_4
);

  _3_input_OR u_3_input_or_1 (.in_1(ADDER[7]), .AND(AND[7]), .XOR(XOR[7]), .out_4(out_4[7]));
  _3_input_OR u_3_input_or_2 (.in_1(ADDER[6]), .AND(AND[6]), .XOR(XOR[6]), .out_4(out_4[6]));
  _3_input_OR u_3_input_or_3 (.in_1(ADDER[5]), .AND(AND[5]), .XOR(XOR[5]), .out_4(out_4[5]));
  _3_input_OR u_3_input_or_4 (.in_1(ADDER[4]), .AND(AND[4]), .XOR(XOR[4]), .out_4(out_4[4]));
  _3_input_OR u_3_input_or_5 (.in_1(ADDER[3]), .AND(AND[3]), .XOR(XOR[3]), .out_4(out_4[3]));
  _3_input_OR u_3_input_or_6 (.in_1(ADDER[2]), .AND(AND[2]), .XOR(XOR[2]), .out_4(out_4[2]));
  _3_input_OR u_3_input_or_7 (.in_1(ADDER[1]), .AND(AND[1]), .XOR(XOR[1]), .out_4(out_4[1]));
  _3_input_OR u_3_input_or_8 (.in_1(ADDER[0]), .AND(AND[0]), .XOR(XOR[0]), .out_4(out_4[0]));
endmodule

module _3_input_OR (
  input  in_1,
  input  AND,
  input  XOR,
  output out_4
);

  wire or_2_out_3;

  OR or_1 (.in_1(or_2_out_3), .in_2(in_1), .out_3(out_4));
  OR or_2 (.in_1(XOR), .in_2(AND), .out_3(or_2_out_3));
endmodule

module Memory_Bit (
  input  Write,
  input  Input,
  output Memory
);

  D_Flip_Flop d_ff_1 (.clk(Write), .D(Input), .Q(Memory));  // open: Qn, preset, en, reset
endmodule

// Memory Bit V2
module Memory_bit_v2 (
  input  Input,
  input  Write,
  output M
);

  wire nor_1_out_3, nor_3_out_3, nor_4_out_3, not_1_q, not_2_q, not_3_q;

  NOT not_1 (.Q(not_1_q));  // open: X
  NOR nor_1 (.in_1(Input), .in_2(not_1_q), .out_3(nor_1_out_3));
  NOR nor_2 (.in_1(nor_4_out_3), .in_2(nor_1_out_3), .out_3(M));
  NOT not_2 (.Q(not_2_q));  // open: X
  NOR nor_3 (.in_1(not_3_q), .in_2(not_2_q), .out_3(nor_3_out_3));
  NOR nor_4 (.in_1(nor_3_out_3), .in_2(M), .out_3(nor_4_out_3));
  NOT not_3 (.Q(not_3_q));  // open: X
endmodule

module Logical_Shift (
  input  [7:0] in_1,
  input  _1_for_Right,
  output [7:0] out_3
);

  wire and_1_out_3, and_3_out_3, and_4_out_3, and_5_out_3, and_6_out_3, and_7_out_3, and_8_out_3,
       and_9_out_3, and_10_out_3, and_11_out_3, and_12_out_3, and_14_out_3, not_1_q;

  NOT not_1 (.Q(not_1_q));  // open: X
  AND and_1 (.in_1(_1_for_Right), .out_3(and_1_out_3), .in_2(in_1[7]));
  AND and_2 (.in_1(in_1[6]), .out_3(out_3[7]), .in_2(not_1_q));
  AND and_3 (.in_1(_1_for_Right), .out_3(and_3_out_3), .in_2(in_1[6]));
  OR or_1 (.in_1(and_4_out_3), .in_2(and_1_out_3), .out_3(out_3[6]));
  AND and_4 (.in_1(in_1[5]), .out_3(and_4_out_3), .in_2(not_1_q));
  AND and_5 (.in_1(_1_for_Right), .out_3(and_5_out_3), .in_2(in_1[5]));
  OR or_2 (.in_1(and_6_out_3), .in_2(and_3_out_3), .out_3(out_3[5]));
  AND and_6 (.in_1(in_1[4]), .out_3(and_6_out_3), .in_2(not_1_q));
  AND and_7 (.in_1(_1_for_Right), .out_3(and_7_out_3), .in_2(in_1[4]));
  OR or_3 (.in_1(and_8_out_3), .in_2(and_5_out_3), .out_3(out_3[4]));
  AND and_8 (.in_1(in_1[3]), .out_3(and_8_out_3), .in_2(not_1_q));
  AND and_9 (.in_1(_1_for_Right), .out_3(and_9_out_3), .in_2(in_1[3]));
  OR or_4 (.in_1(and_10_out_3), .in_2(and_7_out_3), .out_3(out_3[3]));
  AND and_10 (.in_1(in_1[2]), .out_3(and_10_out_3), .in_2(not_1_q));
  AND and_11 (.in_1(_1_for_Right), .out_3(and_11_out_3), .in_2(in_1[2]));
  OR or_5 (.in_1(and_12_out_3), .in_2(and_9_out_3), .out_3(out_3[2]));
  AND and_12 (.in_1(in_1[1]), .out_3(and_12_out_3), .in_2(not_1_q));
  AND and_13 (.in_1(_1_for_Right), .out_3(out_3[0]), .in_2(in_1[1]));
  OR or_6 (.in_1(and_14_out_3), .in_2(and_11_out_3), .out_3(out_3[1]));
  AND and_14 (.in_1(not_1_q), .out_3(and_14_out_3), .in_2(in_1[0]));

  // Notes on the sheet:
  //   0 for Left
endmodule

module Eight_Register (
  input  in_1,
  input  in_2,
  input  in_3,
  input  in_4,
  input  in_5,
  input  in_6,
  input  in_7,
  input  in_8,
  input  in_9,
  output out_10,
  output out_11,
  output out_12,
  output out_13,
  output out_14,
  output out_15,
  output out_16,
  output out_17
);

  Memory_bit_v2 memory_bit_v2_1 (.Input(in_1), .Write(in_9), .M(out_10));
  Memory_bit_v2 memory_bit_v2_2 (.Input(in_2), .Write(in_9), .M(out_11));
  Memory_bit_v2 memory_bit_v2_3 (.Input(in_3), .Write(in_9), .M(out_12));
  Memory_bit_v2 memory_bit_v2_4 (.Input(in_4), .Write(in_9), .M(out_13));
  Memory_bit_v2 memory_bit_v2_5 (.Input(in_5), .Write(in_9), .M(out_14));
  Memory_bit_v2 memory_bit_v2_6 (.Input(in_6), .Write(in_9), .M(out_15));
  Memory_bit_v2 memory_bit_v2_7 (.Input(in_7), .Write(in_9), .M(out_16));
  Memory_bit_v2 memory_bit_v2_8 (.Input(in_8), .Write(in_9), .M(out_17));
endmodule

// Decoder(4-16)
module _4x16_decoder (
  input  w,
  input  x,
  input  y,
  input  z,
  output out_5,
  output out_6,
  output out_7,
  output out_8,
  output out_9,
  output out_10,
  output out_11,
  output out_12,
  output out_13,
  output out_14,
  output out_15,
  output out_16,
  output out_17,
  output out_18,
  output out_19,
  output out_20
);

  wire not_1_q, not_2_q, not_3_q, not_4_q, not_5_q, not_6_q, not_7_q, not_8_q, not_9_q, not_10_q, not_11_q,
       not_12_q, not_13_q, not_14_q, not_15_q, not_16_q, not_17_q, not_18_q, not_19_q, not_20_q, not_21_q,
       not_22_q, not_23_q, not_24_q, not_25_q, not_26_q, not_27_q, not_28_q, not_29_q, not_30_q, not_31_q,
       not_32_q;

  NOT not_1 (.Q(not_1_q), .X(z));
  NOT not_2 (.Q(not_2_q), .X(y));
  NOT not_3 (.Q(not_3_q), .X(y));
  NOT not_4 (.Q(not_4_q), .X(z));
  NOT not_5 (.Q(not_5_q), .X(z));
  NOT not_6 (.Q(not_6_q), .X(z));
  NOT not_7 (.Q(not_7_q), .X(w));
  NOT not_8 (.Q(not_8_q), .X(x));
  NOT not_9 (.Q(not_9_q), .X(w));
  NOT not_10 (.Q(not_10_q), .X(x));
  NOT not_11 (.Q(not_11_q), .X(w));
  NOT not_12 (.Q(not_12_q), .X(x));
  NOT not_13 (.Q(not_13_q), .X(w));
  NOT not_14 (.Q(not_14_q), .X(x));
  NOT not_15 (.Q(not_15_q), .X(w));
  NOT not_16 (.Q(not_16_q), .X(y));
  NOT not_17 (.Q(not_17_q), .X(w));
  NOT not_18 (.Q(not_18_q), .X(y));
  NOT not_19 (.Q(not_19_q), .X(w));
  NOT not_20 (.Q(not_20_q), .X(z));
  NOT not_21 (.Q(not_21_q), .X(w));
  NOT not_22 (.Q(not_22_q), .X(x));
  NOT not_23 (.Q(not_23_q), .X(y));
  NOT not_24 (.Q(not_24_q), .X(x));
  NOT not_25 (.Q(not_25_q), .X(y));
  NOT not_26 (.Q(not_26_q), .X(x));
  NOT not_27 (.Q(not_27_q), .X(z));
  NOT not_28 (.Q(not_28_q), .X(x));
  NOT not_29 (.Q(not_29_q), .X(y));
  NOT not_30 (.Q(not_30_q), .X(z));
  NOT not_31 (.Q(not_31_q), .X(y));
  NOT not_32 (.Q(not_32_q), .X(z));
  _4_bit_AND u_4_bit_and_1 (.in_1(not_7_q), .in_2(not_8_q), .in_3(not_2_q), .in_4(not_1_q), .out_5(out_5));
  _4_bit_AND u_4_bit_and_2 (.in_1(not_9_q), .in_2(not_10_q), .in_3(not_3_q), .in_4(z), .out_5(out_6));
  _4_bit_AND u_4_bit_and_3 (.in_1(not_11_q), .in_2(not_12_q), .in_3(y), .in_4(not_4_q), .out_5(out_7));
  _4_bit_AND u_4_bit_and_4 (.in_1(not_13_q), .in_2(not_14_q), .in_3(y), .in_4(z), .out_5(out_8));
  _4_bit_AND u_4_bit_and_5 (.in_1(not_15_q), .in_2(x), .in_3(not_16_q), .in_4(not_5_q), .out_5(out_9));
  _4_bit_AND u_4_bit_and_6 (.in_1(not_17_q), .in_2(x), .in_3(not_18_q), .in_4(z), .out_5(out_10));
  _4_bit_AND u_4_bit_and_7 (.in_1(not_19_q), .in_2(x), .in_3(y), .in_4(not_20_q), .out_5(out_11));
  _4_bit_AND u_4_bit_and_8 (.in_1(not_21_q), .in_2(x), .in_3(y), .in_4(z), .out_5(out_12));
  _4_bit_AND u_4_bit_and_9 (.in_1(w), .in_2(not_22_q), .in_3(not_23_q), .in_4(not_6_q), .out_5(out_13));
  _4_bit_AND u_4_bit_and_10 (.in_1(w), .in_2(not_24_q), .in_3(not_25_q), .in_4(z), .out_5(out_14));
  _4_bit_AND u_4_bit_and_11 (.in_1(w), .in_2(not_26_q), .in_3(y), .in_4(not_27_q), .out_5(out_15));
  _4_bit_AND u_4_bit_and_12 (.in_1(w), .in_2(not_28_q), .in_3(y), .in_4(z), .out_5(out_16));
  _4_bit_AND u_4_bit_and_13 (.in_1(w), .in_2(x), .in_3(not_29_q), .in_4(not_30_q), .out_5(out_17));
  _4_bit_AND u_4_bit_and_14 (.in_1(w), .in_2(x), .in_3(not_31_q), .in_4(z), .out_5(out_18));
  _4_bit_AND u_4_bit_and_15 (.in_1(w), .in_2(x), .in_3(y), .in_4(not_32_q), .out_5(out_19));
  _4_bit_AND u_4_bit_and_16 (.in_1(w), .in_2(x), .in_3(y), .in_4(z), .out_5(out_20));
endmodule

module O0 (
  input  in_1,
  input  in_2,
  input  in_3,
  output out_4
);

  wire and_1_out_3, not_1_q, not_2_q, not_3_q;

  NOT not_1 (.Q(not_1_q));  // open: X
  AND and_1 (.in_1(not_1_q), .out_3(and_1_out_3), .in_2(not_2_q));
  NOT not_2 (.Q(not_2_q));  // open: X
  NOT not_3 (.Q(not_3_q));  // open: X
  AND and_2 (.in_1(and_1_out_3), .out_3(out_4), .in_2(not_3_q));
endmodule

module _4_bit_AND (
  input  in_1,
  input  in_2,
  input  in_3,
  input  in_4,
  output out_5
);

  wire transistor_1_out, transistor_2_out, transistor_3_out;

  Pull_Resistor pull_resistor_1 (.node(in_1));
  Pull_Resistor pull_resistor_2 (.node(in_2));
  Pull_Resistor pull_resistor_3 (.node(in_3));
  Pull_Resistor pull_resistor_4 (.node(in_4));
  Transistor #(.\type ("n")) transistor_1 (.in(1'b1), .out(transistor_1_out), .gate(in_1));
  Transistor #(.\type ("n")) transistor_2 (.in(transistor_1_out), .out(transistor_2_out), .gate(in_2));
  Transistor #(.\type ("n")) transistor_3 (.in(transistor_2_out), .out(transistor_3_out), .gate(in_3));
  Transistor #(.\type ("n")) transistor_4 (.in(transistor_3_out), .out(out_5), .gate(in_4));
  Pull_Resistor pull_resistor_5 (.node(out_5));
endmodule

module _4_16_Decoder_V2 (
  input  in_1,
  input  in_2,
  input  in_3,
  input  in_4,
  input  in_5,
  output out_6,
  output out_7,
  output out_8,
  output out_9,
  output out_10,
  output out_11,
  output out_12,
  output out_13,
  output out_14,
  output out_15,
  output out_16,
  output out_17,
  output out_18,
  output out_19,
  output out_20,
  output out_21,
  output out_22,
  output out_23,
  output out_24,
  output out_25,
  output out_26,
  output out_27,
  output out_28,
  output out_29,
  output out_30,
  output out_31,
  output out_32,
  output out_33,
  output out_34,
  output out_35,
  output out_36,
  output out_37
);

  wire n3_8_decoder_v2_1__0, n3_8_decoder_v2_1__1, n3_8_decoder_v2_1__2, n3_8_decoder_v2_1__4,
       n3_8_decoder_v2_1__5, n3_8_decoder_v2_1__6, n3_8_decoder_v2_1__7, n3_8_decoder_v2_2__0,
       n3_8_decoder_v2_2__1, n3_8_decoder_v2_2__2, n3_8_decoder_v2_2__4, n3_8_decoder_v2_2__5,
       n3_8_decoder_v2_2__6, n3_8_decoder_v2_2__7, not_1_q;

  NOT not_1 (.Q(not_1_q));  // open: X
  _3_8_Decoder_v2 u_3_8_decoder_v2_1 (
    .A(in_1), .B(in_2), .C(in_3), .X(in_5), ._7(n3_8_decoder_v2_1__7), ._7_2(out_7),
    ._6(n3_8_decoder_v2_1__6), ._6_2(out_9), ._5(n3_8_decoder_v2_1__5), ._5_2(out_11),
    ._4(n3_8_decoder_v2_1__4), ._4_2(out_13), ._3(out_15), ._3_2(out_15), ._2(n3_8_decoder_v2_1__2),
    ._2_2(out_17), ._1(n3_8_decoder_v2_1__1), ._1_2(out_19), ._0(n3_8_decoder_v2_1__0), ._0_2(out_21));
  _3_8_Decoder_v2 u_3_8_decoder_v2_2 (
    .A(in_1), .B(in_2), .C(in_3), .X(in_5), ._7(n3_8_decoder_v2_2__7), ._7_2(out_23),
    ._6(n3_8_decoder_v2_2__6), ._6_2(out_25), ._5(n3_8_decoder_v2_2__5), ._5_2(out_27),
    ._4(n3_8_decoder_v2_2__4), ._4_2(out_29), ._3(out_31), ._3_2(out_31), ._2(n3_8_decoder_v2_2__2),
    ._2_2(out_33), ._1(n3_8_decoder_v2_2__1), ._1_2(out_35), ._0(n3_8_decoder_v2_2__0), ._0_2(out_37));
  AND and_1 (.in_1(n3_8_decoder_v2_1__7), .out_3(out_6), .in_2(not_1_q));
  AND and_2 (.in_1(n3_8_decoder_v2_1__6), .out_3(out_8), .in_2(not_1_q));
  AND and_3 (.in_1(n3_8_decoder_v2_1__5), .out_3(out_10), .in_2(not_1_q));
  AND and_4 (.in_1(n3_8_decoder_v2_1__4), .out_3(out_12), .in_2(not_1_q));
  AND and_5 (.in_1(out_15), .out_3(out_14), .in_2(not_1_q));
  AND and_6 (.in_1(n3_8_decoder_v2_1__2), .out_3(out_16), .in_2(not_1_q));
  AND and_7 (.in_1(n3_8_decoder_v2_1__1), .out_3(out_18), .in_2(not_1_q));
  AND and_8 (.in_1(n3_8_decoder_v2_1__0), .out_3(out_20), .in_2(not_1_q));
  AND and_9 (.in_1(n3_8_decoder_v2_2__7), .out_3(out_22), .in_2(in_4));
  AND and_10 (.in_1(n3_8_decoder_v2_2__6), .out_3(out_24), .in_2(in_4));
  AND and_11 (.in_1(n3_8_decoder_v2_2__5), .out_3(out_26), .in_2(in_4));
  AND and_12 (.in_1(n3_8_decoder_v2_2__4), .out_3(out_28), .in_2(in_4));
  AND and_13 (.in_1(out_31), .out_3(out_30), .in_2(in_4));
  AND and_14 (.in_1(n3_8_decoder_v2_2__2), .out_3(out_32), .in_2(in_4));
  AND and_15 (.in_1(n3_8_decoder_v2_2__1), .out_3(out_34), .in_2(in_4));
  AND and_16 (.in_1(n3_8_decoder_v2_2__0), .out_3(out_36), .in_2(in_4));
  _3_8_Decoder_v2 u_3_8_decoder_v2_3 ();  // open: A, B, C, X, _7, _7_2, _6, _6_2, _5, _5_2, _4, _4_2, _3, _3_2, _2, _2_2, _1, _1_2, _0, _0_2
  _3_8_Decoder_v2 u_3_8_decoder_v2_4 ();  // open: A, B, C, X, _7, _7_2, _6, _6_2, _5, _5_2, _4, _4_2, _3, _3_2, _2, _2_2, _1, _1_2, _0, _0_2
endmodule

module _3_8_Decoder_v2 (
  input  A,
  input  B,
  input  C,
  input  X,
  output _7,
  output _7_2,
  output _6,
  output _6_2,
  output _5,
  output _5_2,
  output _4,
  output _4_2,
  output _3,
  output _3_2,
  output _2,
  output _2_2,
  output _1,
  output _1_2,
  output _0,
  output _0_2
);

  Decoder decoder_1 (
    .in_1(A), .in_2(B), .in_3(C), .out_4(_7), .out_5(_6), .out_6(_5), .out_7(_4), .out_8(_3), .out_9(_2),
    .out_10(_1), .out_11(_0));
  Demux_1_Bit demux_1_bit_1 (
    .in_1(X), .in_2(A), .in_3(B), .in_4(C), .out_5(_7_2), .out_6(_6_2), .out_7(_5_2), .out_8(_4_2),
    .out_9(_3_2), .out_10(_2_2), .out_11(_1_2), .out_12(_0_2));
endmodule

// Clock
module Clock_V2 (
  input  Clock,
  input  run,
  input  halt,
  output Running,
  output fetch,
  output write,
  output Execute,
  output Exec_Write
);

  wire and_2_out_3, and_3_out_3, and_5_out_3, not_1_q, or_1_out_3;

  NOT not_1 (.Q(not_1_q), .X(fetch));
  AND and_1 (.in_1(and_5_out_3), .out_3(Exec_Write), .in_2(Execute));
  AND and_2 (.in_1(not_1_q), .out_3(and_2_out_3), .in_2(and_5_out_3));
  AND and_3 (.in_1(fetch), .out_3(and_3_out_3), .in_2(and_5_out_3));
  AND and_4 (.in_1(and_5_out_3), .out_3(write), .in_2(fetch));
  S_R_Flip_Flop #(.trigger("falling")) s_r_ff_1 (
    .S(and_3_out_3), .clk(and_5_out_3), .R(and_2_out_3), .Q(Execute));  // open: Qn, preset, reset, en
  NOT not_2 (.Q(fetch), .X(Execute));
  AND and_5 (.in_1(Running), .out_3(and_5_out_3), .in_2(Clock));
  S_R_Flip_Flop s_r_ff_2 (.S(run), .clk(or_1_out_3), .R(halt), .Q(Running));  // open: Qn, preset, reset, en
  OR or_1 (.in_1(halt), .in_2(run), .out_3(or_1_out_3));
endmodule

module Decoder (
  input  in_1,
  input  in_2,
  input  in_3,
  output out_4,
  output out_5,
  output out_6,
  output out_7,
  output out_8,
  output out_9,
  output out_10,
  output out_11
);

  O7 o7_1 (.in_1(in_1), .in_2(in_2), .in_3(in_3), .out_4(out_4));
  O6 o6_1 (.in_1(in_1), .in_2(in_2), .in_3(in_3), .out_4(out_5));
  O5 o5_1 (.in_1(in_1), .in_2(in_2), .in_3(in_3), .out_4(out_6));
  O4 o4_1 (.in_1(in_1), .in_2(in_2), .in_3(in_3), .out_4(out_7));
  O3 o3_1 (.in_1(in_1), .in_2(in_2), .in_3(in_3), .out_4(out_8));
  O2 o2_1 (.in_1(in_1), .in_2(in_2), .in_3(in_3), .out_4(out_9));
  O1 o1_1 (.in_1(in_1), .in_2(in_2), .in_3(in_3), .out_4(out_10));
  O0 o0_1 (.in_1(in_3), .in_2(in_2), .in_3(in_1), .out_4(out_11));
endmodule

module O1 (
  input  in_1,
  input  in_2,
  input  in_3,
  output out_4
);

  wire and_1_out_3, not_1_q, not_2_q;

  NOT not_1 (.Q(not_1_q), .X(in_1));
  NOT not_2 (.Q(not_2_q), .X(in_2));
  AND and_1 (.in_1(not_1_q), .out_3(and_1_out_3), .in_2(not_2_q));
  AND and_2 (.in_1(and_1_out_3), .out_3(out_4), .in_2(in_3));
endmodule

module O2 (
  input  in_1,
  input  in_2,
  input  in_3,
  output out_4
);

  wire and_1_out_3, not_1_q, not_2_q;

  NOT not_1 (.Q(not_1_q), .X(in_1));
  NOT not_2 (.Q(not_2_q), .X(in_3));
  AND and_1 (.in_1(not_1_q), .out_3(and_1_out_3), .in_2(not_2_q));
  AND and_2 (.in_1(and_1_out_3), .out_3(out_4), .in_2(in_2));
endmodule

module O3 (
  input  in_1,
  input  in_2,
  input  in_3,
  output out_4
);

  wire and_1_out_3, not_1_q;

  NOT not_1 (.Q(not_1_q), .X(in_1));
  AND and_1 (.in_1(in_2), .out_3(and_1_out_3), .in_2(in_3));
  AND and_2 (.in_1(not_1_q), .out_3(out_4), .in_2(and_1_out_3));
endmodule

module O4 (
  input  in_1,
  input  in_2,
  input  in_3,
  output out_4
);

  wire and_1_out_3, not_1_q, not_2_q;

  AND and_1 (.in_1(not_1_q), .out_3(and_1_out_3), .in_2(not_2_q));
  NOT not_1 (.Q(not_1_q), .X(in_2));
  NOT not_2 (.Q(not_2_q), .X(in_3));
  AND and_2 (.in_1(in_1), .out_3(out_4), .in_2(and_1_out_3));
endmodule

module O5 (
  input  in_1,
  input  in_2,
  input  in_3,
  output out_4
);

  wire and_1_out_3, not_1_q;

  AND and_1 (.in_1(in_1), .out_3(and_1_out_3), .in_2(in_3));
  NOT not_1 (.Q(not_1_q), .X(in_2));
  AND and_2 (.in_1(and_1_out_3), .out_3(out_4), .in_2(not_1_q));
endmodule

module O6 (
  input  in_1,
  input  in_2,
  input  in_3,
  output out_4
);

  wire and_1_out_3, not_1_q;

  AND and_1 (.in_1(in_1), .out_3(and_1_out_3), .in_2(in_2));
  NOT not_1 (.Q(not_1_q), .X(in_3));
  AND and_2 (.in_1(and_1_out_3), .out_3(out_4), .in_2(not_1_q));
endmodule

module O7 (
  input  in_1,
  input  in_2,
  input  in_3,
  output out_4
);

  wire and_1_out_3;

  AND and_1 (.in_1(in_1), .out_3(and_1_out_3), .in_2(in_2));
  AND and_2 (.in_1(and_1_out_3), .out_3(out_4), .in_2(in_3));
endmodule

module Demux_1_Bit (
  input  in_1,
  input  in_2,
  input  in_3,
  input  in_4,
  output out_5,
  output out_6,
  output out_7,
  output out_8,
  output out_9,
  output out_10,
  output out_11,
  output out_12
);

  wire decoder_1_out_4, decoder_1_out_5, decoder_1_out_6, decoder_1_out_7, decoder_1_out_8, decoder_1_out_9,
       decoder_1_out_10, decoder_1_out_11;

  Decoder decoder_1 (
    .in_1(in_2), .in_2(in_3), .in_3(in_4), .out_4(decoder_1_out_4), .out_5(decoder_1_out_5),
    .out_6(decoder_1_out_6), .out_7(decoder_1_out_7), .out_8(decoder_1_out_8), .out_9(decoder_1_out_9),
    .out_10(decoder_1_out_10), .out_11(decoder_1_out_11));
  AND and_1 (.in_1(in_1), .out_3(out_5), .in_2(decoder_1_out_4));
  AND and_2 (.in_1(in_1), .out_3(out_6), .in_2(decoder_1_out_5));
  AND and_3 (.in_1(in_1), .out_3(out_7), .in_2(decoder_1_out_6));
  AND and_4 (.in_1(in_1), .out_3(out_8), .in_2(decoder_1_out_7));
  AND and_5 (.in_1(in_1), .out_3(out_9), .in_2(decoder_1_out_8));
  AND and_6 (.in_1(in_1), .out_3(out_10), .in_2(decoder_1_out_9));
  AND and_7 (.in_1(in_1), .out_3(out_11), .in_2(decoder_1_out_10));
  AND and_8 (.in_1(in_1), .out_3(out_12), .in_2(decoder_1_out_11));
endmodule

module _16_bit_OR (
  input  in_1,
  input  in_2,
  input  in_3,
  input  in_4,
  input  in_5,
  input  in_6,
  input  in_7,
  input  in_8,
  input  in_9,
  input  in_10,
  input  in_11,
  input  in_12,
  input  in_13,
  input  in_14,
  input  in_15,
  input  in_16,
  output Out
);

  wire or_1_out_3, or_3_out_3, or_4_out_3, or_5_out_3, or_6_out_3, or_7_out_3, or_8_out_3, or_9_out_3,
       or_10_out_3, or_11_out_3, or_12_out_3, or_13_out_3, or_14_out_3, or_15_out_3;

  OR or_1 (.in_1(or_5_out_3), .in_2(in_2), .out_3(or_1_out_3));
  OR or_2 (.in_1(or_1_out_3), .in_2(in_1), .out_3(Out));
  OR or_3 (.in_1(or_8_out_3), .in_2(in_5), .out_3(or_3_out_3));
  OR or_4 (.in_1(or_3_out_3), .in_2(in_4), .out_3(or_4_out_3));
  OR or_5 (.in_1(or_4_out_3), .in_2(in_3), .out_3(or_5_out_3));
  OR or_6 (.in_1(or_11_out_3), .in_2(in_8), .out_3(or_6_out_3));
  OR or_7 (.in_1(or_6_out_3), .in_2(in_7), .out_3(or_7_out_3));
  OR or_8 (.in_1(or_7_out_3), .in_2(in_6), .out_3(or_8_out_3));
  OR or_9 (.in_1(or_14_out_3), .in_2(in_11), .out_3(or_9_out_3));
  OR or_10 (.in_1(or_9_out_3), .in_2(in_10), .out_3(or_10_out_3));
  OR or_11 (.in_1(or_10_out_3), .in_2(in_9), .out_3(or_11_out_3));
  OR or_12 (.in_1(or_15_out_3), .in_2(in_14), .out_3(or_12_out_3));
  OR or_13 (.in_1(or_12_out_3), .in_2(in_13), .out_3(or_13_out_3));
  OR or_14 (.in_1(or_13_out_3), .in_2(in_12), .out_3(or_14_out_3));
  OR or_15 (.in_1(in_16), .in_2(in_15), .out_3(or_15_out_3));
endmodule

// Memory Bank
module Mem_Bank (
  input  [7:0] in_1,
  input  Memory_Write,
  input  in_3,
  input  in_4,
  input  in_5,
  input  in_6,
  input  in_7,
  output [7:0] out_8
);

  wire and_1_out_3, and_2_out_3, and_3_out_3, and_4_out_3, and_5_out_3, and_6_out_3, and_7_out_3,
       and_8_out_3, and_9_out_3, and_10_out_3, and_11_out_3, and_12_out_3, and_13_out_3, and_14_out_3,
       and_15_out_3, and_16_out_3, and_17_out_3, and_18_out_3, and_19_out_3, and_20_out_3, and_21_out_3,
       and_22_out_3, and_23_out_3, and_24_out_3, and_25_out_3, and_26_out_3, and_27_out_3, and_28_out_3,
       and_29_out_3, and_30_out_3, and_31_out_3, and_32_out_3, and_33_out_3, and_34_out_3, and_35_out_3,
       and_36_out_3, and_37_out_3, and_38_out_3, and_39_out_3, and_40_out_3, and_41_out_3, and_42_out_3,
       and_43_out_3, and_44_out_3, and_45_out_3, and_46_out_3, and_47_out_3, and_48_out_3, and_49_out_3,
       and_50_out_3, and_51_out_3, and_52_out_3, and_53_out_3, and_54_out_3, and_55_out_3, and_56_out_3,
       and_57_out_3, and_59_out_3, and_60_out_3, and_61_out_3, and_62_out_3, and_63_out_3, and_64_out_3,
       and_65_out_3, and_66_out_3, and_67_out_3, and_68_out_3, and_69_out_3, and_70_out_3, and_71_out_3,
       and_72_out_3, and_73_out_3, and_75_out_3, and_76_out_3, and_77_out_3, and_78_out_3, and_79_out_3,
       and_80_out_3, and_81_out_3, and_82_out_3, and_83_out_3, and_84_out_3, and_85_out_3, and_86_out_3,
       and_87_out_3, and_88_out_3, and_89_out_3, and_90_out_3, and_91_out_3, and_92_out_3, and_93_out_3,
       and_94_out_3, and_95_out_3, and_96_out_3, and_97_out_3, and_98_out_3, and_99_out_3, and_100_out_3,
       and_101_out_3, and_102_out_3, and_103_out_3, and_104_out_3, and_105_out_3, and_106_out_3,
       and_107_out_3, and_108_out_3, and_109_out_3, and_110_out_3, and_111_out_3, and_112_out_3,
       and_113_out_3, and_114_out_3, and_115_out_3, and_116_out_3, and_117_out_3, and_118_out_3,
       and_119_out_3, and_120_out_3, and_121_out_3, and_122_out_3, and_123_out_3, and_124_out_3,
       and_125_out_3, and_126_out_3, and_127_out_3, and_128_out_3, and_129_out_3, and_130_out_3,
       and_131_out_3, and_132_out_3, and_133_out_3, and_134_out_3, and_135_out_3, and_136_out_3,
       and_137_out_3, and_138_out_3, and_139_out_3, and_140_out_3, and_141_out_3, and_142_out_3,
       and_143_out_3, and_144_out_3, and_145_out_3, memory_bit_1_memory, memory_bit_2_memory,
       memory_bit_3_memory, memory_bit_4_memory, memory_bit_5_memory, memory_bit_6_memory,
       memory_bit_7_memory, memory_bit_8_memory, memory_bit_9_memory, memory_bit_10_memory,
       memory_bit_11_memory, memory_bit_12_memory, memory_bit_13_memory, memory_bit_14_memory,
       memory_bit_15_memory, memory_bit_16_memory, memory_bit_17_memory, memory_bit_18_memory,
       memory_bit_19_memory, memory_bit_20_memory, memory_bit_21_memory, memory_bit_22_memory,
       memory_bit_23_memory, memory_bit_24_memory, memory_bit_25_memory, memory_bit_26_memory,
       memory_bit_27_memory, memory_bit_28_memory, memory_bit_29_memory, memory_bit_30_memory,
       memory_bit_31_memory, memory_bit_32_memory, memory_bit_33_memory, memory_bit_35_memory,
       memory_bit_36_memory, memory_bit_37_memory, memory_bit_38_memory, memory_bit_39_memory,
       memory_bit_40_memory, memory_bit_41_memory, memory_bit_42_memory, memory_bit_43_memory,
       memory_bit_44_memory, memory_bit_45_memory, memory_bit_46_memory, memory_bit_47_memory,
       memory_bit_48_memory, memory_bit_49_memory, memory_bit_50_memory, memory_bit_51_memory,
       memory_bit_52_memory, memory_bit_53_memory, memory_bit_54_memory, memory_bit_55_memory,
       memory_bit_56_memory, memory_bit_57_memory, memory_bit_58_memory, memory_bit_59_memory,
       memory_bit_60_memory, memory_bit_61_memory, memory_bit_62_memory, memory_bit_63_memory,
       memory_bit_64_memory, memory_bit_65_memory, memory_bit_66_memory, memory_bit_67_memory,
       memory_bit_68_memory, memory_bit_69_memory, memory_bit_70_memory, memory_bit_71_memory,
       memory_bit_72_memory, memory_bit_73_memory, memory_bit_74_memory, memory_bit_75_memory,
       memory_bit_76_memory, memory_bit_77_memory, memory_bit_78_memory, memory_bit_79_memory,
       memory_bit_80_memory, memory_bit_81_memory, memory_bit_82_memory, memory_bit_83_memory,
       memory_bit_84_memory, memory_bit_85_memory, memory_bit_86_memory, memory_bit_87_memory,
       memory_bit_88_memory, memory_bit_89_memory, memory_bit_90_memory, memory_bit_91_memory,
       memory_bit_92_memory, memory_bit_93_memory, memory_bit_94_memory, memory_bit_95_memory,
       memory_bit_96_memory, memory_bit_97_memory, memory_bit_98_memory, memory_bit_99_memory,
       memory_bit_100_memory, memory_bit_101_memory, memory_bit_102_memory, memory_bit_103_memory,
       memory_bit_104_memory, memory_bit_105_memory, memory_bit_106_memory, memory_bit_107_memory,
       memory_bit_108_memory, memory_bit_109_memory, memory_bit_110_memory, memory_bit_111_memory,
       memory_bit_112_memory, memory_bit_113_memory, memory_bit_114_memory, memory_bit_115_memory,
       memory_bit_116_memory, memory_bit_117_memory, memory_bit_118_memory, memory_bit_119_memory,
       memory_bit_120_memory, memory_bit_121_memory, memory_bit_122_memory, memory_bit_123_memory,
       memory_bit_124_memory, memory_bit_125_memory, memory_bit_126_memory, memory_bit_127_memory,
       memory_bit_128_memory, n4_16_decoder_v2_1_out_6, n4_16_decoder_v2_1_out_7, n4_16_decoder_v2_1_out_8,
       n4_16_decoder_v2_1_out_9, n4_16_decoder_v2_1_out_10, n4_16_decoder_v2_1_out_11,
       n4_16_decoder_v2_1_out_12, n4_16_decoder_v2_1_out_13, n4_16_decoder_v2_1_out_14,
       n4_16_decoder_v2_1_out_15, n4_16_decoder_v2_1_out_16, n4_16_decoder_v2_1_out_17,
       n4_16_decoder_v2_1_out_18, n4_16_decoder_v2_1_out_19, n4_16_decoder_v2_1_out_20,
       n4_16_decoder_v2_1_out_21, n4_16_decoder_v2_1_out_22, n4_16_decoder_v2_1_out_23,
       n4_16_decoder_v2_1_out_24, n4_16_decoder_v2_1_out_25, n4_16_decoder_v2_1_out_26,
       n4_16_decoder_v2_1_out_27, n4_16_decoder_v2_1_out_28, n4_16_decoder_v2_1_out_29,
       n4_16_decoder_v2_1_out_30, n4_16_decoder_v2_1_out_31, n4_16_decoder_v2_1_out_32,
       n4_16_decoder_v2_1_out_33, n4_16_decoder_v2_1_out_34, n4_16_decoder_v2_1_out_35,
       n4_16_decoder_v2_1_out_36, n4_16_decoder_v2_1_out_37;

  _4_16_Decoder_V2 u_4_16_decoder_v2_1 (
    .in_1(in_3), .in_2(in_4), .in_3(in_5), .in_4(in_6), .in_5(in_7), .out_6(n4_16_decoder_v2_1_out_6),
    .out_7(n4_16_decoder_v2_1_out_7), .out_8(n4_16_decoder_v2_1_out_8), .out_9(n4_16_decoder_v2_1_out_9),
    .out_10(n4_16_decoder_v2_1_out_10), .out_11(n4_16_decoder_v2_1_out_11),
    .out_12(n4_16_decoder_v2_1_out_12), .out_13(n4_16_decoder_v2_1_out_13),
    .out_14(n4_16_decoder_v2_1_out_14), .out_15(n4_16_decoder_v2_1_out_15),
    .out_16(n4_16_decoder_v2_1_out_16), .out_17(n4_16_decoder_v2_1_out_17),
    .out_18(n4_16_decoder_v2_1_out_18), .out_19(n4_16_decoder_v2_1_out_19),
    .out_20(n4_16_decoder_v2_1_out_20), .out_21(n4_16_decoder_v2_1_out_21),
    .out_22(n4_16_decoder_v2_1_out_22), .out_23(n4_16_decoder_v2_1_out_23),
    .out_24(n4_16_decoder_v2_1_out_24), .out_25(n4_16_decoder_v2_1_out_25),
    .out_26(n4_16_decoder_v2_1_out_26), .out_27(n4_16_decoder_v2_1_out_27),
    .out_28(n4_16_decoder_v2_1_out_28), .out_29(n4_16_decoder_v2_1_out_29),
    .out_30(n4_16_decoder_v2_1_out_30), .out_31(n4_16_decoder_v2_1_out_31),
    .out_32(n4_16_decoder_v2_1_out_32), .out_33(n4_16_decoder_v2_1_out_33),
    .out_34(n4_16_decoder_v2_1_out_34), .out_35(n4_16_decoder_v2_1_out_35),
    .out_36(n4_16_decoder_v2_1_out_36), .out_37(n4_16_decoder_v2_1_out_37));
  AND and_1 (.in_1(Memory_Write), .out_3(and_1_out_3), .in_2(n4_16_decoder_v2_1_out_6));
  AND and_2 (.in_1(Memory_Write), .out_3(and_2_out_3), .in_2(n4_16_decoder_v2_1_out_8));
  AND and_3 (.in_1(Memory_Write), .out_3(and_3_out_3), .in_2(n4_16_decoder_v2_1_out_22));
  AND and_4 (.in_1(Memory_Write), .out_3(and_4_out_3), .in_2(n4_16_decoder_v2_1_out_26));
  AND and_5 (.in_1(Memory_Write), .out_3(and_5_out_3), .in_2(n4_16_decoder_v2_1_out_28));
  AND and_6 (.in_1(Memory_Write), .out_3(and_6_out_3), .in_2(n4_16_decoder_v2_1_out_10));
  AND and_7 (.in_1(Memory_Write), .out_3(and_7_out_3), .in_2(n4_16_decoder_v2_1_out_12));
  AND and_8 (.in_1(Memory_Write), .out_3(and_8_out_3), .in_2(n4_16_decoder_v2_1_out_14));
  AND and_9 (.in_1(Memory_Write), .out_3(and_9_out_3), .in_2(n4_16_decoder_v2_1_out_16));
  AND and_10 (.in_1(Memory_Write), .out_3(and_10_out_3), .in_2(n4_16_decoder_v2_1_out_20));
  AND and_11 (.in_1(Memory_Write), .out_3(and_11_out_3), .in_2(n4_16_decoder_v2_1_out_24));
  AND and_12 (.in_1(Memory_Write), .out_3(and_12_out_3), .in_2(n4_16_decoder_v2_1_out_25));
  AND and_13 (.in_1(Memory_Write), .out_3(and_13_out_3), .in_2(n4_16_decoder_v2_1_out_36));
  AND and_14 (.in_1(Memory_Write), .out_3(and_14_out_3), .in_2(n4_16_decoder_v2_1_out_18));
  AND and_15 (.in_1(Memory_Write), .out_3(and_15_out_3), .in_2(n4_16_decoder_v2_1_out_30));
  AND and_16 (.in_1(Memory_Write), .out_3(and_16_out_3), .in_2(n4_16_decoder_v2_1_out_32));
  AND and_17 (.in_1(Memory_Write), .out_3(and_17_out_3), .in_2(n4_16_decoder_v2_1_out_34));
  Memory_Bit memory_bit_1 (.Write(and_1_out_3), .Input(in_1[0]), .Memory(memory_bit_1_memory));
  AND and_18 (.in_1(memory_bit_1_memory), .out_3(and_18_out_3), .in_2(n4_16_decoder_v2_1_out_7));
  Memory_Bit memory_bit_2 (.Write(and_2_out_3), .Input(in_1[0]), .Memory(memory_bit_2_memory));
  AND and_19 (.in_1(memory_bit_2_memory), .out_3(and_19_out_3), .in_2(n4_16_decoder_v2_1_out_9));
  Memory_Bit memory_bit_3 (.Write(and_6_out_3), .Input(in_1[0]), .Memory(memory_bit_3_memory));
  AND and_20 (.in_1(memory_bit_3_memory), .out_3(and_20_out_3), .in_2(n4_16_decoder_v2_1_out_11));
  Memory_Bit memory_bit_4 (.Write(and_7_out_3), .Input(in_1[0]), .Memory(memory_bit_4_memory));
  AND and_21 (.in_1(memory_bit_4_memory), .out_3(and_21_out_3), .in_2(n4_16_decoder_v2_1_out_13));
  Memory_Bit memory_bit_5 (.Write(and_8_out_3), .Input(in_1[0]), .Memory(memory_bit_5_memory));
  AND and_22 (.in_1(memory_bit_5_memory), .out_3(and_22_out_3), .in_2(n4_16_decoder_v2_1_out_15));
  Memory_Bit memory_bit_6 (.Write(and_9_out_3), .Input(in_1[0]), .Memory(memory_bit_6_memory));
  AND and_23 (.in_1(memory_bit_6_memory), .out_3(and_23_out_3), .in_2(n4_16_decoder_v2_1_out_17));
  Memory_Bit memory_bit_7 (.Write(and_14_out_3), .Input(in_1[0]), .Memory(memory_bit_7_memory));
  AND and_24 (.in_1(memory_bit_7_memory), .out_3(and_24_out_3), .in_2(n4_16_decoder_v2_1_out_19));
  Memory_Bit memory_bit_8 (.Write(and_10_out_3), .Input(in_1[0]), .Memory(memory_bit_8_memory));
  AND and_25 (.in_1(memory_bit_8_memory), .out_3(and_25_out_3), .in_2(n4_16_decoder_v2_1_out_21));
  Memory_Bit memory_bit_9 (.Write(and_3_out_3), .Input(in_1[0]), .Memory(memory_bit_9_memory));
  AND and_26 (.in_1(memory_bit_9_memory), .out_3(and_26_out_3), .in_2(n4_16_decoder_v2_1_out_23));
  Memory_Bit memory_bit_10 (.Write(and_11_out_3), .Input(in_1[0]), .Memory(memory_bit_10_memory));
  AND and_27 (.in_1(memory_bit_10_memory), .out_3(and_27_out_3), .in_2(and_12_out_3));
  Memory_Bit memory_bit_11 (.Write(and_4_out_3), .Input(in_1[0]), .Memory(memory_bit_11_memory));
  AND and_28 (.in_1(memory_bit_11_memory), .out_3(and_28_out_3), .in_2(n4_16_decoder_v2_1_out_27));
  Memory_Bit memory_bit_12 (.Write(and_5_out_3), .Input(in_1[0]), .Memory(memory_bit_12_memory));
  AND and_29 (.in_1(memory_bit_12_memory), .out_3(and_29_out_3), .in_2(n4_16_decoder_v2_1_out_29));
  Memory_Bit memory_bit_13 (.Write(and_15_out_3), .Input(in_1[0]), .Memory(memory_bit_13_memory));
  AND and_30 (.in_1(memory_bit_13_memory), .out_3(and_30_out_3), .in_2(n4_16_decoder_v2_1_out_31));
  Memory_Bit memory_bit_14 (.Write(and_16_out_3), .Input(in_1[0]), .Memory(memory_bit_14_memory));
  AND and_31 (.in_1(memory_bit_14_memory), .out_3(and_31_out_3), .in_2(n4_16_decoder_v2_1_out_33));
  Memory_Bit memory_bit_15 (.Write(and_17_out_3), .Input(in_1[0]), .Memory(memory_bit_15_memory));
  AND and_32 (.in_1(memory_bit_15_memory), .out_3(and_32_out_3), .in_2(n4_16_decoder_v2_1_out_35));
  Memory_Bit memory_bit_16 (.Write(and_13_out_3), .Input(in_1[0]), .Memory(memory_bit_16_memory));
  AND and_33 (.in_1(memory_bit_16_memory), .out_3(and_33_out_3), .in_2(n4_16_decoder_v2_1_out_37));
  _16_bit_OR u_16_bit_or_1 (
    .Out(out_8[0]), .in_1(and_33_out_3), .in_2(and_32_out_3), .in_3(and_31_out_3), .in_4(and_30_out_3),
    .in_5(and_29_out_3), .in_6(and_28_out_3), .in_7(and_27_out_3), .in_8(and_26_out_3), .in_9(and_25_out_3),
    .in_10(and_24_out_3), .in_11(and_23_out_3), .in_12(and_22_out_3), .in_13(and_21_out_3),
    .in_14(and_20_out_3), .in_15(and_19_out_3), .in_16(and_18_out_3));
  Memory_Bit memory_bit_17 (.Write(and_1_out_3), .Input(in_1[1]), .Memory(memory_bit_17_memory));
  AND and_34 (.in_1(memory_bit_17_memory), .out_3(and_34_out_3), .in_2(n4_16_decoder_v2_1_out_7));
  Memory_Bit memory_bit_18 (.Write(and_2_out_3), .Input(in_1[1]), .Memory(memory_bit_18_memory));
  AND and_35 (.in_1(memory_bit_18_memory), .out_3(and_35_out_3), .in_2(n4_16_decoder_v2_1_out_9));
  Memory_Bit memory_bit_19 (.Write(and_6_out_3), .Input(in_1[1]), .Memory(memory_bit_19_memory));
  AND and_36 (.in_1(memory_bit_19_memory), .out_3(and_36_out_3), .in_2(n4_16_decoder_v2_1_out_11));
  Memory_Bit memory_bit_20 (.Write(and_7_out_3), .Input(in_1[1]), .Memory(memory_bit_20_memory));
  AND and_37 (.in_1(memory_bit_20_memory), .out_3(and_37_out_3), .in_2(n4_16_decoder_v2_1_out_13));
  Memory_Bit memory_bit_21 (.Write(and_8_out_3), .Input(in_1[1]), .Memory(memory_bit_21_memory));
  AND and_38 (.in_1(memory_bit_21_memory), .out_3(and_38_out_3), .in_2(n4_16_decoder_v2_1_out_15));
  Memory_Bit memory_bit_22 (.Write(and_9_out_3), .Input(in_1[1]), .Memory(memory_bit_22_memory));
  AND and_39 (.in_1(memory_bit_22_memory), .out_3(and_39_out_3), .in_2(n4_16_decoder_v2_1_out_17));
  Memory_Bit memory_bit_23 (.Write(and_14_out_3), .Input(in_1[1]), .Memory(memory_bit_23_memory));
  AND and_40 (.in_1(memory_bit_23_memory), .out_3(and_40_out_3), .in_2(n4_16_decoder_v2_1_out_19));
  Memory_Bit memory_bit_24 (.Write(and_10_out_3), .Input(in_1[1]), .Memory(memory_bit_24_memory));
  AND and_41 (.in_1(memory_bit_24_memory), .out_3(and_41_out_3), .in_2(n4_16_decoder_v2_1_out_21));
  Memory_Bit memory_bit_25 (.Write(and_3_out_3), .Input(in_1[1]), .Memory(memory_bit_25_memory));
  AND and_42 (.in_1(memory_bit_25_memory), .out_3(and_42_out_3), .in_2(n4_16_decoder_v2_1_out_23));
  Memory_Bit memory_bit_26 (.Write(and_11_out_3), .Input(in_1[1]), .Memory(memory_bit_26_memory));
  AND and_43 (.in_1(memory_bit_26_memory), .out_3(and_43_out_3), .in_2(and_12_out_3));
  Memory_Bit memory_bit_27 (.Write(and_4_out_3), .Input(in_1[1]), .Memory(memory_bit_27_memory));
  AND and_44 (.in_1(memory_bit_27_memory), .out_3(and_44_out_3), .in_2(n4_16_decoder_v2_1_out_27));
  Memory_Bit memory_bit_28 (.Write(and_5_out_3), .Input(in_1[1]), .Memory(memory_bit_28_memory));
  AND and_45 (.in_1(memory_bit_28_memory), .out_3(and_45_out_3), .in_2(n4_16_decoder_v2_1_out_29));
  Memory_Bit memory_bit_29 (.Write(and_15_out_3), .Input(in_1[1]), .Memory(memory_bit_29_memory));
  AND and_46 (.in_1(memory_bit_29_memory), .out_3(and_46_out_3), .in_2(n4_16_decoder_v2_1_out_31));
  Memory_Bit memory_bit_30 (.Write(and_16_out_3), .Input(in_1[1]), .Memory(memory_bit_30_memory));
  AND and_47 (.in_1(memory_bit_30_memory), .out_3(and_47_out_3), .in_2(n4_16_decoder_v2_1_out_33));
  Memory_Bit memory_bit_31 (.Write(and_17_out_3), .Input(in_1[1]), .Memory(memory_bit_31_memory));
  AND and_48 (.in_1(memory_bit_31_memory), .out_3(and_48_out_3), .in_2(n4_16_decoder_v2_1_out_35));
  Memory_Bit memory_bit_32 (.Write(and_13_out_3), .Input(in_1[1]), .Memory(memory_bit_32_memory));
  AND and_49 (.in_1(memory_bit_32_memory), .out_3(and_49_out_3), .in_2(n4_16_decoder_v2_1_out_37));
  _16_bit_OR u_16_bit_or_2 (
    .Out(out_8[1]), .in_1(and_49_out_3), .in_2(and_48_out_3), .in_3(and_47_out_3), .in_4(and_46_out_3),
    .in_5(and_45_out_3), .in_6(and_44_out_3), .in_7(and_43_out_3), .in_8(and_42_out_3), .in_9(and_41_out_3),
    .in_10(and_40_out_3), .in_11(and_39_out_3), .in_12(and_38_out_3), .in_13(and_37_out_3),
    .in_14(and_36_out_3), .in_15(and_35_out_3), .in_16(and_34_out_3));
  Memory_Bit memory_bit_33 (.Write(and_1_out_3), .Input(in_1[2]), .Memory(memory_bit_33_memory));
  AND and_50 (.in_1(memory_bit_33_memory), .out_3(and_50_out_3), .in_2(n4_16_decoder_v2_1_out_7));
  Memory_Bit memory_bit_34 (.Write(and_2_out_3), .Input(in_1[2]), .Memory(n4_16_decoder_v2_1_out_9));
  AND and_51 (.in_1(n4_16_decoder_v2_1_out_9), .out_3(and_51_out_3), .in_2(n4_16_decoder_v2_1_out_9));
  Memory_Bit memory_bit_35 (.Write(and_6_out_3), .Input(in_1[2]), .Memory(memory_bit_35_memory));
  AND and_52 (.in_1(memory_bit_35_memory), .out_3(and_52_out_3), .in_2(n4_16_decoder_v2_1_out_11));
  Memory_Bit memory_bit_36 (.Write(and_7_out_3), .Input(in_1[2]), .Memory(memory_bit_36_memory));
  AND and_53 (.in_1(memory_bit_36_memory), .out_3(and_53_out_3), .in_2(n4_16_decoder_v2_1_out_13));
  Memory_Bit memory_bit_37 (.Write(and_8_out_3), .Input(in_1[2]), .Memory(memory_bit_37_memory));
  AND and_54 (.in_1(memory_bit_37_memory), .out_3(and_54_out_3), .in_2(n4_16_decoder_v2_1_out_15));
  Memory_Bit memory_bit_38 (.Write(and_9_out_3), .Input(in_1[2]), .Memory(memory_bit_38_memory));
  AND and_55 (.in_1(memory_bit_38_memory), .out_3(and_55_out_3), .in_2(n4_16_decoder_v2_1_out_17));
  Memory_Bit memory_bit_39 (.Write(and_14_out_3), .Input(in_1[2]), .Memory(memory_bit_39_memory));
  AND and_56 (.in_1(memory_bit_39_memory), .out_3(and_56_out_3), .in_2(n4_16_decoder_v2_1_out_19));
  Memory_Bit memory_bit_40 (.Write(and_10_out_3), .Input(in_1[2]), .Memory(memory_bit_40_memory));
  AND and_57 (.in_1(memory_bit_40_memory), .out_3(and_57_out_3), .in_2(n4_16_decoder_v2_1_out_21));
  Memory_Bit memory_bit_41 (.Write(and_3_out_3), .Input(in_1[2]), .Memory(memory_bit_41_memory));
  AND and_58 (.in_1(memory_bit_41_memory), .out_3(n4_16_decoder_v2_1_out_23), .in_2(n4_16_decoder_v2_1_out_23));
  Memory_Bit memory_bit_42 (.Write(and_11_out_3), .Input(in_1[2]), .Memory(memory_bit_42_memory));
  AND and_59 (.in_1(memory_bit_42_memory), .out_3(and_59_out_3), .in_2(and_12_out_3));
  Memory_Bit memory_bit_43 (.Write(and_4_out_3), .Input(in_1[2]), .Memory(memory_bit_43_memory));
  AND and_60 (.in_1(memory_bit_43_memory), .out_3(and_60_out_3), .in_2(n4_16_decoder_v2_1_out_27));
  Memory_Bit memory_bit_44 (.Write(and_5_out_3), .Input(in_1[2]), .Memory(memory_bit_44_memory));
  AND and_61 (.in_1(memory_bit_44_memory), .out_3(and_61_out_3), .in_2(n4_16_decoder_v2_1_out_29));
  Memory_Bit memory_bit_45 (.Write(and_15_out_3), .Input(in_1[2]), .Memory(memory_bit_45_memory));
  AND and_62 (.in_1(memory_bit_45_memory), .out_3(and_62_out_3), .in_2(n4_16_decoder_v2_1_out_31));
  Memory_Bit memory_bit_46 (.Write(and_16_out_3), .Input(in_1[2]), .Memory(memory_bit_46_memory));
  AND and_63 (.in_1(memory_bit_46_memory), .out_3(and_63_out_3), .in_2(n4_16_decoder_v2_1_out_33));
  Memory_Bit memory_bit_47 (.Write(and_17_out_3), .Input(in_1[2]), .Memory(memory_bit_47_memory));
  AND and_64 (.in_1(memory_bit_47_memory), .out_3(and_64_out_3), .in_2(n4_16_decoder_v2_1_out_35));
  Memory_Bit memory_bit_48 (.Write(and_13_out_3), .Input(in_1[2]), .Memory(memory_bit_48_memory));
  AND and_65 (.in_1(memory_bit_48_memory), .out_3(and_65_out_3), .in_2(n4_16_decoder_v2_1_out_37));
  _16_bit_OR u_16_bit_or_3 (
    .Out(out_8[2]), .in_1(and_65_out_3), .in_2(and_64_out_3), .in_3(and_63_out_3), .in_4(and_62_out_3),
    .in_5(and_61_out_3), .in_6(and_60_out_3), .in_7(and_59_out_3), .in_8(n4_16_decoder_v2_1_out_23),
    .in_9(and_57_out_3), .in_10(and_56_out_3), .in_11(and_55_out_3), .in_12(and_54_out_3),
    .in_13(and_53_out_3), .in_14(and_52_out_3), .in_15(and_51_out_3), .in_16(and_50_out_3));
  Memory_Bit memory_bit_49 (.Write(and_1_out_3), .Input(in_1[3]), .Memory(memory_bit_49_memory));
  AND and_66 (.in_1(memory_bit_49_memory), .out_3(and_66_out_3), .in_2(n4_16_decoder_v2_1_out_7));
  Memory_Bit memory_bit_50 (.Write(and_2_out_3), .Input(in_1[3]), .Memory(memory_bit_50_memory));
  AND and_67 (.in_1(memory_bit_50_memory), .out_3(and_67_out_3), .in_2(n4_16_decoder_v2_1_out_9));
  Memory_Bit memory_bit_51 (.Write(and_6_out_3), .Input(in_1[3]), .Memory(memory_bit_51_memory));
  AND and_68 (.in_1(memory_bit_51_memory), .out_3(and_68_out_3), .in_2(n4_16_decoder_v2_1_out_11));
  Memory_Bit memory_bit_52 (.Write(and_7_out_3), .Input(in_1[3]), .Memory(memory_bit_52_memory));
  AND and_69 (.in_1(memory_bit_52_memory), .out_3(and_69_out_3), .in_2(n4_16_decoder_v2_1_out_13));
  Memory_Bit memory_bit_53 (.Write(and_8_out_3), .Input(in_1[3]), .Memory(memory_bit_53_memory));
  AND and_70 (.in_1(memory_bit_53_memory), .out_3(and_70_out_3), .in_2(n4_16_decoder_v2_1_out_15));
  Memory_Bit memory_bit_54 (.Write(and_9_out_3), .Input(in_1[3]), .Memory(memory_bit_54_memory));
  AND and_71 (.in_1(memory_bit_54_memory), .out_3(and_71_out_3), .in_2(n4_16_decoder_v2_1_out_17));
  Memory_Bit memory_bit_55 (.Write(and_14_out_3), .Input(in_1[3]), .Memory(memory_bit_55_memory));
  AND and_72 (.in_1(memory_bit_55_memory), .out_3(and_72_out_3), .in_2(n4_16_decoder_v2_1_out_19));
  Memory_Bit memory_bit_56 (.Write(and_10_out_3), .Input(in_1[3]), .Memory(memory_bit_56_memory));
  AND and_73 (.in_1(memory_bit_56_memory), .out_3(and_73_out_3), .in_2(n4_16_decoder_v2_1_out_21));
  Memory_Bit memory_bit_57 (.Write(and_3_out_3), .Input(in_1[3]), .Memory(memory_bit_57_memory));
  AND and_74 (.in_1(memory_bit_57_memory), .out_3(n4_16_decoder_v2_1_out_23), .in_2(n4_16_decoder_v2_1_out_23));
  Memory_Bit memory_bit_58 (.Write(and_11_out_3), .Input(in_1[3]), .Memory(memory_bit_58_memory));
  AND and_75 (.in_1(memory_bit_58_memory), .out_3(and_75_out_3), .in_2(and_12_out_3));
  Memory_Bit memory_bit_59 (.Write(and_4_out_3), .Input(in_1[3]), .Memory(memory_bit_59_memory));
  AND and_76 (.in_1(memory_bit_59_memory), .out_3(and_76_out_3), .in_2(n4_16_decoder_v2_1_out_27));
  Memory_Bit memory_bit_60 (.Write(and_5_out_3), .Input(in_1[3]), .Memory(memory_bit_60_memory));
  AND and_77 (.in_1(memory_bit_60_memory), .out_3(and_77_out_3), .in_2(n4_16_decoder_v2_1_out_29));
  Memory_Bit memory_bit_61 (.Write(and_15_out_3), .Input(in_1[3]), .Memory(memory_bit_61_memory));
  AND and_78 (.in_1(memory_bit_61_memory), .out_3(and_78_out_3), .in_2(n4_16_decoder_v2_1_out_31));
  Memory_Bit memory_bit_62 (.Write(and_16_out_3), .Input(in_1[3]), .Memory(memory_bit_62_memory));
  AND and_79 (.in_1(memory_bit_62_memory), .out_3(and_79_out_3), .in_2(n4_16_decoder_v2_1_out_33));
  Memory_Bit memory_bit_63 (.Write(and_17_out_3), .Input(in_1[3]), .Memory(memory_bit_63_memory));
  AND and_80 (.in_1(memory_bit_63_memory), .out_3(and_80_out_3), .in_2(n4_16_decoder_v2_1_out_35));
  Memory_Bit memory_bit_64 (.Write(and_13_out_3), .Input(in_1[3]), .Memory(memory_bit_64_memory));
  AND and_81 (.in_1(memory_bit_64_memory), .out_3(and_81_out_3), .in_2(n4_16_decoder_v2_1_out_37));
  _16_bit_OR u_16_bit_or_4 (
    .Out(out_8[3]), .in_1(and_81_out_3), .in_2(and_80_out_3), .in_3(and_79_out_3), .in_4(and_78_out_3),
    .in_5(and_77_out_3), .in_6(and_76_out_3), .in_7(and_75_out_3), .in_8(n4_16_decoder_v2_1_out_23),
    .in_9(and_73_out_3), .in_10(and_72_out_3), .in_11(and_71_out_3), .in_12(and_70_out_3),
    .in_13(and_69_out_3), .in_14(and_68_out_3), .in_15(and_67_out_3), .in_16(and_66_out_3));
  Memory_Bit memory_bit_65 (.Write(and_1_out_3), .Input(in_1[4]), .Memory(memory_bit_65_memory));
  AND and_82 (.in_1(memory_bit_65_memory), .out_3(and_82_out_3), .in_2(n4_16_decoder_v2_1_out_7));
  Memory_Bit memory_bit_66 (.Write(and_2_out_3), .Input(in_1[4]), .Memory(memory_bit_66_memory));
  AND and_83 (.in_1(memory_bit_66_memory), .out_3(and_83_out_3), .in_2(n4_16_decoder_v2_1_out_9));
  Memory_Bit memory_bit_67 (.Write(and_6_out_3), .Input(in_1[4]), .Memory(memory_bit_67_memory));
  AND and_84 (.in_1(memory_bit_67_memory), .out_3(and_84_out_3), .in_2(n4_16_decoder_v2_1_out_11));
  Memory_Bit memory_bit_68 (.Write(and_7_out_3), .Input(in_1[4]), .Memory(memory_bit_68_memory));
  AND and_85 (.in_1(memory_bit_68_memory), .out_3(and_85_out_3), .in_2(n4_16_decoder_v2_1_out_13));
  Memory_Bit memory_bit_69 (.Write(and_8_out_3), .Input(in_1[4]), .Memory(memory_bit_69_memory));
  AND and_86 (.in_1(memory_bit_69_memory), .out_3(and_86_out_3), .in_2(n4_16_decoder_v2_1_out_15));
  Memory_Bit memory_bit_70 (.Write(and_9_out_3), .Input(in_1[4]), .Memory(memory_bit_70_memory));
  AND and_87 (.in_1(memory_bit_70_memory), .out_3(and_87_out_3), .in_2(n4_16_decoder_v2_1_out_17));
  Memory_Bit memory_bit_71 (.Write(and_14_out_3), .Input(in_1[4]), .Memory(memory_bit_71_memory));
  AND and_88 (.in_1(memory_bit_71_memory), .out_3(and_88_out_3), .in_2(n4_16_decoder_v2_1_out_19));
  Memory_Bit memory_bit_72 (.Write(and_10_out_3), .Input(in_1[4]), .Memory(memory_bit_72_memory));
  AND and_89 (.in_1(memory_bit_72_memory), .out_3(and_89_out_3), .in_2(n4_16_decoder_v2_1_out_21));
  Memory_Bit memory_bit_73 (.Write(and_3_out_3), .Input(in_1[4]), .Memory(memory_bit_73_memory));
  AND and_90 (.in_1(memory_bit_73_memory), .out_3(and_90_out_3), .in_2(n4_16_decoder_v2_1_out_23));
  Memory_Bit memory_bit_74 (.Write(and_11_out_3), .Input(in_1[4]), .Memory(memory_bit_74_memory));
  AND and_91 (.in_1(memory_bit_74_memory), .out_3(and_91_out_3), .in_2(and_12_out_3));
  Memory_Bit memory_bit_75 (.Write(and_4_out_3), .Input(in_1[4]), .Memory(memory_bit_75_memory));
  AND and_92 (.in_1(memory_bit_75_memory), .out_3(and_92_out_3), .in_2(n4_16_decoder_v2_1_out_27));
  Memory_Bit memory_bit_76 (.Write(and_5_out_3), .Input(in_1[4]), .Memory(memory_bit_76_memory));
  AND and_93 (.in_1(memory_bit_76_memory), .out_3(and_93_out_3), .in_2(n4_16_decoder_v2_1_out_29));
  Memory_Bit memory_bit_77 (.Write(and_15_out_3), .Input(in_1[4]), .Memory(memory_bit_77_memory));
  AND and_94 (.in_1(memory_bit_77_memory), .out_3(and_94_out_3), .in_2(n4_16_decoder_v2_1_out_31));
  Memory_Bit memory_bit_78 (.Write(and_16_out_3), .Input(in_1[4]), .Memory(memory_bit_78_memory));
  AND and_95 (.in_1(memory_bit_78_memory), .out_3(and_95_out_3), .in_2(n4_16_decoder_v2_1_out_33));
  Memory_Bit memory_bit_79 (.Write(and_17_out_3), .Input(in_1[4]), .Memory(memory_bit_79_memory));
  AND and_96 (.in_1(memory_bit_79_memory), .out_3(and_96_out_3), .in_2(n4_16_decoder_v2_1_out_35));
  Memory_Bit memory_bit_80 (.Write(and_13_out_3), .Input(in_1[4]), .Memory(memory_bit_80_memory));
  AND and_97 (.in_1(memory_bit_80_memory), .out_3(and_97_out_3), .in_2(n4_16_decoder_v2_1_out_37));
  _16_bit_OR u_16_bit_or_5 (
    .Out(out_8[4]), .in_1(and_97_out_3), .in_2(and_96_out_3), .in_3(and_95_out_3), .in_4(and_94_out_3),
    .in_5(and_93_out_3), .in_6(and_92_out_3), .in_7(and_91_out_3), .in_8(and_90_out_3), .in_9(and_89_out_3),
    .in_10(and_88_out_3), .in_11(and_87_out_3), .in_12(and_86_out_3), .in_13(and_85_out_3),
    .in_14(and_84_out_3), .in_15(and_83_out_3), .in_16(and_82_out_3));
  Memory_Bit memory_bit_81 (.Write(and_1_out_3), .Input(in_1[5]), .Memory(memory_bit_81_memory));
  AND and_98 (.in_1(memory_bit_81_memory), .out_3(and_98_out_3), .in_2(n4_16_decoder_v2_1_out_7));
  Memory_Bit memory_bit_82 (.Write(and_2_out_3), .Input(in_1[5]), .Memory(memory_bit_82_memory));
  AND and_99 (.in_1(memory_bit_82_memory), .out_3(and_99_out_3), .in_2(n4_16_decoder_v2_1_out_9));
  Memory_Bit memory_bit_83 (.Write(and_6_out_3), .Input(in_1[5]), .Memory(memory_bit_83_memory));
  AND and_100 (.in_1(memory_bit_83_memory), .out_3(and_100_out_3), .in_2(n4_16_decoder_v2_1_out_11));
  Memory_Bit memory_bit_84 (.Write(and_7_out_3), .Input(in_1[5]), .Memory(memory_bit_84_memory));
  AND and_101 (.in_1(memory_bit_84_memory), .out_3(and_101_out_3), .in_2(n4_16_decoder_v2_1_out_13));
  Memory_Bit memory_bit_85 (.Write(and_8_out_3), .Input(in_1[5]), .Memory(memory_bit_85_memory));
  AND and_102 (.in_1(memory_bit_85_memory), .out_3(and_102_out_3), .in_2(n4_16_decoder_v2_1_out_15));
  Memory_Bit memory_bit_86 (.Write(and_9_out_3), .Input(in_1[5]), .Memory(memory_bit_86_memory));
  AND and_103 (.in_1(memory_bit_86_memory), .out_3(and_103_out_3), .in_2(n4_16_decoder_v2_1_out_17));
  Memory_Bit memory_bit_87 (.Write(and_14_out_3), .Input(in_1[5]), .Memory(memory_bit_87_memory));
  AND and_104 (.in_1(memory_bit_87_memory), .out_3(and_104_out_3), .in_2(n4_16_decoder_v2_1_out_19));
  Memory_Bit memory_bit_88 (.Write(and_10_out_3), .Input(in_1[5]), .Memory(memory_bit_88_memory));
  AND and_105 (.in_1(memory_bit_88_memory), .out_3(and_105_out_3), .in_2(n4_16_decoder_v2_1_out_21));
  Memory_Bit memory_bit_89 (.Write(and_3_out_3), .Input(in_1[5]), .Memory(memory_bit_89_memory));
  AND and_106 (.in_1(memory_bit_89_memory), .out_3(and_106_out_3), .in_2(n4_16_decoder_v2_1_out_23));
  Memory_Bit memory_bit_90 (.Write(and_11_out_3), .Input(in_1[5]), .Memory(memory_bit_90_memory));
  AND and_107 (.in_1(memory_bit_90_memory), .out_3(and_107_out_3), .in_2(and_12_out_3));
  Memory_Bit memory_bit_91 (.Write(and_4_out_3), .Input(in_1[5]), .Memory(memory_bit_91_memory));
  AND and_108 (.in_1(memory_bit_91_memory), .out_3(and_108_out_3), .in_2(n4_16_decoder_v2_1_out_27));
  Memory_Bit memory_bit_92 (.Write(and_5_out_3), .Input(in_1[5]), .Memory(memory_bit_92_memory));
  AND and_109 (.in_1(memory_bit_92_memory), .out_3(and_109_out_3), .in_2(n4_16_decoder_v2_1_out_29));
  Memory_Bit memory_bit_93 (.Write(and_15_out_3), .Input(in_1[5]), .Memory(memory_bit_93_memory));
  AND and_110 (.in_1(memory_bit_93_memory), .out_3(and_110_out_3), .in_2(n4_16_decoder_v2_1_out_31));
  Memory_Bit memory_bit_94 (.Write(and_16_out_3), .Input(in_1[5]), .Memory(memory_bit_94_memory));
  AND and_111 (.in_1(memory_bit_94_memory), .out_3(and_111_out_3), .in_2(n4_16_decoder_v2_1_out_33));
  Memory_Bit memory_bit_95 (.Write(and_17_out_3), .Input(in_1[5]), .Memory(memory_bit_95_memory));
  AND and_112 (.in_1(memory_bit_95_memory), .out_3(and_112_out_3), .in_2(n4_16_decoder_v2_1_out_35));
  Memory_Bit memory_bit_96 (.Write(and_13_out_3), .Input(in_1[5]), .Memory(memory_bit_96_memory));
  AND and_113 (.in_1(memory_bit_96_memory), .out_3(and_113_out_3), .in_2(n4_16_decoder_v2_1_out_37));
  _16_bit_OR u_16_bit_or_6 (
    .Out(out_8[5]), .in_1(and_113_out_3), .in_2(and_112_out_3), .in_3(and_111_out_3), .in_4(and_110_out_3),
    .in_5(and_109_out_3), .in_6(and_108_out_3), .in_7(and_107_out_3), .in_8(and_106_out_3),
    .in_9(and_105_out_3), .in_10(and_104_out_3), .in_11(and_103_out_3), .in_12(and_102_out_3),
    .in_13(and_101_out_3), .in_14(and_100_out_3), .in_15(and_99_out_3), .in_16(and_98_out_3));
  Memory_Bit memory_bit_97 (.Write(and_1_out_3), .Input(in_1[6]), .Memory(memory_bit_97_memory));
  AND and_114 (.in_1(memory_bit_97_memory), .out_3(and_114_out_3), .in_2(n4_16_decoder_v2_1_out_7));
  Memory_Bit memory_bit_98 (.Write(and_2_out_3), .Input(in_1[6]), .Memory(memory_bit_98_memory));
  AND and_115 (.in_1(memory_bit_98_memory), .out_3(and_115_out_3), .in_2(n4_16_decoder_v2_1_out_9));
  Memory_Bit memory_bit_99 (.Write(and_6_out_3), .Input(in_1[6]), .Memory(memory_bit_99_memory));
  AND and_116 (.in_1(memory_bit_99_memory), .out_3(and_116_out_3), .in_2(n4_16_decoder_v2_1_out_11));
  Memory_Bit memory_bit_100 (.Write(and_7_out_3), .Input(in_1[6]), .Memory(memory_bit_100_memory));
  AND and_117 (.in_1(memory_bit_100_memory), .out_3(and_117_out_3), .in_2(n4_16_decoder_v2_1_out_13));
  Memory_Bit memory_bit_101 (.Write(and_8_out_3), .Input(in_1[6]), .Memory(memory_bit_101_memory));
  AND and_118 (.in_1(memory_bit_101_memory), .out_3(and_118_out_3), .in_2(n4_16_decoder_v2_1_out_15));
  Memory_Bit memory_bit_102 (.Write(and_9_out_3), .Input(in_1[6]), .Memory(memory_bit_102_memory));
  AND and_119 (.in_1(memory_bit_102_memory), .out_3(and_119_out_3), .in_2(n4_16_decoder_v2_1_out_17));
  Memory_Bit memory_bit_103 (.Write(and_14_out_3), .Input(in_1[6]), .Memory(memory_bit_103_memory));
  AND and_120 (.in_1(memory_bit_103_memory), .out_3(and_120_out_3), .in_2(n4_16_decoder_v2_1_out_19));
  Memory_Bit memory_bit_104 (.Write(and_10_out_3), .Input(in_1[6]), .Memory(memory_bit_104_memory));
  AND and_121 (.in_1(memory_bit_104_memory), .out_3(and_121_out_3), .in_2(n4_16_decoder_v2_1_out_21));
  Memory_Bit memory_bit_105 (.Write(and_3_out_3), .Input(in_1[6]), .Memory(memory_bit_105_memory));
  AND and_122 (.in_1(memory_bit_105_memory), .out_3(and_122_out_3), .in_2(n4_16_decoder_v2_1_out_23));
  Memory_Bit memory_bit_106 (.Write(and_11_out_3), .Input(in_1[6]), .Memory(memory_bit_106_memory));
  AND and_123 (.in_1(memory_bit_106_memory), .out_3(and_123_out_3), .in_2(and_12_out_3));
  Memory_Bit memory_bit_107 (.Write(and_4_out_3), .Input(in_1[6]), .Memory(memory_bit_107_memory));
  AND and_124 (.in_1(memory_bit_107_memory), .out_3(and_124_out_3), .in_2(n4_16_decoder_v2_1_out_27));
  Memory_Bit memory_bit_108 (.Write(and_5_out_3), .Input(in_1[6]), .Memory(memory_bit_108_memory));
  AND and_125 (.in_1(memory_bit_108_memory), .out_3(and_125_out_3), .in_2(n4_16_decoder_v2_1_out_29));
  Memory_Bit memory_bit_109 (.Write(and_15_out_3), .Input(in_1[6]), .Memory(memory_bit_109_memory));
  AND and_126 (.in_1(memory_bit_109_memory), .out_3(and_126_out_3), .in_2(n4_16_decoder_v2_1_out_31));
  Memory_Bit memory_bit_110 (.Write(and_16_out_3), .Input(in_1[6]), .Memory(memory_bit_110_memory));
  AND and_127 (.in_1(memory_bit_110_memory), .out_3(and_127_out_3), .in_2(n4_16_decoder_v2_1_out_33));
  Memory_Bit memory_bit_111 (.Write(and_17_out_3), .Input(in_1[6]), .Memory(memory_bit_111_memory));
  AND and_128 (.in_1(memory_bit_111_memory), .out_3(and_128_out_3), .in_2(n4_16_decoder_v2_1_out_35));
  Memory_Bit memory_bit_112 (.Write(and_13_out_3), .Input(in_1[6]), .Memory(memory_bit_112_memory));
  AND and_129 (.in_1(memory_bit_112_memory), .out_3(and_129_out_3), .in_2(n4_16_decoder_v2_1_out_37));
  _16_bit_OR u_16_bit_or_7 (
    .Out(out_8[6]), .in_1(and_129_out_3), .in_2(and_128_out_3), .in_3(and_127_out_3), .in_4(and_126_out_3),
    .in_5(and_125_out_3), .in_6(and_124_out_3), .in_7(and_123_out_3), .in_8(and_122_out_3),
    .in_9(and_121_out_3), .in_10(and_120_out_3), .in_11(and_119_out_3), .in_12(and_118_out_3),
    .in_13(and_117_out_3), .in_14(and_116_out_3), .in_15(and_115_out_3), .in_16(and_114_out_3));
  Memory_Bit memory_bit_113 (.Write(and_1_out_3), .Input(in_1[7]), .Memory(memory_bit_113_memory));
  AND and_130 (.in_1(memory_bit_113_memory), .out_3(and_130_out_3), .in_2(n4_16_decoder_v2_1_out_7));
  Memory_Bit memory_bit_114 (.Write(and_2_out_3), .Input(in_1[7]), .Memory(memory_bit_114_memory));
  AND and_131 (.in_1(memory_bit_114_memory), .out_3(and_131_out_3), .in_2(n4_16_decoder_v2_1_out_9));
  Memory_Bit memory_bit_115 (.Write(and_6_out_3), .Input(in_1[7]), .Memory(memory_bit_115_memory));
  AND and_132 (.in_1(memory_bit_115_memory), .out_3(and_132_out_3), .in_2(n4_16_decoder_v2_1_out_11));
  Memory_Bit memory_bit_116 (.Write(and_7_out_3), .Input(in_1[7]), .Memory(memory_bit_116_memory));
  AND and_133 (.in_1(memory_bit_116_memory), .out_3(and_133_out_3), .in_2(n4_16_decoder_v2_1_out_13));
  Memory_Bit memory_bit_117 (.Write(and_8_out_3), .Input(in_1[7]), .Memory(memory_bit_117_memory));
  AND and_134 (.in_1(memory_bit_117_memory), .out_3(and_134_out_3), .in_2(n4_16_decoder_v2_1_out_15));
  Memory_Bit memory_bit_118 (.Write(and_9_out_3), .Input(in_1[7]), .Memory(memory_bit_118_memory));
  AND and_135 (.in_1(memory_bit_118_memory), .out_3(and_135_out_3), .in_2(n4_16_decoder_v2_1_out_17));
  Memory_Bit memory_bit_119 (.Write(and_14_out_3), .Input(in_1[7]), .Memory(memory_bit_119_memory));
  AND and_136 (.in_1(memory_bit_119_memory), .out_3(and_136_out_3), .in_2(n4_16_decoder_v2_1_out_19));
  Memory_Bit memory_bit_120 (.Write(and_10_out_3), .Input(in_1[7]), .Memory(memory_bit_120_memory));
  AND and_137 (.in_1(memory_bit_120_memory), .out_3(and_137_out_3), .in_2(n4_16_decoder_v2_1_out_21));
  Memory_Bit memory_bit_121 (.Write(and_3_out_3), .Input(in_1[7]), .Memory(memory_bit_121_memory));
  AND and_138 (.in_1(memory_bit_121_memory), .out_3(and_138_out_3), .in_2(n4_16_decoder_v2_1_out_23));
  Memory_Bit memory_bit_122 (.Write(and_11_out_3), .Input(in_1[7]), .Memory(memory_bit_122_memory));
  AND and_139 (.in_1(memory_bit_122_memory), .out_3(and_139_out_3), .in_2(and_12_out_3));
  Memory_Bit memory_bit_123 (.Write(and_4_out_3), .Input(in_1[7]), .Memory(memory_bit_123_memory));
  AND and_140 (.in_1(memory_bit_123_memory), .out_3(and_140_out_3), .in_2(n4_16_decoder_v2_1_out_27));
  Memory_Bit memory_bit_124 (.Write(and_5_out_3), .Input(in_1[7]), .Memory(memory_bit_124_memory));
  AND and_141 (.in_1(memory_bit_124_memory), .out_3(and_141_out_3), .in_2(n4_16_decoder_v2_1_out_29));
  Memory_Bit memory_bit_125 (.Write(and_15_out_3), .Input(in_1[7]), .Memory(memory_bit_125_memory));
  AND and_142 (.in_1(memory_bit_125_memory), .out_3(and_142_out_3), .in_2(n4_16_decoder_v2_1_out_31));
  Memory_Bit memory_bit_126 (.Write(and_16_out_3), .Input(in_1[7]), .Memory(memory_bit_126_memory));
  AND and_143 (.in_1(memory_bit_126_memory), .out_3(and_143_out_3), .in_2(n4_16_decoder_v2_1_out_33));
  Memory_Bit memory_bit_127 (.Write(and_17_out_3), .Input(in_1[7]), .Memory(memory_bit_127_memory));
  AND and_144 (.in_1(memory_bit_127_memory), .out_3(and_144_out_3), .in_2(n4_16_decoder_v2_1_out_35));
  Memory_Bit memory_bit_128 (.Write(and_13_out_3), .Input(in_1[7]), .Memory(memory_bit_128_memory));
  AND and_145 (.in_1(memory_bit_128_memory), .out_3(and_145_out_3), .in_2(n4_16_decoder_v2_1_out_37));
  _16_bit_OR u_16_bit_or_8 (
    .Out(out_8[7]), .in_1(and_145_out_3), .in_2(and_144_out_3), .in_3(and_143_out_3), .in_4(and_142_out_3),
    .in_5(and_141_out_3), .in_6(and_140_out_3), .in_7(and_139_out_3), .in_8(and_138_out_3),
    .in_9(and_137_out_3), .in_10(and_136_out_3), .in_11(and_135_out_3), .in_12(and_134_out_3),
    .in_13(and_133_out_3), .in_14(and_132_out_3), .in_15(and_131_out_3), .in_16(and_130_out_3));
endmodule
module backup_mem_bank (
  input  Input_2,
  input  Input_0,
  input  Input_1,
  input  Input_3,
  input  Input_4,
  input  Input_5,
  input  Input_6,
  input  Input_7,
  input  Memory_Write,
  input  in_10,
  input  in_11,
  input  in_12,
  input  in_13,
  input  X,
  output O2,
  output O0,
  output O1,
  output O3,
  output O4,
  output O5,
  output O6,
  output O7
);

  wire and_1_out_3, and_2_out_3, and_3_out_3, and_4_out_3, and_5_out_3, and_6_out_3, and_7_out_3,
       and_8_out_3, and_9_out_3, and_10_out_3, and_11_out_3, and_12_out_3, and_13_out_3, and_14_out_3,
       and_15_out_3, and_16_out_3, and_17_out_3, and_18_out_3, and_19_out_3, and_20_out_3, and_21_out_3,
       and_22_out_3, and_23_out_3, and_24_out_3, and_25_out_3, and_26_out_3, and_27_out_3, and_28_out_3,
       and_29_out_3, and_30_out_3, and_31_out_3, and_32_out_3, and_33_out_3, and_34_out_3, and_35_out_3,
       and_36_out_3, and_37_out_3, and_38_out_3, and_39_out_3, and_40_out_3, and_41_out_3, and_42_out_3,
       and_43_out_3, and_44_out_3, and_45_out_3, and_46_out_3, and_47_out_3, and_48_out_3, and_49_out_3,
       and_50_out_3, and_51_out_3, and_52_out_3, and_53_out_3, and_54_out_3, and_55_out_3, and_56_out_3,
       and_57_out_3, and_59_out_3, and_60_out_3, and_61_out_3, and_62_out_3, and_63_out_3, and_64_out_3,
       and_65_out_3, and_66_out_3, and_67_out_3, and_68_out_3, and_69_out_3, and_70_out_3, and_71_out_3,
       and_72_out_3, and_73_out_3, and_75_out_3, and_76_out_3, and_77_out_3, and_78_out_3, and_79_out_3,
       and_80_out_3, and_81_out_3, and_82_out_3, and_83_out_3, and_84_out_3, and_85_out_3, and_86_out_3,
       and_87_out_3, and_88_out_3, and_89_out_3, and_90_out_3, and_91_out_3, and_92_out_3, and_93_out_3,
       and_94_out_3, and_95_out_3, and_96_out_3, and_97_out_3, and_98_out_3, and_99_out_3, and_100_out_3,
       and_101_out_3, and_102_out_3, and_103_out_3, and_104_out_3, and_105_out_3, and_106_out_3,
       and_107_out_3, and_108_out_3, and_109_out_3, and_110_out_3, and_111_out_3, and_112_out_3,
       and_113_out_3, and_114_out_3, and_115_out_3, and_116_out_3, and_117_out_3, and_118_out_3,
       and_119_out_3, and_120_out_3, and_121_out_3, and_122_out_3, and_123_out_3, and_124_out_3,
       and_125_out_3, and_126_out_3, and_127_out_3, and_128_out_3, and_129_out_3, and_130_out_3,
       and_131_out_3, and_132_out_3, and_133_out_3, and_134_out_3, and_135_out_3, and_136_out_3,
       and_137_out_3, and_138_out_3, and_139_out_3, and_140_out_3, and_141_out_3, and_142_out_3,
       and_143_out_3, and_144_out_3, and_145_out_3, memory_bit_1_memory, memory_bit_2_memory,
       memory_bit_3_memory, memory_bit_4_memory, memory_bit_5_memory, memory_bit_6_memory,
       memory_bit_7_memory, memory_bit_8_memory, memory_bit_9_memory, memory_bit_10_memory,
       memory_bit_11_memory, memory_bit_12_memory, memory_bit_13_memory, memory_bit_14_memory,
       memory_bit_15_memory, memory_bit_16_memory, memory_bit_17_memory, memory_bit_18_memory,
       memory_bit_19_memory, memory_bit_20_memory, memory_bit_21_memory, memory_bit_22_memory,
       memory_bit_23_memory, memory_bit_24_memory, memory_bit_25_memory, memory_bit_26_memory,
       memory_bit_27_memory, memory_bit_28_memory, memory_bit_29_memory, memory_bit_30_memory,
       memory_bit_31_memory, memory_bit_32_memory, memory_bit_33_memory, memory_bit_35_memory,
       memory_bit_36_memory, memory_bit_37_memory, memory_bit_38_memory, memory_bit_39_memory,
       memory_bit_40_memory, memory_bit_41_memory, memory_bit_42_memory, memory_bit_43_memory,
       memory_bit_44_memory, memory_bit_45_memory, memory_bit_46_memory, memory_bit_47_memory,
       memory_bit_48_memory, memory_bit_49_memory, memory_bit_50_memory, memory_bit_51_memory,
       memory_bit_52_memory, memory_bit_53_memory, memory_bit_54_memory, memory_bit_55_memory,
       memory_bit_56_memory, memory_bit_57_memory, memory_bit_58_memory, memory_bit_59_memory,
       memory_bit_60_memory, memory_bit_61_memory, memory_bit_62_memory, memory_bit_63_memory,
       memory_bit_64_memory, memory_bit_65_memory, memory_bit_66_memory, memory_bit_67_memory,
       memory_bit_68_memory, memory_bit_69_memory, memory_bit_70_memory, memory_bit_71_memory,
       memory_bit_72_memory, memory_bit_73_memory, memory_bit_74_memory, memory_bit_75_memory,
       memory_bit_76_memory, memory_bit_77_memory, memory_bit_78_memory, memory_bit_79_memory,
       memory_bit_80_memory, memory_bit_81_memory, memory_bit_82_memory, memory_bit_83_memory,
       memory_bit_84_memory, memory_bit_85_memory, memory_bit_86_memory, memory_bit_87_memory,
       memory_bit_88_memory, memory_bit_89_memory, memory_bit_90_memory, memory_bit_91_memory,
       memory_bit_92_memory, memory_bit_93_memory, memory_bit_94_memory, memory_bit_95_memory,
       memory_bit_96_memory, memory_bit_97_memory, memory_bit_98_memory, memory_bit_99_memory,
       memory_bit_100_memory, memory_bit_101_memory, memory_bit_102_memory, memory_bit_103_memory,
       memory_bit_104_memory, memory_bit_105_memory, memory_bit_106_memory, memory_bit_107_memory,
       memory_bit_108_memory, memory_bit_109_memory, memory_bit_110_memory, memory_bit_111_memory,
       memory_bit_112_memory, memory_bit_113_memory, memory_bit_114_memory, memory_bit_115_memory,
       memory_bit_116_memory, memory_bit_117_memory, memory_bit_118_memory, memory_bit_119_memory,
       memory_bit_120_memory, memory_bit_121_memory, memory_bit_122_memory, memory_bit_123_memory,
       memory_bit_124_memory, memory_bit_125_memory, memory_bit_126_memory, memory_bit_127_memory,
       memory_bit_128_memory, n4_16_decoder_v2_1_out_6, n4_16_decoder_v2_1_out_7, n4_16_decoder_v2_1_out_8,
       n4_16_decoder_v2_1_out_9, n4_16_decoder_v2_1_out_10, n4_16_decoder_v2_1_out_11,
       n4_16_decoder_v2_1_out_12, n4_16_decoder_v2_1_out_13, n4_16_decoder_v2_1_out_14,
       n4_16_decoder_v2_1_out_15, n4_16_decoder_v2_1_out_16, n4_16_decoder_v2_1_out_17,
       n4_16_decoder_v2_1_out_18, n4_16_decoder_v2_1_out_19, n4_16_decoder_v2_1_out_20,
       n4_16_decoder_v2_1_out_21, n4_16_decoder_v2_1_out_22, n4_16_decoder_v2_1_out_23,
       n4_16_decoder_v2_1_out_24, n4_16_decoder_v2_1_out_25, n4_16_decoder_v2_1_out_26,
       n4_16_decoder_v2_1_out_27, n4_16_decoder_v2_1_out_28, n4_16_decoder_v2_1_out_29,
       n4_16_decoder_v2_1_out_30, n4_16_decoder_v2_1_out_31, n4_16_decoder_v2_1_out_32,
       n4_16_decoder_v2_1_out_33, n4_16_decoder_v2_1_out_34, n4_16_decoder_v2_1_out_35,
       n4_16_decoder_v2_1_out_36, n4_16_decoder_v2_1_out_37;

  _4_16_Decoder_V2 u_4_16_decoder_v2_1 (
    .in_1(in_10), .in_2(in_11), .in_3(in_12), .in_4(in_13), .in_5(X), .out_6(n4_16_decoder_v2_1_out_6),
    .out_7(n4_16_decoder_v2_1_out_7), .out_8(n4_16_decoder_v2_1_out_8), .out_9(n4_16_decoder_v2_1_out_9),
    .out_10(n4_16_decoder_v2_1_out_10), .out_11(n4_16_decoder_v2_1_out_11),
    .out_12(n4_16_decoder_v2_1_out_12), .out_13(n4_16_decoder_v2_1_out_13),
    .out_14(n4_16_decoder_v2_1_out_14), .out_15(n4_16_decoder_v2_1_out_15),
    .out_16(n4_16_decoder_v2_1_out_16), .out_17(n4_16_decoder_v2_1_out_17),
    .out_18(n4_16_decoder_v2_1_out_18), .out_19(n4_16_decoder_v2_1_out_19),
    .out_20(n4_16_decoder_v2_1_out_20), .out_21(n4_16_decoder_v2_1_out_21),
    .out_22(n4_16_decoder_v2_1_out_22), .out_23(n4_16_decoder_v2_1_out_23),
    .out_24(n4_16_decoder_v2_1_out_24), .out_25(n4_16_decoder_v2_1_out_25),
    .out_26(n4_16_decoder_v2_1_out_26), .out_27(n4_16_decoder_v2_1_out_27),
    .out_28(n4_16_decoder_v2_1_out_28), .out_29(n4_16_decoder_v2_1_out_29),
    .out_30(n4_16_decoder_v2_1_out_30), .out_31(n4_16_decoder_v2_1_out_31),
    .out_32(n4_16_decoder_v2_1_out_32), .out_33(n4_16_decoder_v2_1_out_33),
    .out_34(n4_16_decoder_v2_1_out_34), .out_35(n4_16_decoder_v2_1_out_35),
    .out_36(n4_16_decoder_v2_1_out_36), .out_37(n4_16_decoder_v2_1_out_37));
  AND and_1 (.in_1(Memory_Write), .out_3(and_1_out_3), .in_2(n4_16_decoder_v2_1_out_6));
  AND and_2 (.in_1(Memory_Write), .out_3(and_2_out_3), .in_2(n4_16_decoder_v2_1_out_8));
  AND and_3 (.in_1(Memory_Write), .out_3(and_3_out_3), .in_2(n4_16_decoder_v2_1_out_22));
  AND and_4 (.in_1(Memory_Write), .out_3(and_4_out_3), .in_2(n4_16_decoder_v2_1_out_26));
  AND and_5 (.in_1(Memory_Write), .out_3(and_5_out_3), .in_2(n4_16_decoder_v2_1_out_28));
  AND and_6 (.in_1(Memory_Write), .out_3(and_6_out_3), .in_2(n4_16_decoder_v2_1_out_10));
  AND and_7 (.in_1(Memory_Write), .out_3(and_7_out_3), .in_2(n4_16_decoder_v2_1_out_12));
  AND and_8 (.in_1(Memory_Write), .out_3(and_8_out_3), .in_2(n4_16_decoder_v2_1_out_14));
  AND and_9 (.in_1(Memory_Write), .out_3(and_9_out_3), .in_2(n4_16_decoder_v2_1_out_16));
  AND and_10 (.in_1(Memory_Write), .out_3(and_10_out_3), .in_2(n4_16_decoder_v2_1_out_20));
  AND and_11 (.in_1(Memory_Write), .out_3(and_11_out_3), .in_2(n4_16_decoder_v2_1_out_24));
  AND and_12 (.in_1(Memory_Write), .out_3(and_12_out_3), .in_2(n4_16_decoder_v2_1_out_25));
  AND and_13 (.in_1(Memory_Write), .out_3(and_13_out_3), .in_2(n4_16_decoder_v2_1_out_30));
  AND and_14 (.in_1(Memory_Write), .out_3(and_14_out_3), .in_2(n4_16_decoder_v2_1_out_36));
  AND and_15 (.in_1(Memory_Write), .out_3(and_15_out_3), .in_2(n4_16_decoder_v2_1_out_18));
  AND and_16 (.in_1(Memory_Write), .out_3(and_16_out_3), .in_2(n4_16_decoder_v2_1_out_32));
  AND and_17 (.in_1(Memory_Write), .out_3(and_17_out_3), .in_2(n4_16_decoder_v2_1_out_34));
  Memory_Bit memory_bit_1 (.Write(Input_0), .Input(and_1_out_3), .Memory(memory_bit_1_memory));
  AND and_18 (.in_1(memory_bit_1_memory), .out_3(and_18_out_3), .in_2(n4_16_decoder_v2_1_out_7));
  Memory_Bit memory_bit_2 (.Write(Input_0), .Input(and_2_out_3), .Memory(memory_bit_2_memory));
  AND and_19 (.in_1(memory_bit_2_memory), .out_3(and_19_out_3), .in_2(n4_16_decoder_v2_1_out_9));
  Memory_Bit memory_bit_3 (.Write(Input_0), .Input(and_6_out_3), .Memory(memory_bit_3_memory));
  AND and_20 (.in_1(memory_bit_3_memory), .out_3(and_20_out_3), .in_2(n4_16_decoder_v2_1_out_11));
  Memory_Bit memory_bit_4 (.Write(Input_0), .Input(and_7_out_3), .Memory(memory_bit_4_memory));
  AND and_21 (.in_1(memory_bit_4_memory), .out_3(and_21_out_3), .in_2(n4_16_decoder_v2_1_out_13));
  Memory_Bit memory_bit_5 (.Write(Input_0), .Input(and_8_out_3), .Memory(memory_bit_5_memory));
  AND and_22 (.in_1(memory_bit_5_memory), .out_3(and_22_out_3), .in_2(n4_16_decoder_v2_1_out_15));
  Memory_Bit memory_bit_6 (.Write(Input_0), .Input(and_9_out_3), .Memory(memory_bit_6_memory));
  AND and_23 (.in_1(memory_bit_6_memory), .out_3(and_23_out_3), .in_2(n4_16_decoder_v2_1_out_17));
  Memory_Bit memory_bit_7 (.Write(Input_0), .Input(and_15_out_3), .Memory(memory_bit_7_memory));
  AND and_24 (.in_1(memory_bit_7_memory), .out_3(and_24_out_3), .in_2(n4_16_decoder_v2_1_out_19));
  Memory_Bit memory_bit_8 (.Write(Input_0), .Input(and_10_out_3), .Memory(memory_bit_8_memory));
  AND and_25 (.in_1(memory_bit_8_memory), .out_3(and_25_out_3), .in_2(n4_16_decoder_v2_1_out_21));
  Memory_Bit memory_bit_9 (.Write(Input_0), .Input(and_3_out_3), .Memory(memory_bit_9_memory));
  AND and_26 (.in_1(memory_bit_9_memory), .out_3(and_26_out_3), .in_2(n4_16_decoder_v2_1_out_23));
  Memory_Bit memory_bit_10 (.Write(Input_0), .Input(and_11_out_3), .Memory(memory_bit_10_memory));
  AND and_27 (.in_1(memory_bit_10_memory), .out_3(and_27_out_3), .in_2(and_12_out_3));
  Memory_Bit memory_bit_11 (.Write(Input_0), .Input(and_4_out_3), .Memory(memory_bit_11_memory));
  AND and_28 (.in_1(memory_bit_11_memory), .out_3(and_28_out_3), .in_2(n4_16_decoder_v2_1_out_27));
  Memory_Bit memory_bit_12 (.Write(Input_0), .Input(and_5_out_3), .Memory(memory_bit_12_memory));
  AND and_29 (.in_1(memory_bit_12_memory), .out_3(and_29_out_3), .in_2(n4_16_decoder_v2_1_out_29));
  Memory_Bit memory_bit_13 (.Write(Input_0), .Input(and_13_out_3), .Memory(memory_bit_13_memory));
  AND and_30 (.in_1(memory_bit_13_memory), .out_3(and_30_out_3), .in_2(n4_16_decoder_v2_1_out_31));
  Memory_Bit memory_bit_14 (.Write(Input_0), .Input(and_16_out_3), .Memory(memory_bit_14_memory));
  AND and_31 (.in_1(memory_bit_14_memory), .out_3(and_31_out_3), .in_2(n4_16_decoder_v2_1_out_33));
  Memory_Bit memory_bit_15 (.Write(Input_0), .Input(and_17_out_3), .Memory(memory_bit_15_memory));
  AND and_32 (.in_1(memory_bit_15_memory), .out_3(and_32_out_3), .in_2(n4_16_decoder_v2_1_out_35));
  Memory_Bit memory_bit_16 (.Write(Input_0), .Input(and_14_out_3), .Memory(memory_bit_16_memory));
  AND and_33 (.in_1(memory_bit_16_memory), .out_3(and_33_out_3), .in_2(n4_16_decoder_v2_1_out_37));
  _16_bit_OR u_16_bit_or_1 (
    .Out(O0), .in_1(and_33_out_3), .in_2(and_32_out_3), .in_3(and_31_out_3), .in_4(and_30_out_3),
    .in_5(and_29_out_3), .in_6(and_28_out_3), .in_7(and_27_out_3), .in_8(and_26_out_3), .in_9(and_25_out_3),
    .in_10(and_24_out_3), .in_11(and_23_out_3), .in_12(and_22_out_3), .in_13(and_21_out_3),
    .in_14(and_20_out_3), .in_15(and_19_out_3), .in_16(and_18_out_3));
  Memory_Bit memory_bit_17 (.Write(Input_1), .Input(and_1_out_3), .Memory(memory_bit_17_memory));
  AND and_34 (.in_1(memory_bit_17_memory), .out_3(and_34_out_3), .in_2(n4_16_decoder_v2_1_out_7));
  Memory_Bit memory_bit_18 (.Write(Input_1), .Input(and_2_out_3), .Memory(memory_bit_18_memory));
  AND and_35 (.in_1(memory_bit_18_memory), .out_3(and_35_out_3), .in_2(n4_16_decoder_v2_1_out_9));
  Memory_Bit memory_bit_19 (.Write(Input_1), .Input(and_6_out_3), .Memory(memory_bit_19_memory));
  AND and_36 (.in_1(memory_bit_19_memory), .out_3(and_36_out_3), .in_2(n4_16_decoder_v2_1_out_11));
  Memory_Bit memory_bit_20 (.Write(Input_1), .Input(and_7_out_3), .Memory(memory_bit_20_memory));
  AND and_37 (.in_1(memory_bit_20_memory), .out_3(and_37_out_3), .in_2(n4_16_decoder_v2_1_out_13));
  Memory_Bit memory_bit_21 (.Write(Input_1), .Input(and_8_out_3), .Memory(memory_bit_21_memory));
  AND and_38 (.in_1(memory_bit_21_memory), .out_3(and_38_out_3), .in_2(n4_16_decoder_v2_1_out_15));
  Memory_Bit memory_bit_22 (.Write(Input_1), .Input(and_9_out_3), .Memory(memory_bit_22_memory));
  AND and_39 (.in_1(memory_bit_22_memory), .out_3(and_39_out_3), .in_2(n4_16_decoder_v2_1_out_17));
  Memory_Bit memory_bit_23 (.Write(Input_1), .Input(and_15_out_3), .Memory(memory_bit_23_memory));
  AND and_40 (.in_1(memory_bit_23_memory), .out_3(and_40_out_3), .in_2(n4_16_decoder_v2_1_out_19));
  Memory_Bit memory_bit_24 (.Write(Input_1), .Input(and_10_out_3), .Memory(memory_bit_24_memory));
  AND and_41 (.in_1(memory_bit_24_memory), .out_3(and_41_out_3), .in_2(n4_16_decoder_v2_1_out_21));
  Memory_Bit memory_bit_25 (.Write(Input_1), .Input(and_3_out_3), .Memory(memory_bit_25_memory));
  AND and_42 (.in_1(memory_bit_25_memory), .out_3(and_42_out_3), .in_2(n4_16_decoder_v2_1_out_23));
  Memory_Bit memory_bit_26 (.Write(Input_1), .Input(and_11_out_3), .Memory(memory_bit_26_memory));
  AND and_43 (.in_1(memory_bit_26_memory), .out_3(and_43_out_3), .in_2(and_12_out_3));
  Memory_Bit memory_bit_27 (.Write(Input_1), .Input(and_4_out_3), .Memory(memory_bit_27_memory));
  AND and_44 (.in_1(memory_bit_27_memory), .out_3(and_44_out_3), .in_2(n4_16_decoder_v2_1_out_27));
  Memory_Bit memory_bit_28 (.Write(Input_1), .Input(and_5_out_3), .Memory(memory_bit_28_memory));
  AND and_45 (.in_1(memory_bit_28_memory), .out_3(and_45_out_3), .in_2(n4_16_decoder_v2_1_out_29));
  Memory_Bit memory_bit_29 (.Write(Input_1), .Input(and_13_out_3), .Memory(memory_bit_29_memory));
  AND and_46 (.in_1(memory_bit_29_memory), .out_3(and_46_out_3), .in_2(n4_16_decoder_v2_1_out_31));
  Memory_Bit memory_bit_30 (.Write(Input_1), .Input(and_16_out_3), .Memory(memory_bit_30_memory));
  AND and_47 (.in_1(memory_bit_30_memory), .out_3(and_47_out_3), .in_2(n4_16_decoder_v2_1_out_33));
  Memory_Bit memory_bit_31 (.Write(Input_1), .Input(and_17_out_3), .Memory(memory_bit_31_memory));
  AND and_48 (.in_1(memory_bit_31_memory), .out_3(and_48_out_3), .in_2(n4_16_decoder_v2_1_out_35));
  Memory_Bit memory_bit_32 (.Write(Input_1), .Input(and_14_out_3), .Memory(memory_bit_32_memory));
  AND and_49 (.in_1(memory_bit_32_memory), .out_3(and_49_out_3), .in_2(n4_16_decoder_v2_1_out_37));
  _16_bit_OR u_16_bit_or_2 (
    .Out(O1), .in_1(and_49_out_3), .in_2(and_48_out_3), .in_3(and_47_out_3), .in_4(and_46_out_3),
    .in_5(and_45_out_3), .in_6(and_44_out_3), .in_7(and_43_out_3), .in_8(and_42_out_3), .in_9(and_41_out_3),
    .in_10(and_40_out_3), .in_11(and_39_out_3), .in_12(and_38_out_3), .in_13(and_37_out_3),
    .in_14(and_36_out_3), .in_15(and_35_out_3), .in_16(and_34_out_3));
  Memory_Bit memory_bit_33 (.Write(Input_2), .Input(and_1_out_3), .Memory(memory_bit_33_memory));
  AND and_50 (.in_1(memory_bit_33_memory), .out_3(and_50_out_3), .in_2(n4_16_decoder_v2_1_out_7));
  Memory_Bit memory_bit_34 (.Write(Input_2), .Input(and_2_out_3), .Memory(n4_16_decoder_v2_1_out_9));
  AND and_51 (.in_1(n4_16_decoder_v2_1_out_9), .out_3(and_51_out_3), .in_2(n4_16_decoder_v2_1_out_9));
  Memory_Bit memory_bit_35 (.Write(Input_2), .Input(and_6_out_3), .Memory(memory_bit_35_memory));
  AND and_52 (.in_1(memory_bit_35_memory), .out_3(and_52_out_3), .in_2(n4_16_decoder_v2_1_out_11));
  Memory_Bit memory_bit_36 (.Write(Input_2), .Input(and_7_out_3), .Memory(memory_bit_36_memory));
  AND and_53 (.in_1(memory_bit_36_memory), .out_3(and_53_out_3), .in_2(n4_16_decoder_v2_1_out_13));
  Memory_Bit memory_bit_37 (.Write(Input_2), .Input(and_8_out_3), .Memory(memory_bit_37_memory));
  AND and_54 (.in_1(memory_bit_37_memory), .out_3(and_54_out_3), .in_2(n4_16_decoder_v2_1_out_15));
  Memory_Bit memory_bit_38 (.Write(Input_2), .Input(and_9_out_3), .Memory(memory_bit_38_memory));
  AND and_55 (.in_1(memory_bit_38_memory), .out_3(and_55_out_3), .in_2(n4_16_decoder_v2_1_out_17));
  Memory_Bit memory_bit_39 (.Write(Input_2), .Input(and_15_out_3), .Memory(memory_bit_39_memory));
  AND and_56 (.in_1(memory_bit_39_memory), .out_3(and_56_out_3), .in_2(n4_16_decoder_v2_1_out_19));
  Memory_Bit memory_bit_40 (.Write(Input_2), .Input(and_10_out_3), .Memory(memory_bit_40_memory));
  AND and_57 (.in_1(memory_bit_40_memory), .out_3(and_57_out_3), .in_2(n4_16_decoder_v2_1_out_21));
  Memory_Bit memory_bit_41 (.Write(Input_2), .Input(and_3_out_3), .Memory(memory_bit_41_memory));
  AND and_58 (.in_1(memory_bit_41_memory), .out_3(n4_16_decoder_v2_1_out_23), .in_2(n4_16_decoder_v2_1_out_23));
  Memory_Bit memory_bit_42 (.Write(Input_2), .Input(and_11_out_3), .Memory(memory_bit_42_memory));
  AND and_59 (.in_1(memory_bit_42_memory), .out_3(and_59_out_3), .in_2(and_12_out_3));
  Memory_Bit memory_bit_43 (.Write(Input_2), .Input(and_4_out_3), .Memory(memory_bit_43_memory));
  AND and_60 (.in_1(memory_bit_43_memory), .out_3(and_60_out_3), .in_2(n4_16_decoder_v2_1_out_27));
  Memory_Bit memory_bit_44 (.Write(Input_2), .Input(and_5_out_3), .Memory(memory_bit_44_memory));
  AND and_61 (.in_1(memory_bit_44_memory), .out_3(and_61_out_3), .in_2(n4_16_decoder_v2_1_out_29));
  Memory_Bit memory_bit_45 (.Write(Input_2), .Input(and_13_out_3), .Memory(memory_bit_45_memory));
  AND and_62 (.in_1(memory_bit_45_memory), .out_3(and_62_out_3), .in_2(n4_16_decoder_v2_1_out_31));
  Memory_Bit memory_bit_46 (.Write(Input_2), .Input(and_16_out_3), .Memory(memory_bit_46_memory));
  AND and_63 (.in_1(memory_bit_46_memory), .out_3(and_63_out_3), .in_2(n4_16_decoder_v2_1_out_33));
  Memory_Bit memory_bit_47 (.Write(Input_2), .Input(and_17_out_3), .Memory(memory_bit_47_memory));
  AND and_64 (.in_1(memory_bit_47_memory), .out_3(and_64_out_3), .in_2(n4_16_decoder_v2_1_out_35));
  Memory_Bit memory_bit_48 (.Write(Input_2), .Input(and_14_out_3), .Memory(memory_bit_48_memory));
  AND and_65 (.in_1(memory_bit_48_memory), .out_3(and_65_out_3), .in_2(n4_16_decoder_v2_1_out_37));
  _16_bit_OR u_16_bit_or_3 (
    .Out(O2), .in_1(and_65_out_3), .in_2(and_64_out_3), .in_3(and_63_out_3), .in_4(and_62_out_3),
    .in_5(and_61_out_3), .in_6(and_60_out_3), .in_7(and_59_out_3), .in_8(n4_16_decoder_v2_1_out_23),
    .in_9(and_57_out_3), .in_10(and_56_out_3), .in_11(and_55_out_3), .in_12(and_54_out_3),
    .in_13(and_53_out_3), .in_14(and_52_out_3), .in_15(and_51_out_3), .in_16(and_50_out_3));
  Memory_Bit memory_bit_49 (.Write(Input_3), .Input(and_1_out_3), .Memory(memory_bit_49_memory));
  AND and_66 (.in_1(memory_bit_49_memory), .out_3(and_66_out_3), .in_2(n4_16_decoder_v2_1_out_7));
  Memory_Bit memory_bit_50 (.Write(Input_3), .Input(and_2_out_3), .Memory(memory_bit_50_memory));
  AND and_67 (.in_1(memory_bit_50_memory), .out_3(and_67_out_3), .in_2(n4_16_decoder_v2_1_out_9));
  Memory_Bit memory_bit_51 (.Write(Input_3), .Input(and_6_out_3), .Memory(memory_bit_51_memory));
  AND and_68 (.in_1(memory_bit_51_memory), .out_3(and_68_out_3), .in_2(n4_16_decoder_v2_1_out_11));
  Memory_Bit memory_bit_52 (.Write(Input_3), .Input(and_7_out_3), .Memory(memory_bit_52_memory));
  AND and_69 (.in_1(memory_bit_52_memory), .out_3(and_69_out_3), .in_2(n4_16_decoder_v2_1_out_13));
  Memory_Bit memory_bit_53 (.Write(Input_3), .Input(and_8_out_3), .Memory(memory_bit_53_memory));
  AND and_70 (.in_1(memory_bit_53_memory), .out_3(and_70_out_3), .in_2(n4_16_decoder_v2_1_out_15));
  Memory_Bit memory_bit_54 (.Write(Input_3), .Input(and_9_out_3), .Memory(memory_bit_54_memory));
  AND and_71 (.in_1(memory_bit_54_memory), .out_3(and_71_out_3), .in_2(n4_16_decoder_v2_1_out_17));
  Memory_Bit memory_bit_55 (.Write(Input_3), .Input(and_15_out_3), .Memory(memory_bit_55_memory));
  AND and_72 (.in_1(memory_bit_55_memory), .out_3(and_72_out_3), .in_2(n4_16_decoder_v2_1_out_19));
  Memory_Bit memory_bit_56 (.Write(Input_3), .Input(and_10_out_3), .Memory(memory_bit_56_memory));
  AND and_73 (.in_1(memory_bit_56_memory), .out_3(and_73_out_3), .in_2(n4_16_decoder_v2_1_out_21));
  Memory_Bit memory_bit_57 (.Write(Input_3), .Input(and_3_out_3), .Memory(memory_bit_57_memory));
  AND and_74 (.in_1(memory_bit_57_memory), .out_3(n4_16_decoder_v2_1_out_23), .in_2(n4_16_decoder_v2_1_out_23));
  Memory_Bit memory_bit_58 (.Write(Input_3), .Input(and_11_out_3), .Memory(memory_bit_58_memory));
  AND and_75 (.in_1(memory_bit_58_memory), .out_3(and_75_out_3), .in_2(and_12_out_3));
  Memory_Bit memory_bit_59 (.Write(Input_3), .Input(and_4_out_3), .Memory(memory_bit_59_memory));
  AND and_76 (.in_1(memory_bit_59_memory), .out_3(and_76_out_3), .in_2(n4_16_decoder_v2_1_out_27));
  Memory_Bit memory_bit_60 (.Write(Input_3), .Input(and_5_out_3), .Memory(memory_bit_60_memory));
  AND and_77 (.in_1(memory_bit_60_memory), .out_3(and_77_out_3), .in_2(n4_16_decoder_v2_1_out_29));
  Memory_Bit memory_bit_61 (.Write(Input_3), .Input(and_13_out_3), .Memory(memory_bit_61_memory));
  AND and_78 (.in_1(memory_bit_61_memory), .out_3(and_78_out_3), .in_2(n4_16_decoder_v2_1_out_31));
  Memory_Bit memory_bit_62 (.Write(Input_3), .Input(and_16_out_3), .Memory(memory_bit_62_memory));
  AND and_79 (.in_1(memory_bit_62_memory), .out_3(and_79_out_3), .in_2(n4_16_decoder_v2_1_out_33));
  Memory_Bit memory_bit_63 (.Write(Input_3), .Input(and_17_out_3), .Memory(memory_bit_63_memory));
  AND and_80 (.in_1(memory_bit_63_memory), .out_3(and_80_out_3), .in_2(n4_16_decoder_v2_1_out_35));
  Memory_Bit memory_bit_64 (.Write(Input_3), .Input(and_14_out_3), .Memory(memory_bit_64_memory));
  AND and_81 (.in_1(memory_bit_64_memory), .out_3(and_81_out_3), .in_2(n4_16_decoder_v2_1_out_37));
  _16_bit_OR u_16_bit_or_4 (
    .Out(O3), .in_1(and_81_out_3), .in_2(and_80_out_3), .in_3(and_79_out_3), .in_4(and_78_out_3),
    .in_5(and_77_out_3), .in_6(and_76_out_3), .in_7(and_75_out_3), .in_8(n4_16_decoder_v2_1_out_23),
    .in_9(and_73_out_3), .in_10(and_72_out_3), .in_11(and_71_out_3), .in_12(and_70_out_3),
    .in_13(and_69_out_3), .in_14(and_68_out_3), .in_15(and_67_out_3), .in_16(and_66_out_3));
  Memory_Bit memory_bit_65 (.Write(Input_4), .Input(and_1_out_3), .Memory(memory_bit_65_memory));
  AND and_82 (.in_1(memory_bit_65_memory), .out_3(and_82_out_3), .in_2(n4_16_decoder_v2_1_out_7));
  Memory_Bit memory_bit_66 (.Write(Input_4), .Input(and_2_out_3), .Memory(memory_bit_66_memory));
  AND and_83 (.in_1(memory_bit_66_memory), .out_3(and_83_out_3), .in_2(n4_16_decoder_v2_1_out_9));
  Memory_Bit memory_bit_67 (.Write(Input_4), .Input(and_6_out_3), .Memory(memory_bit_67_memory));
  AND and_84 (.in_1(memory_bit_67_memory), .out_3(and_84_out_3), .in_2(n4_16_decoder_v2_1_out_11));
  Memory_Bit memory_bit_68 (.Write(Input_4), .Input(and_7_out_3), .Memory(memory_bit_68_memory));
  AND and_85 (.in_1(memory_bit_68_memory), .out_3(and_85_out_3), .in_2(n4_16_decoder_v2_1_out_13));
  Memory_Bit memory_bit_69 (.Write(Input_4), .Input(and_8_out_3), .Memory(memory_bit_69_memory));
  AND and_86 (.in_1(memory_bit_69_memory), .out_3(and_86_out_3), .in_2(n4_16_decoder_v2_1_out_15));
  Memory_Bit memory_bit_70 (.Write(Input_4), .Input(and_9_out_3), .Memory(memory_bit_70_memory));
  AND and_87 (.in_1(memory_bit_70_memory), .out_3(and_87_out_3), .in_2(n4_16_decoder_v2_1_out_17));
  Memory_Bit memory_bit_71 (.Write(Input_4), .Input(and_15_out_3), .Memory(memory_bit_71_memory));
  AND and_88 (.in_1(memory_bit_71_memory), .out_3(and_88_out_3), .in_2(n4_16_decoder_v2_1_out_19));
  Memory_Bit memory_bit_72 (.Write(Input_4), .Input(and_10_out_3), .Memory(memory_bit_72_memory));
  AND and_89 (.in_1(memory_bit_72_memory), .out_3(and_89_out_3), .in_2(n4_16_decoder_v2_1_out_21));
  Memory_Bit memory_bit_73 (.Write(Input_4), .Input(and_3_out_3), .Memory(memory_bit_73_memory));
  AND and_90 (.in_1(memory_bit_73_memory), .out_3(and_90_out_3), .in_2(n4_16_decoder_v2_1_out_23));
  Memory_Bit memory_bit_74 (.Write(Input_4), .Input(and_11_out_3), .Memory(memory_bit_74_memory));
  AND and_91 (.in_1(memory_bit_74_memory), .out_3(and_91_out_3), .in_2(and_12_out_3));
  Memory_Bit memory_bit_75 (.Write(Input_4), .Input(and_4_out_3), .Memory(memory_bit_75_memory));
  AND and_92 (.in_1(memory_bit_75_memory), .out_3(and_92_out_3), .in_2(n4_16_decoder_v2_1_out_27));
  Memory_Bit memory_bit_76 (.Write(Input_4), .Input(and_5_out_3), .Memory(memory_bit_76_memory));
  AND and_93 (.in_1(memory_bit_76_memory), .out_3(and_93_out_3), .in_2(n4_16_decoder_v2_1_out_29));
  Memory_Bit memory_bit_77 (.Write(Input_4), .Input(and_13_out_3), .Memory(memory_bit_77_memory));
  AND and_94 (.in_1(memory_bit_77_memory), .out_3(and_94_out_3), .in_2(n4_16_decoder_v2_1_out_31));
  Memory_Bit memory_bit_78 (.Write(Input_4), .Input(and_16_out_3), .Memory(memory_bit_78_memory));
  AND and_95 (.in_1(memory_bit_78_memory), .out_3(and_95_out_3), .in_2(n4_16_decoder_v2_1_out_33));
  Memory_Bit memory_bit_79 (.Write(Input_4), .Input(and_17_out_3), .Memory(memory_bit_79_memory));
  AND and_96 (.in_1(memory_bit_79_memory), .out_3(and_96_out_3), .in_2(n4_16_decoder_v2_1_out_35));
  Memory_Bit memory_bit_80 (.Write(Input_4), .Input(and_14_out_3), .Memory(memory_bit_80_memory));
  AND and_97 (.in_1(memory_bit_80_memory), .out_3(and_97_out_3), .in_2(n4_16_decoder_v2_1_out_37));
  _16_bit_OR u_16_bit_or_5 (
    .Out(O4), .in_1(and_97_out_3), .in_2(and_96_out_3), .in_3(and_95_out_3), .in_4(and_94_out_3),
    .in_5(and_93_out_3), .in_6(and_92_out_3), .in_7(and_91_out_3), .in_8(and_90_out_3), .in_9(and_89_out_3),
    .in_10(and_88_out_3), .in_11(and_87_out_3), .in_12(and_86_out_3), .in_13(and_85_out_3),
    .in_14(and_84_out_3), .in_15(and_83_out_3), .in_16(and_82_out_3));
  Memory_Bit memory_bit_81 (.Write(Input_5), .Input(and_1_out_3), .Memory(memory_bit_81_memory));
  AND and_98 (.in_1(memory_bit_81_memory), .out_3(and_98_out_3), .in_2(n4_16_decoder_v2_1_out_7));
  Memory_Bit memory_bit_82 (.Write(Input_5), .Input(and_2_out_3), .Memory(memory_bit_82_memory));
  AND and_99 (.in_1(memory_bit_82_memory), .out_3(and_99_out_3), .in_2(n4_16_decoder_v2_1_out_9));
  Memory_Bit memory_bit_83 (.Write(Input_5), .Input(and_6_out_3), .Memory(memory_bit_83_memory));
  AND and_100 (.in_1(memory_bit_83_memory), .out_3(and_100_out_3), .in_2(n4_16_decoder_v2_1_out_11));
  Memory_Bit memory_bit_84 (.Write(Input_5), .Input(and_7_out_3), .Memory(memory_bit_84_memory));
  AND and_101 (.in_1(memory_bit_84_memory), .out_3(and_101_out_3), .in_2(n4_16_decoder_v2_1_out_13));
  Memory_Bit memory_bit_85 (.Write(Input_5), .Input(and_8_out_3), .Memory(memory_bit_85_memory));
  AND and_102 (.in_1(memory_bit_85_memory), .out_3(and_102_out_3), .in_2(n4_16_decoder_v2_1_out_15));
  Memory_Bit memory_bit_86 (.Write(Input_5), .Input(and_9_out_3), .Memory(memory_bit_86_memory));
  AND and_103 (.in_1(memory_bit_86_memory), .out_3(and_103_out_3), .in_2(n4_16_decoder_v2_1_out_17));
  Memory_Bit memory_bit_87 (.Write(Input_5), .Input(and_15_out_3), .Memory(memory_bit_87_memory));
  AND and_104 (.in_1(memory_bit_87_memory), .out_3(and_104_out_3), .in_2(n4_16_decoder_v2_1_out_19));
  Memory_Bit memory_bit_88 (.Write(Input_5), .Input(and_10_out_3), .Memory(memory_bit_88_memory));
  AND and_105 (.in_1(memory_bit_88_memory), .out_3(and_105_out_3), .in_2(n4_16_decoder_v2_1_out_21));
  Memory_Bit memory_bit_89 (.Write(Input_5), .Input(and_3_out_3), .Memory(memory_bit_89_memory));
  AND and_106 (.in_1(memory_bit_89_memory), .out_3(and_106_out_3), .in_2(n4_16_decoder_v2_1_out_23));
  Memory_Bit memory_bit_90 (.Write(Input_5), .Input(and_11_out_3), .Memory(memory_bit_90_memory));
  AND and_107 (.in_1(memory_bit_90_memory), .out_3(and_107_out_3), .in_2(and_12_out_3));
  Memory_Bit memory_bit_91 (.Write(Input_5), .Input(and_4_out_3), .Memory(memory_bit_91_memory));
  AND and_108 (.in_1(memory_bit_91_memory), .out_3(and_108_out_3), .in_2(n4_16_decoder_v2_1_out_27));
  Memory_Bit memory_bit_92 (.Write(Input_5), .Input(and_5_out_3), .Memory(memory_bit_92_memory));
  AND and_109 (.in_1(memory_bit_92_memory), .out_3(and_109_out_3), .in_2(n4_16_decoder_v2_1_out_29));
  Memory_Bit memory_bit_93 (.Write(Input_5), .Input(and_13_out_3), .Memory(memory_bit_93_memory));
  AND and_110 (.in_1(memory_bit_93_memory), .out_3(and_110_out_3), .in_2(n4_16_decoder_v2_1_out_31));
  Memory_Bit memory_bit_94 (.Write(Input_5), .Input(and_16_out_3), .Memory(memory_bit_94_memory));
  AND and_111 (.in_1(memory_bit_94_memory), .out_3(and_111_out_3), .in_2(n4_16_decoder_v2_1_out_33));
  Memory_Bit memory_bit_95 (.Write(Input_5), .Input(and_17_out_3), .Memory(memory_bit_95_memory));
  AND and_112 (.in_1(memory_bit_95_memory), .out_3(and_112_out_3), .in_2(n4_16_decoder_v2_1_out_35));
  Memory_Bit memory_bit_96 (.Write(Input_5), .Input(and_14_out_3), .Memory(memory_bit_96_memory));
  AND and_113 (.in_1(memory_bit_96_memory), .out_3(and_113_out_3), .in_2(n4_16_decoder_v2_1_out_37));
  _16_bit_OR u_16_bit_or_6 (
    .Out(O5), .in_1(and_113_out_3), .in_2(and_112_out_3), .in_3(and_111_out_3), .in_4(and_110_out_3),
    .in_5(and_109_out_3), .in_6(and_108_out_3), .in_7(and_107_out_3), .in_8(and_106_out_3),
    .in_9(and_105_out_3), .in_10(and_104_out_3), .in_11(and_103_out_3), .in_12(and_102_out_3),
    .in_13(and_101_out_3), .in_14(and_100_out_3), .in_15(and_99_out_3), .in_16(and_98_out_3));
  Memory_Bit memory_bit_97 (.Write(Input_6), .Input(and_1_out_3), .Memory(memory_bit_97_memory));
  AND and_114 (.in_1(memory_bit_97_memory), .out_3(and_114_out_3), .in_2(n4_16_decoder_v2_1_out_7));
  Memory_Bit memory_bit_98 (.Write(Input_6), .Input(and_2_out_3), .Memory(memory_bit_98_memory));
  AND and_115 (.in_1(memory_bit_98_memory), .out_3(and_115_out_3), .in_2(n4_16_decoder_v2_1_out_9));
  Memory_Bit memory_bit_99 (.Write(Input_6), .Input(and_6_out_3), .Memory(memory_bit_99_memory));
  AND and_116 (.in_1(memory_bit_99_memory), .out_3(and_116_out_3), .in_2(n4_16_decoder_v2_1_out_11));
  Memory_Bit memory_bit_100 (.Write(Input_6), .Input(and_7_out_3), .Memory(memory_bit_100_memory));
  AND and_117 (.in_1(memory_bit_100_memory), .out_3(and_117_out_3), .in_2(n4_16_decoder_v2_1_out_13));
  Memory_Bit memory_bit_101 (.Write(Input_6), .Input(and_8_out_3), .Memory(memory_bit_101_memory));
  AND and_118 (.in_1(memory_bit_101_memory), .out_3(and_118_out_3), .in_2(n4_16_decoder_v2_1_out_15));
  Memory_Bit memory_bit_102 (.Write(Input_6), .Input(and_9_out_3), .Memory(memory_bit_102_memory));
  AND and_119 (.in_1(memory_bit_102_memory), .out_3(and_119_out_3), .in_2(n4_16_decoder_v2_1_out_17));
  Memory_Bit memory_bit_103 (.Write(Input_6), .Input(and_15_out_3), .Memory(memory_bit_103_memory));
  AND and_120 (.in_1(memory_bit_103_memory), .out_3(and_120_out_3), .in_2(n4_16_decoder_v2_1_out_19));
  Memory_Bit memory_bit_104 (.Write(Input_6), .Input(and_10_out_3), .Memory(memory_bit_104_memory));
  AND and_121 (.in_1(memory_bit_104_memory), .out_3(and_121_out_3), .in_2(n4_16_decoder_v2_1_out_21));
  Memory_Bit memory_bit_105 (.Write(Input_6), .Input(and_3_out_3), .Memory(memory_bit_105_memory));
  AND and_122 (.in_1(memory_bit_105_memory), .out_3(and_122_out_3), .in_2(n4_16_decoder_v2_1_out_23));
  Memory_Bit memory_bit_106 (.Write(Input_6), .Input(and_11_out_3), .Memory(memory_bit_106_memory));
  AND and_123 (.in_1(memory_bit_106_memory), .out_3(and_123_out_3), .in_2(and_12_out_3));
  Memory_Bit memory_bit_107 (.Write(Input_6), .Input(and_4_out_3), .Memory(memory_bit_107_memory));
  AND and_124 (.in_1(memory_bit_107_memory), .out_3(and_124_out_3), .in_2(n4_16_decoder_v2_1_out_27));
  Memory_Bit memory_bit_108 (.Write(Input_6), .Input(and_5_out_3), .Memory(memory_bit_108_memory));
  AND and_125 (.in_1(memory_bit_108_memory), .out_3(and_125_out_3), .in_2(n4_16_decoder_v2_1_out_29));
  Memory_Bit memory_bit_109 (.Write(Input_6), .Input(and_13_out_3), .Memory(memory_bit_109_memory));
  AND and_126 (.in_1(memory_bit_109_memory), .out_3(and_126_out_3), .in_2(n4_16_decoder_v2_1_out_31));
  Memory_Bit memory_bit_110 (.Write(Input_6), .Input(and_16_out_3), .Memory(memory_bit_110_memory));
  AND and_127 (.in_1(memory_bit_110_memory), .out_3(and_127_out_3), .in_2(n4_16_decoder_v2_1_out_33));
  Memory_Bit memory_bit_111 (.Write(Input_6), .Input(and_17_out_3), .Memory(memory_bit_111_memory));
  AND and_128 (.in_1(memory_bit_111_memory), .out_3(and_128_out_3), .in_2(n4_16_decoder_v2_1_out_35));
  Memory_Bit memory_bit_112 (.Write(Input_6), .Input(and_14_out_3), .Memory(memory_bit_112_memory));
  AND and_129 (.in_1(memory_bit_112_memory), .out_3(and_129_out_3), .in_2(n4_16_decoder_v2_1_out_37));
  _16_bit_OR u_16_bit_or_7 (
    .Out(O6), .in_1(and_129_out_3), .in_2(and_128_out_3), .in_3(and_127_out_3), .in_4(and_126_out_3),
    .in_5(and_125_out_3), .in_6(and_124_out_3), .in_7(and_123_out_3), .in_8(and_122_out_3),
    .in_9(and_121_out_3), .in_10(and_120_out_3), .in_11(and_119_out_3), .in_12(and_118_out_3),
    .in_13(and_117_out_3), .in_14(and_116_out_3), .in_15(and_115_out_3), .in_16(and_114_out_3));
  Memory_Bit memory_bit_113 (.Write(Input_7), .Input(and_1_out_3), .Memory(memory_bit_113_memory));
  AND and_130 (.in_1(memory_bit_113_memory), .out_3(and_130_out_3), .in_2(n4_16_decoder_v2_1_out_7));
  Memory_Bit memory_bit_114 (.Write(Input_7), .Input(and_2_out_3), .Memory(memory_bit_114_memory));
  AND and_131 (.in_1(memory_bit_114_memory), .out_3(and_131_out_3), .in_2(n4_16_decoder_v2_1_out_9));
  Memory_Bit memory_bit_115 (.Write(Input_7), .Input(and_6_out_3), .Memory(memory_bit_115_memory));
  AND and_132 (.in_1(memory_bit_115_memory), .out_3(and_132_out_3), .in_2(n4_16_decoder_v2_1_out_11));
  Memory_Bit memory_bit_116 (.Write(Input_7), .Input(and_7_out_3), .Memory(memory_bit_116_memory));
  AND and_133 (.in_1(memory_bit_116_memory), .out_3(and_133_out_3), .in_2(n4_16_decoder_v2_1_out_13));
  Memory_Bit memory_bit_117 (.Write(Input_7), .Input(and_8_out_3), .Memory(memory_bit_117_memory));
  AND and_134 (.in_1(memory_bit_117_memory), .out_3(and_134_out_3), .in_2(n4_16_decoder_v2_1_out_15));
  Memory_Bit memory_bit_118 (.Write(Input_7), .Input(and_9_out_3), .Memory(memory_bit_118_memory));
  AND and_135 (.in_1(memory_bit_118_memory), .out_3(and_135_out_3), .in_2(n4_16_decoder_v2_1_out_17));
  Memory_Bit memory_bit_119 (.Write(Input_7), .Input(and_15_out_3), .Memory(memory_bit_119_memory));
  AND and_136 (.in_1(memory_bit_119_memory), .out_3(and_136_out_3), .in_2(n4_16_decoder_v2_1_out_19));
  Memory_Bit memory_bit_120 (.Write(Input_7), .Input(and_10_out_3), .Memory(memory_bit_120_memory));
  AND and_137 (.in_1(memory_bit_120_memory), .out_3(and_137_out_3), .in_2(n4_16_decoder_v2_1_out_21));
  Memory_Bit memory_bit_121 (.Write(Input_7), .Input(and_3_out_3), .Memory(memory_bit_121_memory));
  AND and_138 (.in_1(memory_bit_121_memory), .out_3(and_138_out_3), .in_2(n4_16_decoder_v2_1_out_23));
  Memory_Bit memory_bit_122 (.Write(Input_7), .Input(and_11_out_3), .Memory(memory_bit_122_memory));
  AND and_139 (.in_1(memory_bit_122_memory), .out_3(and_139_out_3), .in_2(and_12_out_3));
  Memory_Bit memory_bit_123 (.Write(Input_7), .Input(and_4_out_3), .Memory(memory_bit_123_memory));
  AND and_140 (.in_1(memory_bit_123_memory), .out_3(and_140_out_3), .in_2(n4_16_decoder_v2_1_out_27));
  Memory_Bit memory_bit_124 (.Write(Input_7), .Input(and_5_out_3), .Memory(memory_bit_124_memory));
  AND and_141 (.in_1(memory_bit_124_memory), .out_3(and_141_out_3), .in_2(n4_16_decoder_v2_1_out_29));
  Memory_Bit memory_bit_125 (.Write(Input_7), .Input(and_13_out_3), .Memory(memory_bit_125_memory));
  AND and_142 (.in_1(memory_bit_125_memory), .out_3(and_142_out_3), .in_2(n4_16_decoder_v2_1_out_31));
  Memory_Bit memory_bit_126 (.Write(Input_7), .Input(and_16_out_3), .Memory(memory_bit_126_memory));
  AND and_143 (.in_1(memory_bit_126_memory), .out_3(and_143_out_3), .in_2(n4_16_decoder_v2_1_out_33));
  Memory_Bit memory_bit_127 (.Write(Input_7), .Input(and_17_out_3), .Memory(memory_bit_127_memory));
  AND and_144 (.in_1(memory_bit_127_memory), .out_3(and_144_out_3), .in_2(n4_16_decoder_v2_1_out_35));
  Memory_Bit memory_bit_128 (.Write(Input_7), .Input(and_14_out_3), .Memory(memory_bit_128_memory));
  AND and_145 (.in_1(memory_bit_128_memory), .out_3(and_145_out_3), .in_2(n4_16_decoder_v2_1_out_37));
  _16_bit_OR u_16_bit_or_8 (
    .Out(O7), .in_1(and_145_out_3), .in_2(and_144_out_3), .in_3(and_143_out_3), .in_4(and_142_out_3),
    .in_5(and_141_out_3), .in_6(and_140_out_3), .in_7(and_139_out_3), .in_8(and_138_out_3),
    .in_9(and_137_out_3), .in_10(and_136_out_3), .in_11(and_135_out_3), .in_12(and_134_out_3),
    .in_13(and_133_out_3), .in_14(and_132_out_3), .in_15(and_131_out_3), .in_16(and_130_out_3));
endmodule

module _4_bit_Register (
  input  in_1,
  input  in_2,
  input  in_3,
  input  in_4,
  input  in_5,
  output out_6,
  output out_7,
  output out_8,
  output out_9
);

  Memory_Bit memory_bit_1 (.Write(in_5), .Input(in_1), .Memory(out_6));
  Memory_Bit memory_bit_2 (.Write(in_5), .Input(in_2), .Memory(out_7));
  Memory_Bit memory_bit_3 (.Write(in_5), .Input(in_3), .Memory(out_8));
  Memory_Bit memory_bit_4 (.Write(in_5), .Input(in_4), .Memory(out_9));
endmodule

module _4_bit_Incrementer (
  input  in_1,
  input  in_2,
  input  in_3,
  input  in_4,
  output out_5,
  output out_6,
  output out_7,
  output out_8
);

  wire and_2_out_3, and_3_out_3, and_4_out_3;

  AND and_1 (.in_1(in_4), .in_2(and_2_out_3));  // open: out_3
  XOR xor_1 (.INPUT_1(in_4), .INPUT_2(and_2_out_3), .OUT(out_8));
  AND and_2 (.in_1(in_3), .out_3(and_2_out_3), .in_2(and_3_out_3));
  XOR xor_2 (.INPUT_1(in_2), .INPUT_2(and_4_out_3), .OUT(out_6));
  XOR xor_3 (.INPUT_1(in_3), .INPUT_2(and_3_out_3), .OUT(out_7));
  AND and_3 (.in_1(in_2), .out_3(and_3_out_3), .in_2(and_4_out_3));
  AND and_4 (.in_1(in_1), .out_3(and_4_out_3), .in_2(1'b1));
  XOR xor_4 (.INPUT_1(in_1), .INPUT_2(1'b1), .OUT(out_5));
endmodule

module _2_way_Bus_MUX (
  input  in_1,
  input  in_2,
  input  in_3,
  input  in_4,
  input  in_5,
  input  in_6,
  input  in_7,
  input  in_8,
  input  INCREMENT,
  input  LOAD,
  output out_11,
  output out_12,
  output out_13,
  output out_14
);

  wire and_1_out_3, and_2_out_3, and_3_out_3, and_4_out_3, and_5_out_3, and_6_out_3, and_7_out_3, and_8_out_3;

  AND and_1 (.in_1(in_5), .out_3(and_1_out_3), .in_2(LOAD));
  AND and_2 (.in_1(in_1), .out_3(and_2_out_3), .in_2(INCREMENT));
  XOR xor_1 (.INPUT_1(and_1_out_3), .INPUT_2(and_2_out_3), .OUT(out_11));
  AND and_3 (.in_1(in_2), .out_3(and_3_out_3), .in_2(INCREMENT));
  AND and_4 (.in_1(in_6), .out_3(and_4_out_3), .in_2(LOAD));
  XOR xor_2 (.INPUT_1(and_4_out_3), .INPUT_2(and_3_out_3), .OUT(out_12));
  AND and_5 (.in_1(in_3), .out_3(and_5_out_3), .in_2(INCREMENT));
  AND and_6 (.in_1(in_7), .out_3(and_6_out_3), .in_2(LOAD));
  XOR xor_3 (.INPUT_1(and_6_out_3), .INPUT_2(and_5_out_3), .OUT(out_13));
  AND and_7 (.in_1(in_4), .out_3(and_7_out_3), .in_2(INCREMENT));
  AND and_8 (.in_1(in_8), .out_3(and_8_out_3), .in_2(LOAD));
  XOR xor_4 (.INPUT_1(and_8_out_3), .INPUT_2(and_7_out_3), .OUT(out_14));
endmodule

// PC
module PC2 (
  input  in_1,
  input  in_2,
  input  in_3,
  input  in_4,
  input  INCREMENT,
  input  LOAD,
  input  WRITE,
  output out_8,
  output out_9,
  output out_10,
  output out_11
);

  wire n2_way_bus_mux_1_out_11, n2_way_bus_mux_1_out_12, n2_way_bus_mux_1_out_13, n2_way_bus_mux_1_out_14,
       n4_bit_incrementer_1_out_5, n4_bit_incrementer_1_out_6, n4_bit_incrementer_1_out_7,
       n4_bit_incrementer_1_out_8;

  _4_bit_Incrementer u_4_bit_incrementer_1 (
    .in_1(out_8), .in_2(out_9), .in_3(out_10), .in_4(out_11), .out_5(n4_bit_incrementer_1_out_5),
    .out_6(n4_bit_incrementer_1_out_6), .out_7(n4_bit_incrementer_1_out_7), .out_8(n4_bit_incrementer_1_out_8));
  _2_way_Bus_MUX u_2_way_bus_mux_1 (
    .in_1(n4_bit_incrementer_1_out_5), .in_2(n4_bit_incrementer_1_out_6), .in_3(n4_bit_incrementer_1_out_7),
    .in_4(n4_bit_incrementer_1_out_8), .in_5(in_1), .in_6(in_2), .in_7(in_3), .in_8(in_4),
    .INCREMENT(INCREMENT), .LOAD(LOAD), .out_11(n2_way_bus_mux_1_out_11), .out_12(n2_way_bus_mux_1_out_12),
    .out_13(n2_way_bus_mux_1_out_13), .out_14(n2_way_bus_mux_1_out_14));
  _4_bit_Register u_4_bit_register_1 (
    .in_5(WRITE), .in_1(n2_way_bus_mux_1_out_11), .in_2(n2_way_bus_mux_1_out_12),
    .in_3(n2_way_bus_mux_1_out_13), .in_4(n2_way_bus_mux_1_out_14), .out_6(out_8), .out_7(out_9),
    .out_8(out_10), .out_9(out_11));
endmodule

module Control_Unit (
  input  FETCH,
  input  FETCH_WRITE,
  input  EXECUTE,
  input  EXECUTE_WRITE,
  input  [2:0] OP,
  input  [7:0] R,
  output HALT,
  output ALU_ADD,
  output ALU_AND,
  output ALU_XOR,
  output MEMORY_WRITE,
  output PC_INCREMENT,
  output R_MUX_ALU,
  output PC_LOAD,
  output R_MUX_MEM,
  output PC_WRITE,
  output R_MUX_IR,
  output R_WRITE,
  output ADDER_MUX_PC,
  output IR_WRITE,
  output ADDER_MUX_IR
);

  wire and_7_out, and_8_out, and_11_out, and_12_out, and_13_out, and_14_out, and_15_out;

  or or_1 (R_MUX_ALU, ALU_ADD, ALU_AND, ALU_XOR);
  // AND_Gate and_1 has open pins: in0=EXECUTE, in1=OP[0], in2=OP[1], in3=OP[2], out=open
  and and_2 (ALU_ADD, EXECUTE, OP[0], ~OP[1], ~OP[2]);  // AND_Gate
  and and_3 (ALU_AND, EXECUTE, ~OP[0], OP[1], ~OP[2]);  // AND_Gate
  and and_4 (ALU_XOR, EXECUTE, OP[0], OP[1], ~OP[2]);  // AND_Gate
  and and_5 (R_MUX_IR, EXECUTE, ~OP[0], ~OP[1], OP[2]);  // AND_Gate
  and and_6 (R_MUX_MEM, EXECUTE, OP[0], ~OP[1], OP[2]);  // AND_Gate
  and and_7 (and_7_out, EXECUTE, ~OP[0], OP[1], OP[2]);  // AND_Gate
  and and_8 (and_8_out, EXECUTE, OP[0], OP[1], OP[2]);
  and and_9 (PC_LOAD, ~R[7], ~R[6], ~R[5], ~R[4], ~R[3], ~R[2], ~R[1], ~R[0], and_8_out);  // AND_Gate
  and and_10 (HALT, EXECUTE_WRITE, ~OP[0], ~OP[1], ~OP[2]);  // AND_Gate
  and and_11 (and_11_out, EXECUTE_WRITE, OP[0], ~OP[1], ~OP[2]);  // AND_Gate
  and and_12 (and_12_out, EXECUTE_WRITE, ~OP[0], OP[1], ~OP[2]);  // AND_Gate
  and and_13 (and_13_out, EXECUTE_WRITE, OP[0], OP[1], ~OP[2]);  // AND_Gate
  and and_14 (and_14_out, EXECUTE_WRITE, ~OP[0], ~OP[1], OP[2]);  // AND_Gate
  and and_15 (and_15_out, EXECUTE_WRITE, OP[0], ~OP[1], OP[2]);  // AND_Gate
  and and_16 (MEMORY_WRITE, EXECUTE_WRITE, ~OP[0], OP[1], OP[2]);  // AND_Gate
  // AND_Gate and_17 has open pins: in0=EXECUTE_WRITE, in1=OP[0], in2=OP[1], in3=OP[2], out=open
  or or_2 (R_WRITE, and_15_out, and_14_out, and_13_out, and_12_out, and_11_out);
  or or_3 (ADDER_MUX_IR, and_7_out, R_MUX_ALU, R_MUX_MEM);
  NOT not_1 (.Q(PC_INCREMENT), .X(PC_LOAD));

  assign ADDER_MUX_PC = FETCH;
  assign IR_WRITE = FETCH_WRITE;
  assign PC_WRITE = EXECUTE_WRITE;
endmodule

module _9bit_NOR (
  input  a,
  input  b,
  input  c,
  input  d,
  input  e,
  input  f,
  input  g,
  input  h,
  input  i,
  output x
);

  wire not_1_q, not_2_q, not_3_q, not_4_q, not_5_q, not_6_q, not_7_q, not_8_q, not_9_q;

  NOT not_1 (.Q(not_1_q), .X(a));
  NOT not_2 (.Q(not_2_q), .X(b));
  NOT not_3 (.Q(not_3_q), .X(c));
  NOT not_4 (.Q(not_4_q), .X(d));
  NOT not_5 (.Q(not_5_q), .X(e));
  NOT not_6 (.Q(not_6_q), .X(f));
  NOT not_7 (.Q(not_7_q), .X(g));
  NOT not_8 (.Q(not_8_q), .X(h));
  NOT not_9 (.Q(not_9_q), .X(i));
  _9bit_AND u_9bit_and_1 (
    .in_1(not_9_q), .in_2(not_8_q), .in_3(not_7_q), .in_4(not_6_q), .in_5(not_5_q), .in_6(not_4_q),
    .in_7(not_3_q), .in_8(not_2_q), .in_9(not_1_q), .out_10(x));
endmodule

// 9-bit AND
module _9bit_AND (
  input  in_1,
  input  in_2,
  input  in_3,
  input  in_4,
  input  in_5,
  input  in_6,
  input  in_7,
  input  in_8,
  input  in_9,
  output out_10
);

  wire and_1_out_3, and_3_out_3, and_4_out_3, and_5_out_3, and_6_out_3, and_7_out_3, and_8_out_3;

  AND and_1 (.in_1(and_6_out_3), .out_3(and_1_out_3), .in_2(in_2));
  AND and_2 (.in_1(and_1_out_3), .out_3(out_10), .in_2(in_1));
  AND and_3 (.in_1(and_8_out_3), .out_3(and_3_out_3), .in_2(in_6));
  AND and_4 (.in_1(and_3_out_3), .out_3(and_4_out_3), .in_2(in_5));
  AND and_5 (.in_1(and_4_out_3), .out_3(and_5_out_3), .in_2(in_4));
  AND and_6 (.in_1(and_5_out_3), .out_3(and_6_out_3), .in_2(in_3));
  AND and_7 (.in_1(in_9), .out_3(and_7_out_3), .in_2(in_8));
  AND and_8 (.in_1(and_7_out_3), .out_3(and_8_out_3), .in_2(in_7));
endmodule

module _4bit_NOR (
  input  in_1,
  input  in_2,
  input  in_3,
  input  in_4,
  output out_5
);

  wire transistor_1_out, transistor_2_out, transistor_3_out;

  Transistor transistor_1 (.in(1'b1), .out(transistor_1_out), .gate(in_1));
  Pull_Resistor pull_resistor_1 (.node(transistor_1_out));
  Transistor transistor_2 (.in(transistor_1_out), .out(transistor_2_out), .gate(in_2));
  Pull_Resistor pull_resistor_2 (.node(transistor_2_out));
  Transistor transistor_3 (.in(transistor_2_out), .out(transistor_3_out), .gate(in_3));
  Pull_Resistor pull_resistor_3 (.node(transistor_3_out));
  Transistor transistor_4 (.in(transistor_3_out), .out(out_5), .gate(in_4));
  Pull_Resistor pull_resistor_4 (.node(out_5));
endmodule

module _5bit_OR (
  input  in_1,
  input  in_2,
  input  in_3,
  input  in_4,
  input  in_5,
  output out_6
);

  wire or_1_out_3, or_2_out_3, or_3_out_3;

  OR or_1 (.in_1(in_4), .in_2(in_5), .out_3(or_1_out_3));
  OR or_2 (.in_1(in_1), .in_2(in_2), .out_3(or_2_out_3));
  OR or_3 (.in_1(or_2_out_3), .in_2(in_3), .out_3(or_3_out_3));
  OR or_4 (.in_1(or_3_out_3), .in_2(or_1_out_3), .out_3(out_6));
endmodule

module _4bit_AND (
  input  in_1,
  input  in_2,
  input  in_3,
  input  in_4,
  output out_5
);

  wire transistor_1_out, transistor_2_out, transistor_3_out;

  Pull_Resistor pull_resistor_1 (.node(in_1));
  Pull_Resistor pull_resistor_2 (.node(in_2));
  Pull_Resistor pull_resistor_3 (.node(in_3));
  Pull_Resistor pull_resistor_4 (.node(in_4));
  Transistor #(.\type ("n")) transistor_1 (.in(1'b1), .out(transistor_1_out), .gate(in_1));
  Transistor #(.\type ("n")) transistor_2 (.in(transistor_1_out), .out(transistor_2_out), .gate(in_2));
  Transistor #(.\type ("n")) transistor_3 (.in(transistor_2_out), .out(transistor_3_out), .gate(in_3));
  Transistor #(.\type ("n")) transistor_4 (.in(transistor_3_out), .out(out_5), .gate(in_4));
  Pull_Resistor pull_resistor_5 (.node(out_5));
endmodule

module _4b_decider (
  input  Selection,
  input  [3:0] A,
  input  [3:0] B,
  output [3:0] out_4
);

  wire not_1_q;
  wire [3:0] n5_bit_and_1_out, n5_bit_and_2_out;

  _5_bit_AND u_5_bit_and_1 (.Selection(Selection), .A(A), .Out(n5_bit_and_1_out));
  NOT not_1 (.Q(not_1_q));  // open: X
  _5_bit_AND u_5_bit_and_2 (.Selection(not_1_q), .A(B), .Out(n5_bit_and_2_out));
  _4_bit_OR u_4_bit_or_1 (.in_1(n5_bit_and_1_out), .in_2(n5_bit_and_2_out), .out_3(out_4));
endmodule

module _3bit_OR (
  input  in_1,
  input  in_2,
  input  in_3,
  output out_4
);

  wire or_1_out_3;

  OR or_1 (.in_1(in_1), .in_2(in_2), .out_3(or_1_out_3));
  OR or_2 (.in_1(or_1_out_3), .in_2(in_3), .out_3(out_4));
endmodule

// R
module _8R (
  input  in_1,
  input  in_2,
  input  in_3,
  input  in_4,
  input  in_5,
  input  in_6,
  input  in_7,
  input  in_8,
  input  R_WRITE,
  output [7:0] out_10
);

  Memory_Bit memory_bit_1 (.Write(R_WRITE), .Input(in_1), .Memory(out_10[0]));
  Memory_Bit memory_bit_2 (.Write(R_WRITE), .Input(in_2), .Memory(out_10[1]));
  Memory_Bit memory_bit_3 (.Write(R_WRITE), .Input(in_3), .Memory(out_10[2]));
  Memory_Bit memory_bit_4 (.Write(R_WRITE), .Input(in_4), .Memory(out_10[3]));
  Memory_Bit memory_bit_5 (.Write(R_WRITE), .Input(in_5), .Memory(out_10[4]));
  Memory_Bit memory_bit_6 (.Write(R_WRITE), .Input(in_6), .Memory(out_10[5]));
  Memory_Bit memory_bit_7 (.Write(R_WRITE), .Input(in_7), .Memory(out_10[6]));
  Memory_Bit memory_bit_8 (.Write(R_WRITE), .Input(in_8), .Memory(out_10[7]));
endmodule

module IR (
  input  in_1,
  input  in_2,
  input  in_3,
  input  in_4,
  input  in_5,
  input  in_6,
  input  in_7,
  input  in_8,
  input  IR_WRITE,
  output out_10,
  output out_11,
  output out_12,
  output out_13,
  output out_14,
  output out_15,
  output out_16,
  output out_17
);

  Memory_Bit memory_bit_1 (.Write(IR_WRITE), .Input(in_1), .Memory(out_10));
  Memory_Bit memory_bit_2 (.Write(IR_WRITE), .Input(in_2), .Memory(out_11));
  Memory_Bit memory_bit_3 (.Write(IR_WRITE), .Input(in_3), .Memory(out_12));
  Memory_Bit memory_bit_4 (.Write(IR_WRITE), .Input(in_4), .Memory(out_13));
  Memory_Bit memory_bit_5 (.Write(IR_WRITE), .Input(in_5), .Memory(out_14));
  Memory_Bit memory_bit_6 (.Write(IR_WRITE), .Input(in_6), .Memory(out_15));
  Memory_Bit memory_bit_7 (.Write(IR_WRITE), .Input(in_7), .Memory(out_16));
  Memory_Bit memory_bit_8 (.Write(IR_WRITE), .Input(in_8), .Memory(out_17));
endmodule

// 2-way addr MUX
module addr_MUX_2_way (
  input  in_1,
  input  in_2,
  input  in_3,
  input  in_4,
  input  in_5,
  input  in_6,
  input  in_7,
  input  in_8,
  input  ADDR_MUX_PC,
  input  ADDR_MUX_IR,
  output out_11,
  output out_12,
  output out_13,
  output out_14
);

  wire and_1_out_3, and_2_out_3, and_3_out_3, and_4_out_3, and_5_out_3, and_6_out_3, and_7_out_3, and_8_out_3;

  AND and_1 (.in_1(ADDR_MUX_PC), .out_3(and_1_out_3), .in_2(in_1));
  AND and_2 (.in_1(ADDR_MUX_IR), .out_3(and_2_out_3), .in_2(in_5));
  OR or_1 (.in_1(and_1_out_3), .in_2(and_2_out_3), .out_3(out_11));
  AND and_3 (.in_1(ADDR_MUX_PC), .out_3(and_3_out_3), .in_2(in_2));
  AND and_4 (.in_1(ADDR_MUX_IR), .out_3(and_4_out_3), .in_2(in_6));
  OR or_2 (.in_1(and_3_out_3), .in_2(and_4_out_3), .out_3(out_12));
  AND and_5 (.in_1(ADDR_MUX_PC), .out_3(and_5_out_3), .in_2(in_3));
  AND and_6 (.in_1(ADDR_MUX_IR), .out_3(and_6_out_3), .in_2(in_7));
  OR or_3 (.in_1(and_5_out_3), .in_2(and_6_out_3), .out_3(out_13));
  AND and_7 (.in_1(ADDR_MUX_PC), .out_3(and_7_out_3), .in_2(in_4));
  AND and_8 (.in_1(ADDR_MUX_IR), .out_3(and_8_out_3), .in_2(in_8));
  OR or_4 (.in_1(and_7_out_3), .in_2(and_8_out_3), .out_3(out_14));
endmodule

module decider_OR (
  input  [7:0] A,
  input  [7:0] B,
  output [7:0] O
);

  OR or_1 (.in_1(B[7]), .in_2(A[7]), .out_3(O[7]));
  OR or_2 (.in_1(B[6]), .in_2(A[6]), .out_3(O[6]));
  OR or_3 (.in_1(B[5]), .in_2(A[5]), .out_3(O[5]));
  OR or_4 (.in_1(B[3]), .in_2(A[3]), .out_3(O[3]));
  OR or_5 (.in_1(B[4]), .in_2(A[4]), .out_3(O[4]));
  OR or_6 (.in_1(B[1]), .in_2(A[1]), .out_3(O[1]));
  OR or_7 (.in_1(B[2]), .in_2(A[2]), .out_3(O[2]));
  OR or_8 (.in_1(B[0]), .in_2(A[0]), .out_3(O[0]));
endmodule

// 3-way R MUX
module _3_way_r_mux (
  input  in_1,
  input  in_2,
  input  in_3,
  input  in_4,
  input  in_5,
  input  in_6,
  input  in_7,
  input  in_8,
  input  in_9,
  input  in_10,
  input  in_11,
  input  in_12,
  input  in_13,
  input  in_14,
  input  in_15,
  input  in_16,
  input  in_17,
  input  in_18,
  input  in_19,
  input  in_20,
  input  R_MUX_ALU,
  input  R_MUX_MEM,
  input  R_MUX_IR,
  output out_24,
  output out_25,
  output out_26,
  output out_27,
  output out_28,
  output out_29,
  output out_30,
  output out_31
);

  wire and_1_out_3, and_2_out_3, and_3_out_3, and_4_out_3, and_5_out_3, and_6_out_3, and_7_out_3,
       and_8_out_3, and_9_out_3, and_10_out_3, and_11_out_3, and_12_out_3, and_13_out_3, and_14_out_3,
       and_15_out_3, and_16_out_3, and_17_out_3, and_18_out_3, and_19_out_3, and_20_out_3, and_21_out_3,
       and_22_out_3, and_23_out_3, and_24_out_3;

  AND and_1 (.in_1(R_MUX_ALU), .out_3(and_1_out_3), .in_2(in_1));
  AND and_2 (.in_1(R_MUX_MEM), .out_3(and_2_out_3), .in_2(in_9));
  AND and_3 (.in_1(R_MUX_IR), .out_3(and_3_out_3), .in_2(in_17));
  AND and_4 (.in_1(R_MUX_ALU), .out_3(and_4_out_3), .in_2(in_2));
  AND and_5 (.in_1(R_MUX_MEM), .out_3(and_5_out_3), .in_2(in_10));
  AND and_6 (.in_1(R_MUX_IR), .out_3(and_6_out_3), .in_2(in_18));
  _3bit_OR u_3bit_or_1 (.in_1(and_1_out_3), .in_2(and_2_out_3), .in_3(and_3_out_3), .out_4(out_24));
  AND and_7 (.in_1(R_MUX_ALU), .out_3(and_7_out_3), .in_2(in_3));
  AND and_8 (.in_1(R_MUX_MEM), .out_3(and_8_out_3), .in_2(in_11));
  AND and_9 (.in_1(R_MUX_IR), .out_3(and_9_out_3), .in_2(in_19));
  _3bit_OR u_3bit_or_2 (.in_1(and_4_out_3), .in_2(and_5_out_3), .in_3(and_6_out_3), .out_4(out_25));
  _3bit_OR u_3bit_or_3 (.in_1(and_7_out_3), .in_2(and_8_out_3), .in_3(and_9_out_3), .out_4(out_26));
  AND and_10 (.in_1(R_MUX_ALU), .out_3(and_10_out_3), .in_2(in_4));
  AND and_11 (.in_1(R_MUX_MEM), .out_3(and_11_out_3), .in_2(in_12));
  AND and_12 (.in_1(R_MUX_IR), .out_3(and_12_out_3), .in_2(in_20));
  _3bit_OR u_3bit_or_4 (.in_1(and_10_out_3), .in_2(and_11_out_3), .in_3(and_12_out_3), .out_4(out_27));
  AND and_13 (.in_1(R_MUX_ALU), .out_3(and_13_out_3), .in_2(in_5));
  AND and_14 (.in_1(R_MUX_MEM), .out_3(and_14_out_3), .in_2(in_13));
  AND and_15 (.in_1(R_MUX_IR), .out_3(and_15_out_3), .in_2(1'b0));
  _3bit_OR u_3bit_or_5 (.in_1(and_13_out_3), .in_2(and_14_out_3), .in_3(and_15_out_3), .out_4(out_28));
  AND and_16 (.in_1(R_MUX_ALU), .out_3(and_16_out_3), .in_2(in_6));
  AND and_17 (.in_1(R_MUX_MEM), .out_3(and_17_out_3), .in_2(in_14));
  AND and_18 (.in_1(R_MUX_IR), .out_3(and_18_out_3), .in_2(1'b0));
  _3bit_OR u_3bit_or_6 (.in_1(and_16_out_3), .in_2(and_17_out_3), .in_3(and_18_out_3), .out_4(out_29));
  AND and_19 (.in_1(R_MUX_ALU), .out_3(and_19_out_3), .in_2(in_7));
  AND and_20 (.in_1(R_MUX_MEM), .out_3(and_20_out_3), .in_2(in_15));
  AND and_21 (.in_1(R_MUX_IR), .out_3(and_21_out_3), .in_2(1'b0));
  _3bit_OR u_3bit_or_7 (.in_1(and_19_out_3), .in_2(and_20_out_3), .in_3(and_21_out_3), .out_4(out_30));
  AND and_22 (.in_1(R_MUX_ALU), .out_3(and_22_out_3), .in_2(in_8));
  AND and_23 (.in_1(R_MUX_MEM), .out_3(and_23_out_3), .in_2(in_16));
  AND and_24 (.in_1(R_MUX_IR), .out_3(and_24_out_3), .in_2(1'b0));
  _3bit_OR u_3bit_or_8 (.in_1(and_22_out_3), .in_2(and_23_out_3), .in_3(and_24_out_3), .out_4(out_31));
endmodule

module decider (
  input  in_1,
  input  [7:0] in_2,
  input  [7:0] in_3,
  output [7:0] out_4
);

  wire not_1_q;
  wire [7:0] n9_bit_and_1_out_3, n9_bit_and_2_out_3;

  _9_bit_AND u_9_bit_and_1 (.O(in_2), .in_2(in_1), .out_3(n9_bit_and_1_out_3));
  NOT not_1 (.Q(not_1_q));  // open: X
  _9_bit_AND u_9_bit_and_2 (.O(in_3), .in_2(not_1_q), .out_3(n9_bit_and_2_out_3));
  decider_OR decider_or_1 (.A(n9_bit_and_1_out_3), .B(n9_bit_and_2_out_3), .O(out_4));
endmodule

module _5_bit_AND (
  input  Selection,
  input  [3:0] A,
  output [3:0] Out
);

  AND and_1 (.in_1(A[3]), .out_3(Out[3]), .in_2(Selection));
  AND and_2 (.in_1(A[1]), .out_3(Out[1]), .in_2(Selection));
  AND and_3 (.in_1(A[2]), .out_3(Out[2]), .in_2(Selection));
  AND and_4 (.in_1(A[0]), .out_3(Out[0]), .in_2(Selection));
endmodule

module _4_bit_OR (
  input  [3:0] in_1,
  input  [3:0] in_2,
  output [3:0] out_3
);

  XOR xor_1 (.INPUT_1(in_2[3]), .INPUT_2(in_1[3]), .OUT(out_3[3]));
  XOR xor_2 (.INPUT_1(in_2[2]), .INPUT_2(in_1[2]), .OUT(out_3[2]));
  XOR xor_3 (.INPUT_1(in_2[1]), .INPUT_2(in_1[1]), .OUT(out_3[1]));
  XOR xor_4 (.INPUT_1(in_2[0]), .INPUT_2(in_1[0]), .OUT(out_3[0]));
endmodule

// DEMUX
module Demux_4_16 (
  input  [3:0] I,
  input  E,
  output out_3,
  output out_4,
  output out_5,
  output out_6,
  output out_7,
  output out_8,
  output out_9,
  output out_10,
  output out_11,
  output out_12,
  output out_13,
  output out_14,
  output out_15,
  output out_16,
  output out_17,
  output out_18
);

  wire n4_bit_and_1_out_5, n4_bit_and_2_out_5, n4_bit_and_3_out_5, n4_bit_and_4_out_5, n4_bit_and_5_out_5,
       n4_bit_and_6_out_5, n4_bit_and_7_out_5, n4_bit_and_8_out_5, n4_bit_and_9_out_5, n4_bit_and_10_out_5,
       n4_bit_and_11_out_5, n4_bit_and_12_out_5, n4_bit_and_13_out_5, n4_bit_and_14_out_5,
       n4_bit_and_15_out_5, n4_bit_and_16_out_5, not_1_q, not_2_q, not_3_q, not_4_q, not_5_q, not_6_q,
       not_7_q, not_8_q, not_9_q, not_10_q, not_11_q, not_12_q, not_13_q, not_14_q, not_15_q, not_16_q,
       not_17_q, not_18_q, not_19_q, not_20_q, not_21_q, not_22_q, not_23_q, not_24_q, not_25_q, not_26_q,
       not_27_q, not_28_q, not_29_q, not_30_q, not_31_q, not_32_q;

  NOT not_1 (.Q(not_1_q), .X(I[0]));
  NOT not_2 (.Q(not_2_q), .X(I[1]));
  NOT not_3 (.Q(not_3_q), .X(I[2]));
  NOT not_4 (.Q(not_4_q), .X(I[3]));
  NOT not_5 (.Q(not_5_q), .X(I[1]));
  NOT not_6 (.Q(not_6_q), .X(I[2]));
  NOT not_7 (.Q(not_7_q), .X(I[3]));
  NOT not_8 (.Q(not_8_q), .X(I[0]));
  NOT not_9 (.Q(not_9_q), .X(I[2]));
  NOT not_10 (.Q(not_10_q), .X(I[3]));
  NOT not_11 (.Q(not_11_q), .X(I[2]));
  NOT not_12 (.Q(not_12_q), .X(I[3]));
  NOT not_13 (.Q(not_13_q), .X(I[0]));
  NOT not_14 (.Q(not_14_q), .X(I[1]));
  NOT not_15 (.Q(not_15_q), .X(I[3]));
  NOT not_16 (.Q(not_16_q), .X(I[1]));
  NOT not_17 (.Q(not_17_q), .X(I[3]));
  NOT not_18 (.Q(not_18_q), .X(I[0]));
  NOT not_19 (.Q(not_19_q), .X(I[3]));
  NOT not_20 (.Q(not_20_q), .X(I[3]));
  NOT not_21 (.Q(not_21_q), .X(I[0]));
  NOT not_22 (.Q(not_22_q), .X(I[1]));
  NOT not_23 (.Q(not_23_q), .X(I[2]));
  NOT not_24 (.Q(not_24_q), .X(I[1]));
  NOT not_25 (.Q(not_25_q), .X(I[2]));
  NOT not_26 (.Q(not_26_q), .X(I[0]));
  NOT not_27 (.Q(not_27_q), .X(I[2]));
  NOT not_28 (.Q(not_28_q), .X(I[2]));
  NOT not_29 (.Q(not_29_q), .X(I[0]));
  NOT not_30 (.Q(not_30_q), .X(I[1]));
  NOT not_31 (.Q(not_31_q), .X(I[1]));
  NOT not_32 (.Q(not_32_q), .X(I[0]));
  AND and_1 (.in_1(n4_bit_and_1_out_5), .out_3(out_3), .in_2(E));
  _4_bit_AND u_4_bit_and_1 (.in_1(not_1_q), .in_2(not_2_q), .in_3(not_3_q), .in_4(not_4_q), .out_5(n4_bit_and_1_out_5));
  AND and_2 (.in_1(n4_bit_and_2_out_5), .out_3(out_4), .in_2(E));
  _4_bit_AND u_4_bit_and_2 (.in_1(I[0]), .in_2(not_5_q), .in_3(not_6_q), .in_4(not_7_q), .out_5(n4_bit_and_2_out_5));
  _4_bit_AND u_4_bit_and_3 (.in_1(not_8_q), .in_2(I[1]), .in_3(not_9_q), .in_4(not_10_q), .out_5(n4_bit_and_3_out_5));
  AND and_3 (.in_1(n4_bit_and_3_out_5), .out_3(out_5), .in_2(E));
  AND and_4 (.in_1(n4_bit_and_4_out_5), .out_3(out_6), .in_2(E));
  _4_bit_AND u_4_bit_and_4 (.in_1(I[0]), .in_2(I[1]), .in_3(not_11_q), .in_4(not_12_q), .out_5(n4_bit_and_4_out_5));
  _4_bit_AND u_4_bit_and_5 (.in_1(not_13_q), .in_2(not_14_q), .in_3(I[2]), .in_4(not_15_q), .out_5(n4_bit_and_5_out_5));
  AND and_5 (.in_1(n4_bit_and_5_out_5), .out_3(out_7), .in_2(E));
  _4_bit_AND u_4_bit_and_6 (.in_1(I[0]), .in_2(not_16_q), .in_3(I[2]), .in_4(not_17_q), .out_5(n4_bit_and_6_out_5));
  AND and_6 (.in_1(n4_bit_and_6_out_5), .out_3(out_8), .in_2(E));
  AND and_7 (.in_1(n4_bit_and_7_out_5), .out_3(out_9), .in_2(E));
  _4_bit_AND u_4_bit_and_7 (.in_1(not_18_q), .in_2(I[1]), .in_3(I[2]), .in_4(not_19_q), .out_5(n4_bit_and_7_out_5));
  AND and_8 (.in_1(n4_bit_and_8_out_5), .out_3(out_10), .in_2(E));
  _4_bit_AND u_4_bit_and_8 (.in_1(I[0]), .in_2(I[1]), .in_3(I[2]), .in_4(not_20_q), .out_5(n4_bit_and_8_out_5));
  AND and_9 (.in_1(n4_bit_and_9_out_5), .out_3(out_11), .in_2(E));
  _4_bit_AND u_4_bit_and_9 (.in_1(not_21_q), .in_2(not_22_q), .in_3(not_23_q), .in_4(I[3]), .out_5(n4_bit_and_9_out_5));
  AND and_10 (.in_1(n4_bit_and_10_out_5), .out_3(out_12), .in_2(E));
  _4_bit_AND u_4_bit_and_10 (.in_1(I[0]), .in_2(not_24_q), .in_3(not_25_q), .in_4(I[3]), .out_5(n4_bit_and_10_out_5));
  AND and_11 (.in_1(n4_bit_and_11_out_5), .out_3(out_13), .in_2(E));
  _4_bit_AND u_4_bit_and_11 (.in_1(not_26_q), .in_2(I[1]), .in_3(not_27_q), .in_4(I[3]), .out_5(n4_bit_and_11_out_5));
  AND and_12 (.in_1(n4_bit_and_12_out_5), .out_3(out_14), .in_2(E));
  _4_bit_AND u_4_bit_and_12 (.in_1(I[0]), .in_2(I[1]), .in_3(not_28_q), .in_4(I[3]), .out_5(n4_bit_and_12_out_5));
  _4_bit_AND u_4_bit_and_13 (.in_1(not_29_q), .in_2(not_30_q), .in_3(I[2]), .in_4(I[3]), .out_5(n4_bit_and_13_out_5));
  AND and_13 (.in_1(n4_bit_and_13_out_5), .out_3(out_15), .in_2(E));
  _4_bit_AND u_4_bit_and_14 (.in_1(I[0]), .in_2(not_31_q), .in_3(I[2]), .in_4(I[3]), .out_5(n4_bit_and_14_out_5));
  AND and_14 (.in_1(n4_bit_and_14_out_5), .out_3(out_16), .in_2(E));
  AND and_15 (.in_1(n4_bit_and_15_out_5), .out_3(out_17), .in_2(E));
  _4_bit_AND u_4_bit_and_15 (.in_1(not_32_q), .in_2(I[1]), .in_3(I[2]), .in_4(I[3]), .out_5(n4_bit_and_15_out_5));
  _4_bit_AND u_4_bit_and_16 (.in_1(I[0]), .in_2(I[1]), .in_3(I[2]), .in_4(I[3]), .out_5(n4_bit_and_16_out_5));
  AND and_16 (.in_1(n4_bit_and_16_out_5), .out_3(out_18), .in_2(E));
endmodule

// DECODER
module Decoder_4_16 (
  input  [3:0] in_1,
  output out_2,
  output out_3,
  output out_4,
  output out_5,
  output out_6,
  output out_7,
  output out_8,
  output out_9,
  output out_10,
  output out_11,
  output out_12,
  output out_13,
  output out_14,
  output out_15,
  output out_16,
  output out_17
);

  wire not_1_q, not_2_q, not_3_q, not_4_q, not_5_q, not_6_q, not_7_q, not_8_q, not_9_q, not_10_q, not_11_q,
       not_12_q, not_13_q, not_14_q, not_15_q, not_16_q, not_17_q, not_18_q, not_19_q, not_20_q, not_21_q,
       not_22_q, not_23_q, not_24_q, not_25_q, not_26_q, not_27_q, not_28_q, not_29_q, not_30_q, not_31_q,
       not_32_q;

  NOT not_1 (.Q(not_1_q), .X(in_1[0]));
  NOT not_2 (.Q(not_2_q), .X(in_1[1]));
  NOT not_3 (.Q(not_3_q), .X(in_1[2]));
  NOT not_4 (.Q(not_4_q), .X(in_1[3]));
  NOT not_5 (.Q(not_5_q), .X(in_1[1]));
  NOT not_6 (.Q(not_6_q), .X(in_1[2]));
  NOT not_7 (.Q(not_7_q), .X(in_1[3]));
  NOT not_8 (.Q(not_8_q), .X(in_1[0]));
  NOT not_9 (.Q(not_9_q), .X(in_1[2]));
  NOT not_10 (.Q(not_10_q), .X(in_1[3]));
  NOT not_11 (.Q(not_11_q), .X(in_1[2]));
  NOT not_12 (.Q(not_12_q), .X(in_1[3]));
  NOT not_13 (.Q(not_13_q), .X(in_1[0]));
  NOT not_14 (.Q(not_14_q), .X(in_1[1]));
  NOT not_15 (.Q(not_15_q), .X(in_1[3]));
  NOT not_16 (.Q(not_16_q), .X(in_1[1]));
  NOT not_17 (.Q(not_17_q), .X(in_1[3]));
  NOT not_18 (.Q(not_18_q), .X(in_1[0]));
  NOT not_19 (.Q(not_19_q), .X(in_1[3]));
  NOT not_20 (.Q(not_20_q), .X(in_1[3]));
  NOT not_21 (.Q(not_21_q), .X(in_1[0]));
  NOT not_22 (.Q(not_22_q), .X(in_1[1]));
  NOT not_23 (.Q(not_23_q), .X(in_1[2]));
  NOT not_24 (.Q(not_24_q), .X(in_1[1]));
  NOT not_25 (.Q(not_25_q), .X(in_1[2]));
  NOT not_26 (.Q(not_26_q), .X(in_1[0]));
  NOT not_27 (.Q(not_27_q), .X(in_1[2]));
  NOT not_28 (.Q(not_28_q), .X(in_1[2]));
  NOT not_29 (.Q(not_29_q), .X(in_1[0]));
  NOT not_30 (.Q(not_30_q), .X(in_1[1]));
  NOT not_31 (.Q(not_31_q), .X(in_1[1]));
  NOT not_32 (.Q(not_32_q), .X(in_1[0]));
  _4_bit_AND u_4_bit_and_1 (.in_1(not_1_q), .in_2(not_2_q), .in_3(not_3_q), .in_4(not_4_q), .out_5(out_2));
  _4_bit_AND u_4_bit_and_2 (.in_1(in_1[0]), .in_2(not_5_q), .in_3(not_6_q), .in_4(not_7_q), .out_5(out_3));
  _4_bit_AND u_4_bit_and_3 (.in_1(not_8_q), .in_2(in_1[1]), .in_3(not_9_q), .in_4(not_10_q), .out_5(out_4));
  _4_bit_AND u_4_bit_and_4 (.in_1(in_1[0]), .in_2(in_1[1]), .in_3(not_11_q), .in_4(not_12_q), .out_5(out_5));
  _4_bit_AND u_4_bit_and_5 (.in_1(not_13_q), .in_2(not_14_q), .in_3(in_1[2]), .in_4(not_15_q), .out_5(out_6));
  _4_bit_AND u_4_bit_and_6 (.in_1(in_1[0]), .in_2(not_16_q), .in_3(in_1[2]), .in_4(not_17_q), .out_5(out_7));
  _4_bit_AND u_4_bit_and_7 (.in_1(not_18_q), .in_2(in_1[1]), .in_3(in_1[2]), .in_4(not_19_q), .out_5(out_8));
  _4_bit_AND u_4_bit_and_8 (.in_1(in_1[0]), .in_2(in_1[1]), .in_3(in_1[2]), .in_4(not_20_q), .out_5(out_9));
  _4_bit_AND u_4_bit_and_9 (.in_1(not_21_q), .in_2(not_22_q), .in_3(not_23_q), .in_4(in_1[3]), .out_5(out_10));
  _4_bit_AND u_4_bit_and_10 (.in_1(in_1[0]), .in_2(not_24_q), .in_3(not_25_q), .in_4(in_1[3]), .out_5(out_11));
  _4_bit_AND u_4_bit_and_11 (.in_1(not_26_q), .in_2(in_1[1]), .in_3(not_27_q), .in_4(in_1[3]), .out_5(out_12));
  _4_bit_AND u_4_bit_and_12 (.in_1(in_1[0]), .in_2(in_1[1]), .in_3(not_28_q), .in_4(in_1[3]), .out_5(out_13));
  _4_bit_AND u_4_bit_and_13 (.in_1(not_29_q), .in_2(not_30_q), .in_3(in_1[2]), .in_4(in_1[3]), .out_5(out_14));
  _4_bit_AND u_4_bit_and_14 (.in_1(in_1[0]), .in_2(not_31_q), .in_3(in_1[2]), .in_4(in_1[3]), .out_5(out_15));
  _4_bit_AND u_4_bit_and_15 (.in_1(not_32_q), .in_2(in_1[1]), .in_3(in_1[2]), .in_4(in_1[3]), .out_5(out_16));
  _4_bit_AND u_4_bit_and_16 (.in_1(in_1[0]), .in_2(in_1[1]), .in_3(in_1[2]), .in_4(in_1[3]), .out_5(out_17));
endmodule

// Register 8-bit
module Mem_8_bit_Register (
  input  WE,
  input  [7:0] I,
  output [7:0] out_3
);

  Memory_Bit memory_bit_1 (.Write(WE), .Input(I[0]), .Memory(out_3[0]));
  Memory_Bit memory_bit_2 (.Write(WE), .Input(I[1]), .Memory(out_3[1]));
  Memory_Bit memory_bit_3 (.Write(WE), .Input(I[2]), .Memory(out_3[2]));
  Memory_Bit memory_bit_4 (.Write(WE), .Input(I[3]), .Memory(out_3[3]));
  Memory_Bit memory_bit_5 (.Write(WE), .Input(I[4]), .Memory(out_3[4]));
  Memory_Bit memory_bit_6 (.Write(WE), .Input(I[5]), .Memory(out_3[5]));
  Memory_Bit memory_bit_7 (.Write(WE), .Input(I[6]), .Memory(out_3[6]));
  Memory_Bit memory_bit_8 (.Write(WE), .Input(I[7]), .Memory(out_3[7]));
endmodule

module Enable (
  input  E,
  input  [7:0] I,
  output [7:0] out_3
);

  AND and_1 (.in_1(E), .out_3(out_3[0]), .in_2(I[0]));
  AND and_2 (.in_1(E), .out_3(out_3[1]), .in_2(I[1]));
  AND and_3 (.in_1(E), .out_3(out_3[2]), .in_2(I[2]));
  AND and_4 (.in_1(E), .out_3(out_3[3]), .in_2(I[3]));
  AND and_5 (.in_1(E), .out_3(out_3[4]), .in_2(I[4]));
  AND and_6 (.in_1(E), .out_3(out_3[5]), .in_2(I[5]));
  AND and_7 (.in_1(E), .out_3(out_3[6]), .in_2(I[6]));
  AND and_8 (.in_1(E), .out_3(out_3[7]), .in_2(I[7]));
endmodule

// BITWISE OR
module _8_bitwise_OR (
  input  [7:0] A,
  input  [7:0] B,
  output [7:0] O
);

  OR or_1 (.in_1(B[7]), .in_2(A[7]), .out_3(O[7]));
  OR or_2 (.in_1(B[6]), .in_2(A[6]), .out_3(O[6]));
  OR or_3 (.in_1(B[5]), .in_2(A[5]), .out_3(O[5]));
  OR or_4 (.in_1(B[3]), .in_2(A[3]), .out_3(O[3]));
  OR or_5 (.in_1(B[4]), .in_2(A[4]), .out_3(O[4]));
  OR or_6 (.in_1(B[1]), .in_2(A[1]), .out_3(O[1]));
  OR or_7 (.in_1(B[2]), .in_2(A[2]), .out_3(O[2]));
  OR or_8 (.in_1(B[0]), .in_2(A[0]), .out_3(O[0]));
endmodule

// Memory Bank
module Memory_Bank__again (
  input  [7:0] In,
  input  [3:0] Addr,
  input  WE,
  output [7:0] x0,
  output [7:0] x1,
  output [7:0] x2,
  output [7:0] x3,
  output [7:0] x4,
  output [7:0] x5,
  output [7:0] x6,
  output [7:0] x7,
  output [7:0] x8,
  output [7:0] x9,
  output [7:0] xA,
  output [7:0] xB,
  output [7:0] xC,
  output [7:0] xD,
  output [7:0] xE,
  output [7:0] xF,
  output [7:0] OUT
);

  wire decoder_4_16_1_out_2, decoder_4_16_1_out_3, decoder_4_16_1_out_4, decoder_4_16_1_out_5,
       decoder_4_16_1_out_6, decoder_4_16_1_out_7, decoder_4_16_1_out_8, decoder_4_16_1_out_9,
       decoder_4_16_1_out_10, decoder_4_16_1_out_11, decoder_4_16_1_out_12, decoder_4_16_1_out_13,
       decoder_4_16_1_out_14, decoder_4_16_1_out_15, decoder_4_16_1_out_16, decoder_4_16_1_out_17,
       demux_4_16_1_out_3, demux_4_16_1_out_4, demux_4_16_1_out_5, demux_4_16_1_out_6, demux_4_16_1_out_7,
       demux_4_16_1_out_8, demux_4_16_1_out_9, demux_4_16_1_out_10, demux_4_16_1_out_11, demux_4_16_1_out_12,
       demux_4_16_1_out_13, demux_4_16_1_out_14, demux_4_16_1_out_15, demux_4_16_1_out_16,
       demux_4_16_1_out_17, demux_4_16_1_out_18;
  wire [7:0] enable_1_out_3, enable_2_out_3, enable_3_out_3, enable_4_out_3, enable_5_out_3, enable_6_out_3,
       enable_7_out_3, enable_8_out_3, enable_9_out_3, enable_10_out_3, enable_11_out_3, enable_12_out_3,
       enable_13_out_3, enable_14_out_3, enable_15_out_3, enable_16_out_3, n8_bitwise_or_1_o,
       n8_bitwise_or_2_o, n8_bitwise_or_3_o, n8_bitwise_or_4_o, n8_bitwise_or_5_o, n8_bitwise_or_6_o,
       n8_bitwise_or_7_o, n8_bitwise_or_8_o, n8_bitwise_or_9_o, n8_bitwise_or_10_o, n8_bitwise_or_11_o,
       n8_bitwise_or_12_o, n8_bitwise_or_13_o, n8_bitwise_or_14_o;

  Demux_4_16 demux_4_16_1 (
    .E(WE), .out_3(demux_4_16_1_out_3), .out_4(demux_4_16_1_out_4), .out_5(demux_4_16_1_out_5),
    .out_6(demux_4_16_1_out_6), .out_7(demux_4_16_1_out_7), .out_8(demux_4_16_1_out_8),
    .out_9(demux_4_16_1_out_9), .out_10(demux_4_16_1_out_10), .out_11(demux_4_16_1_out_11),
    .out_12(demux_4_16_1_out_12), .out_13(demux_4_16_1_out_13), .out_14(demux_4_16_1_out_14),
    .out_15(demux_4_16_1_out_15), .out_16(demux_4_16_1_out_16), .out_17(demux_4_16_1_out_17),
    .out_18(demux_4_16_1_out_18), .I(Addr));
  Decoder_4_16 decoder_4_16_1 (
    .out_2(decoder_4_16_1_out_2), .out_3(decoder_4_16_1_out_3), .out_4(decoder_4_16_1_out_4),
    .out_5(decoder_4_16_1_out_5), .out_6(decoder_4_16_1_out_6), .out_7(decoder_4_16_1_out_7),
    .out_8(decoder_4_16_1_out_8), .out_9(decoder_4_16_1_out_9), .out_10(decoder_4_16_1_out_10),
    .out_11(decoder_4_16_1_out_11), .out_12(decoder_4_16_1_out_12), .out_13(decoder_4_16_1_out_13),
    .out_14(decoder_4_16_1_out_14), .out_15(decoder_4_16_1_out_15), .out_16(decoder_4_16_1_out_16),
    .out_17(decoder_4_16_1_out_17), .in_1(Addr));
  Mem_8_bit_Register mem_8_bit_register_1 (.WE(demux_4_16_1_out_3), .out_3(x0), .I(In));
  Mem_8_bit_Register mem_8_bit_register_2 (.WE(demux_4_16_1_out_4), .out_3(x1), .I(In));
  Mem_8_bit_Register mem_8_bit_register_3 (.WE(demux_4_16_1_out_5), .out_3(x2), .I(In));
  Mem_8_bit_Register mem_8_bit_register_4 (.WE(demux_4_16_1_out_6), .out_3(x3), .I(In));
  Mem_8_bit_Register mem_8_bit_register_5 (.WE(demux_4_16_1_out_7), .out_3(x4), .I(In));
  Mem_8_bit_Register mem_8_bit_register_6 (.WE(demux_4_16_1_out_8), .out_3(x5), .I(In));
  Mem_8_bit_Register mem_8_bit_register_7 (.WE(demux_4_16_1_out_9), .out_3(x6), .I(In));
  Mem_8_bit_Register mem_8_bit_register_8 (.WE(demux_4_16_1_out_10), .out_3(x7), .I(In));
  Mem_8_bit_Register mem_8_bit_register_9 (.WE(demux_4_16_1_out_11), .out_3(x8), .I(In));
  Mem_8_bit_Register mem_8_bit_register_10 (.WE(demux_4_16_1_out_12), .out_3(x9), .I(In));
  Mem_8_bit_Register mem_8_bit_register_11 (.WE(demux_4_16_1_out_13), .out_3(xA), .I(In));
  Mem_8_bit_Register mem_8_bit_register_12 (.WE(demux_4_16_1_out_14), .out_3(xB), .I(In));
  Mem_8_bit_Register mem_8_bit_register_13 (.WE(demux_4_16_1_out_15), .out_3(xC), .I(In));
  Mem_8_bit_Register mem_8_bit_register_14 (.WE(demux_4_16_1_out_16), .out_3(xD), .I(In));
  Mem_8_bit_Register mem_8_bit_register_15 (.WE(demux_4_16_1_out_17), .out_3(xE), .I(In));
  Mem_8_bit_Register mem_8_bit_register_16 (.WE(demux_4_16_1_out_18), .out_3(xF), .I(In));
  Enable enable_1 (.E(decoder_4_16_1_out_2), .out_3(enable_1_out_3), .I(x0));
  Enable enable_2 (.E(decoder_4_16_1_out_3), .out_3(enable_2_out_3), .I(x1));
  Enable enable_3 (.E(decoder_4_16_1_out_4), .out_3(enable_3_out_3), .I(x2));
  Enable enable_4 (.E(decoder_4_16_1_out_5), .out_3(enable_4_out_3), .I(x3));
  Enable enable_5 (.E(decoder_4_16_1_out_6), .out_3(enable_5_out_3), .I(x4));
  Enable enable_6 (.E(decoder_4_16_1_out_7), .out_3(enable_6_out_3), .I(x5));
  Enable enable_7 (.E(decoder_4_16_1_out_8), .out_3(enable_7_out_3), .I(x6));
  Enable enable_8 (.E(decoder_4_16_1_out_9), .out_3(enable_8_out_3), .I(x7));
  Enable enable_9 (.E(decoder_4_16_1_out_10), .out_3(enable_9_out_3), .I(x8));
  Enable enable_10 (.E(decoder_4_16_1_out_11), .out_3(enable_10_out_3), .I(x9));
  Enable enable_11 (.E(decoder_4_16_1_out_12), .out_3(enable_11_out_3), .I(xA));
  Enable enable_12 (.E(decoder_4_16_1_out_13), .out_3(enable_12_out_3), .I(xB));
  Enable enable_13 (.E(decoder_4_16_1_out_14), .out_3(enable_13_out_3), .I(xC));
  Enable enable_14 (.E(decoder_4_16_1_out_15), .out_3(enable_14_out_3), .I(xD));
  Enable enable_15 (.E(decoder_4_16_1_out_16), .out_3(enable_15_out_3), .I(xE));
  Enable enable_16 (.E(decoder_4_16_1_out_17), .out_3(enable_16_out_3), .I(xF));
  _8_bitwise_OR u_8_bitwise_or_1 (.A(enable_1_out_3), .B(enable_2_out_3), .O(n8_bitwise_or_1_o));
  _8_bitwise_OR u_8_bitwise_or_2 (.A(n8_bitwise_or_1_o), .B(enable_3_out_3), .O(n8_bitwise_or_2_o));
  _8_bitwise_OR u_8_bitwise_or_3 (.A(n8_bitwise_or_2_o), .B(enable_4_out_3), .O(n8_bitwise_or_3_o));
  _8_bitwise_OR u_8_bitwise_or_4 (.A(n8_bitwise_or_3_o), .B(enable_5_out_3), .O(n8_bitwise_or_4_o));
  _8_bitwise_OR u_8_bitwise_or_5 (.A(n8_bitwise_or_4_o), .B(enable_6_out_3), .O(n8_bitwise_or_5_o));
  _8_bitwise_OR u_8_bitwise_or_6 (.A(n8_bitwise_or_5_o), .B(enable_7_out_3), .O(n8_bitwise_or_6_o));
  _8_bitwise_OR u_8_bitwise_or_7 (.A(n8_bitwise_or_6_o), .B(enable_8_out_3), .O(n8_bitwise_or_7_o));
  _8_bitwise_OR u_8_bitwise_or_8 (.A(n8_bitwise_or_7_o), .B(enable_9_out_3), .O(n8_bitwise_or_8_o));
  _8_bitwise_OR u_8_bitwise_or_9 (.A(n8_bitwise_or_8_o), .B(enable_10_out_3), .O(n8_bitwise_or_9_o));
  _8_bitwise_OR u_8_bitwise_or_10 (.A(n8_bitwise_or_9_o), .B(enable_11_out_3), .O(n8_bitwise_or_10_o));
  _8_bitwise_OR u_8_bitwise_or_11 (.A(n8_bitwise_or_10_o), .B(enable_12_out_3), .O(n8_bitwise_or_11_o));
  _8_bitwise_OR u_8_bitwise_or_12 (.A(n8_bitwise_or_11_o), .B(enable_13_out_3), .O(n8_bitwise_or_12_o));
  _8_bitwise_OR u_8_bitwise_or_13 (.A(n8_bitwise_or_12_o), .B(enable_14_out_3), .O(n8_bitwise_or_13_o));
  _8_bitwise_OR u_8_bitwise_or_14 (.A(n8_bitwise_or_13_o), .B(enable_15_out_3), .O(n8_bitwise_or_14_o));
  _8_bitwise_OR u_8_bitwise_or_15 (.A(n8_bitwise_or_14_o), .B(enable_16_out_3), .O(OUT));
endmodule
